// Logisim project lab1.circ as structural Verilog: 8 circuits, main circuit 四位二进制并行加法器
module \四位二进制并行加法器  (
  input  A3,
  input  B3,
  input  A2,
  input  B2,
  input  A1,
  input  B1,
  input  A0,
  input  B0,
  input  C0,
  output C4,
  output S3,
  output S2,
  output S1,
  output S0
);

  wire and_1_out, and_2_out, and_3_out, and_4_out, and_5_out, and_6_out, and_7_out, and_8_out, and_9_out,
       and_10_out, C1_out, C2_out, C3_out, G1_out, G2_out, G3_out, G4_out, P1_out, P2_out, P3_out, P4_out;

  and and_1 (and_1_out, P4_out, P3_out, P2_out, P1_out, C0);
  or or_1 (C4, and_1_out, and_2_out, G4_out, and_3_out, and_4_out);
  and and_2 (and_2_out, P4_out, P3_out, P2_out, G1_out);
  and and_3 (and_3_out, P4_out, P3_out, G2_out);
  and and_4 (and_4_out, P4_out, G3_out);
  and G4 (G4_out, B3, A3);
  xor xor_1 (S3, P4_out, C3_out);
  xor P4 (P4_out, A3, B3);
  and and_5 (and_5_out, P3_out, P2_out, C0, P1_out);
  and and_6 (and_6_out, G1_out, P3_out, P2_out);
  or C3 (C3_out, and_5_out, and_6_out, G3_out, and_7_out);
  and and_7 (and_7_out, P3_out, G2_out);
  and G3 (G3_out, B2, A2);
  xor xor_2 (S2, P3_out, C2_out);
  xor P3 (P3_out, A2, B2);
  and and_8 (and_8_out, P2_out, C0, P1_out);
  or C2 (C2_out, and_8_out, and_9_out, G2_out);
  and and_9 (and_9_out, P2_out, G1_out);
  and G2 (G2_out, B1, A1);
  xor xor_3 (S1, P2_out, C1_out);
  xor P2 (P2_out, A1, B1);
  or C1 (C1_out, and_10_out, G1_out);
  and and_10 (and_10_out, P1_out, C0);
  and G1 (G1_out, A0, B0);
  xor P1 (P1_out, A0, B0);
  xor xor_4 (S0, P1_out, C0);
endmodule

module \_1四位二进制并行加法器  (
  input  in_1,
  input  in_2,
  input  in_3,
  input  in_4,
  input  in_5,
  input  in_6,
  input  in_7,
  input  in_8,
  input  in_9,
  output out_10,
  output out_11,
  output out_12,
  output out_13,
  output out_14
);

  \四位二进制并行加法器  \u_四位二进制并行加法器_1  (
    .C4(out_14), .S3(out_10), .S2(out_11), .S1(out_12), .S0(out_13), .A3(in_2), .B3(in_6), .A2(in_3),
    .B2(in_7), .A1(in_4), .B1(in_8), .A0(in_5), .B0(in_9), .C0(in_1));
endmodule

module \四位二进制可逆计数器  (
  input  CLR,
  input  CUP,
  input  CPD,
  output Sd,
  output Sc,
  output Sb,
  output Sa
);

  wire and_1_out, and_2_out, and_3_out, and_4_out, not_1_out, or_1_out, \四位二进制并行加法器_1_s0 , \四位二进制并行加法器_1_s1 ,
       \四位二进制并行加法器_1_s2 , \四位二进制并行加法器_1_s3 ;

  and and_1 (and_1_out, not_1_out, \四位二进制并行加法器_1_s3 );
  and and_2 (and_2_out, not_1_out, \四位二进制并行加法器_1_s2 );
  and and_3 (and_3_out, not_1_out, \四位二进制并行加法器_1_s1 );
  and and_4 (and_4_out, not_1_out, \四位二进制并行加法器_1_s0 );
  not not_1 (not_1_out, CLR);
  \四位二进制并行加法器  \u_四位二进制并行加法器_1  (
    .S3(\四位二进制并行加法器_1_s3 ), .S2(\四位二进制并行加法器_1_s2 ), .S1(\四位二进制并行加法器_1_s1 ), .S0(\四位二进制并行加法器_1_s0 ), .A3(Sd),
    .B3(CPD), .A2(Sc), .B2(CPD), .A1(Sb), .B1(CPD), .A0(Sa), .B0(CPD), .C0(CUP));  // open: C4
  D_Flip_Flop #(.trigger("falling")) d_ff_1 (.clk(or_1_out), .D(and_1_out), .Q(Sd));  // open: Qn, preset, en, reset
  D_Flip_Flop #(.trigger("falling")) d_ff_2 (.clk(or_1_out), .D(and_2_out), .Q(Sc));  // open: Qn, preset, en, reset
  D_Flip_Flop #(.trigger("falling")) d_ff_3 (.clk(or_1_out), .D(and_3_out), .Q(Sb));  // open: Qn, preset, en, reset
  D_Flip_Flop #(.trigger("falling")) d_ff_4 (.clk(or_1_out), .D(and_4_out), .Q(Sa));  // open: Qn, preset, en, reset
  or or_1 (or_1_out, CUP, CLR, CPD);
endmodule

module \二进制转8421BCD码  (
  input  A3,
  input  A2,
  input  A1,
  input  A0,
  output Q7,
  output Q6,
  output Q5,
  output Q4,
  output out_9,
  output out_10,
  output out_11,
  output out_12
);

  wire and_2_out, and_3_out, and_4_out, and_5_out, and_6_out, and_7_out, and_8_out, and_9_out, not_1_out,
       or_1_out, \四位二进制并行加法器_1_s0 , \四位二进制并行加法器_1_s1 , \四位二进制并行加法器_1_s2 , \四位二进制并行加法器_1_s3 ;

  and and_1 (Q4, or_1_out, A3);
  or or_1 (or_1_out, A2, A1);
  not not_1 (not_1_out, Q4);
  and and_2 (and_2_out, not_1_out, A3);
  and and_3 (and_3_out, not_1_out, A2);
  and and_4 (and_4_out, not_1_out, A1);
  and and_5 (and_5_out, not_1_out, A0);
  or or_2 (out_9, and_2_out, and_6_out);
  and and_6 (and_6_out, Q4, \四位二进制并行加法器_1_s3 );
  \四位二进制并行加法器  \u_四位二进制并行加法器_1  (
    .S3(\四位二进制并行加法器_1_s3 ), .S2(\四位二进制并行加法器_1_s2 ), .S1(\四位二进制并行加法器_1_s1 ), .S0(\四位二进制并行加法器_1_s0 ), .A3(A3),
    .B3(1'b0), .A2(A2), .B2(1'b1), .A1(A1), .B1(1'b1), .A0(A0), .B0(1'b0), .C0(1'b0));  // open: C4
  or or_3 (out_10, and_3_out, and_7_out);
  and and_7 (and_7_out, Q4, \四位二进制并行加法器_1_s2 );
  or or_4 (out_11, and_4_out, and_8_out);
  and and_8 (and_8_out, Q4, \四位二进制并行加法器_1_s1 );
  or or_5 (out_12, and_5_out, and_9_out);
  and and_9 (and_9_out, Q4, \四位二进制并行加法器_1_s0 );

  assign Q5 = 1'b0;
  assign Q6 = 1'b0;
  assign Q7 = 1'b0;
endmodule

module \_7段译码器  (
  input  A3,
  input  A2,
  input  A1,
  input  A0,
  output g,
  output f,
  output e,
  output d,
  output c,
  output b,
  output a
);

  wire and_1_out, and_2_out, and_3_out, and_4_out, and_5_out, and_6_out, and_7_out, and_8_out, and_9_out,
       and_10_out, and_11_out, and_12_out, and_13_out, and_14_out, and_15_out, and_16_out, and_17_out,
       and_18_out, and_19_out, and_20_out, and_21_out, and_22_out, and_23_out, and_24_out, and_25_out,
       and_26_out, not_1_out, not_2_out, not_3_out, not_4_out;

  and and_1 (and_1_out, A1, not_2_out);
  or or_1 (g, and_1_out, and_3_out, and_2_out, and_5_out);
  and and_2 (and_2_out, A2, not_3_out);
  and and_3 (and_3_out, A2, not_4_out);
  and and_4 (and_4_out, A3, not_3_out, A0);
  and and_5 (and_5_out, A3, not_2_out);
  or or_2 (f, and_4_out, and_6_out, and_7_out, and_8_out);
  and and_6 (and_6_out, A2, not_3_out);
  and and_7 (and_7_out, A2, not_4_out);
  not not_1 (not_1_out, A3);
  or or_3 (e, and_9_out, and_11_out);
  and and_8 (and_8_out, not_3_out, not_4_out);
  and and_9 (and_9_out, not_4_out, not_3_out, not_2_out);
  and and_10 (and_10_out, A1, not_4_out);
  and and_11 (and_11_out, A1, not_4_out);
  or or_4 (d, and_10_out, and_13_out, and_12_out, and_15_out);
  and and_12 (and_12_out, A1, not_2_out);
  and and_13 (and_13_out, A2, not_3_out, A0);
  not not_2 (not_2_out, A2);
  and and_14 (and_14_out, not_1_out, A2);
  and and_15 (and_15_out, not_2_out, not_4_out);
  or or_5 (c, and_14_out, and_17_out, and_16_out);
  and and_16 (and_16_out, not_2_out, A1, A0);
  and and_17 (and_17_out, not_2_out, not_3_out);
  or or_6 (b, and_19_out, and_18_out, and_21_out, and_20_out);
  and and_18 (and_18_out, not_3_out, not_4_out);
  and and_19 (and_19_out, not_1_out, not_2_out);
  not not_3 (not_3_out, A1);
  and and_20 (and_20_out, A3, not_2_out, not_3_out);
  and and_21 (and_21_out, not_1_out, A1, A0);
  or or_7 (a, and_23_out, and_22_out, and_24_out, and_25_out, and_26_out);
  and and_22 (and_22_out, A3, not_3_out, A0);
  and and_23 (and_23_out, not_1_out, not_2_out, A1);
  and and_24 (and_24_out, not_3_out, A0, A2);
  not not_4 (not_4_out, A0);
  and and_25 (and_25_out, not_1_out, A2, A0);
  and and_26 (and_26_out, not_2_out, not_3_out, not_4_out);
endmodule

module \警报器  (
  input  CLR,
  input  CPU,
  input  CPD,
  output Alert,
  output Qd,
  output Qc,
  output Qb,
  output Qa
);

  wire and_1_out, and_2_out, and_3_out, and_4_out, and_5_out, and_6_out, not_1_out, not_2_out, or_1_out,
       \判满_out , \判空_out , \四位二进制并行加法器_1_s0 , \四位二进制并行加法器_1_s1 , \四位二进制并行加法器_1_s2 , \四位二进制并行加法器_1_s3 ;

  and and_1 (and_1_out, not_1_out, \四位二进制并行加法器_1_s3 );
  and and_2 (and_2_out, not_1_out, \四位二进制并行加法器_1_s2 );
  and and_3 (and_3_out, not_1_out, \四位二进制并行加法器_1_s1 );
  and and_4 (and_4_out, not_1_out, \四位二进制并行加法器_1_s0 );
  not not_1 (not_1_out, CLR);
  \四位二进制并行加法器  \u_四位二进制并行加法器_1  (
    .S3(\四位二进制并行加法器_1_s3 ), .S2(\四位二进制并行加法器_1_s2 ), .S1(\四位二进制并行加法器_1_s1 ), .S0(\四位二进制并行加法器_1_s0 ), .A3(Qd),
    .B3(and_5_out), .A2(Qc), .B2(and_5_out), .A1(Qb), .B1(and_5_out), .A0(Qa), .B0(and_5_out), .C0(and_6_out));  // open: C4
  D_Flip_Flop #(.trigger("falling")) d_ff_1 (.clk(or_1_out), .D(and_1_out), .Q(Qd));  // open: Qn, preset, en, reset
  D_Flip_Flop #(.trigger("falling")) d_ff_2 (.clk(or_1_out), .D(and_2_out), .Q(Qc));  // open: Qn, preset, en, reset
  and and_5 (and_5_out, CPD, \判空_out );
  D_Flip_Flop #(.trigger("falling")) d_ff_3 (.clk(or_1_out), .D(and_3_out), .Q(Qb));  // open: Qn, preset, en, reset
  and and_6 (and_6_out, CPU, not_2_out);
  D_Flip_Flop #(.trigger("falling")) d_ff_4 (.clk(or_1_out), .D(and_4_out), .Q(Qa));  // open: Qn, preset, en, reset
  not not_2 (not_2_out, \判满_out );
  or \u_判空  (\判空_out , Qa, Qb, Qc, Qd);
  and and_7 (Alert, CPU, \判满_out );
  or or_1 (or_1_out, CLR, CPU, CPD);
  and \u_判满  (\判满_out , Qa, Qb, Qc, Qd);
endmodule

module \门禁系统  (
  input  CPu,
  input  CLR,
  input  CPd,
  output out_4,
  output out_5,
  output out_6,
  output out_7,
  output out_8,
  output out_9,
  output out_10,
  output out_11,
  output out_12,
  output out_13,
  output out_14,
  output out_15,
  output out_16,
  output out_17,
  output Alert
);

  wire \二进制转8421bcd码_1_out_9 , \二进制转8421bcd码_1_out_10 , \二进制转8421bcd码_1_out_11 , \二进制转8421bcd码_1_out_12 ,
       \二进制转8421bcd码_1_q4 , \二进制转8421bcd码_1_q5 , \二进制转8421bcd码_1_q6 , \二进制转8421bcd码_1_q7 , \警报器_1_qa ,
       \警报器_1_qb , \警报器_1_qc , \警报器_1_qd ;

  \_7段译码器  \u_7段译码器_1  (
    .g(out_10), .f(out_9), .e(out_8), .d(out_7), .c(out_6), .b(out_5), .a(out_4), .A3(\二进制转8421bcd码_1_q7 ),
    .A2(\二进制转8421bcd码_1_q6 ), .A1(\二进制转8421bcd码_1_q5 ), .A0(\二进制转8421bcd码_1_q4 ));
  \二进制转8421BCD码  \u_二进制转8421bcd码_1  (
    .Q7(\二进制转8421bcd码_1_q7 ), .Q6(\二进制转8421bcd码_1_q6 ), .Q5(\二进制转8421bcd码_1_q5 ), .Q4(\二进制转8421bcd码_1_q4 ),
    .out_9(\二进制转8421bcd码_1_out_9 ), .out_10(\二进制转8421bcd码_1_out_10 ), .out_11(\二进制转8421bcd码_1_out_11 ),
    .out_12(\二进制转8421bcd码_1_out_12 ), .A3(\警报器_1_qd ), .A2(\警报器_1_qc ), .A1(\警报器_1_qb ), .A0(\警报器_1_qa ));
  \警报器  \u_警报器_1  (
    .CPD(CPd), .Alert(Alert), .CLR(CLR), .CPU(CPu), .Qd(\警报器_1_qd ), .Qc(\警报器_1_qc ), .Qb(\警报器_1_qb ),
    .Qa(\警报器_1_qa ));
  \_7段译码器  \u_7段译码器_2  (
    .g(out_17), .f(out_16), .e(out_15), .d(out_14), .c(out_13), .b(out_12), .a(out_11),
    .A3(\二进制转8421bcd码_1_out_9 ), .A2(\二进制转8421bcd码_1_out_10 ), .A1(\二进制转8421bcd码_1_out_11 ),
    .A0(\二进制转8421bcd码_1_out_12 ));
endmodule

module test (
  input  in_1,
  input  in_2,
  input  in_3,
  input  in_4,
  input  in_5,
  input  in_6,
  input  in_7,
  input  in_8,
  input  in_9,
  input  in_10,
  input  in_11,
  input  in_12,
  input  in_13,
  input  in_14,
  output out_15,
  output out_16,
  output out_17,
  output out_18,
  output out_19,
  output out_20,
  output out_21,
  output out_22,
  output out_23,
  output out_24,
  output out_25,
  output out_26,
  output out_27,
  output out_28,
  output out_29,
  output out_30
);

  wire button_1_out, button_2_out, button_3_out, \n7段译码器_1_a , \n7段译码器_1_b , \n7段译码器_1_c , \n7段译码器_1_d ,
       \n7段译码器_1_e , \n7段译码器_1_f , \n7段译码器_1_g , \警报器_1_alert , \门禁系统_1_alert , \门禁系统_1_out_4 ,
       \门禁系统_1_out_5 , \门禁系统_1_out_6 , \门禁系统_1_out_7 , \门禁系统_1_out_8 , \门禁系统_1_out_9 , \门禁系统_1_out_10 ,
       \门禁系统_1_out_11 , \门禁系统_1_out_12 , \门禁系统_1_out_13 , \门禁系统_1_out_14 , \门禁系统_1_out_15 , \门禁系统_1_out_16 ,
       \门禁系统_1_out_17 ;

  \四位二进制可逆计数器  \u_四位二进制可逆计数器_1  (
    .CPD(in_3), .CLR(in_2), .CUP(in_1), .Sd(out_15), .Sc(out_16), .Sb(out_17), .Sa(out_18));
  \二进制转8421BCD码  \u_二进制转8421bcd码_1  (
    .Q7(out_19), .Q6(out_20), .Q5(out_21), .Q4(out_22), .out_9(out_23), .out_10(out_24), .out_11(out_25),
    .out_12(out_26), .A3(in_4), .A2(in_5), .A1(in_6), .A0(in_7));
  \警报器  \u_警报器_1  (
    .CPD(in_10), .Alert(\警报器_1_alert ), .CLR(in_9), .CPU(in_8), .Qd(out_27), .Qc(out_28), .Qb(out_29),
    .Qa(out_30));
  LED led_1 (.in(\警报器_1_alert ));
  Button button_1 (.out(button_1_out));
  Button button_2 (.out(button_2_out));
  Button button_3 (.out(button_3_out));
  \门禁系统  \u_门禁系统_1  (
    .CPu(button_1_out), .CLR(button_2_out), .CPd(button_3_out), .Alert(\门禁系统_1_alert ),
    .out_4(\门禁系统_1_out_4 ), .out_5(\门禁系统_1_out_5 ), .out_6(\门禁系统_1_out_6 ), .out_7(\门禁系统_1_out_7 ),
    .out_8(\门禁系统_1_out_8 ), .out_9(\门禁系统_1_out_9 ), .out_10(\门禁系统_1_out_10 ), .out_11(\门禁系统_1_out_11 ),
    .out_12(\门禁系统_1_out_12 ), .out_13(\门禁系统_1_out_13 ), .out_14(\门禁系统_1_out_14 ), .out_15(\门禁系统_1_out_15 ),
    .out_16(\门禁系统_1_out_16 ), .out_17(\门禁系统_1_out_17 ));
  _7_Segment_Display u_7_segment_display_1 (
    .g(\门禁系统_1_out_10 ), .f(\门禁系统_1_out_9 ), .a(\门禁系统_1_out_4 ), .b(\门禁系统_1_out_5 ), .e(\门禁系统_1_out_8 ),
    .d(\门禁系统_1_out_7 ), .c(\门禁系统_1_out_6 ));  // open: dp
  \_7段译码器  \u_7段译码器_1  (
    .g(\n7段译码器_1_g ), .f(\n7段译码器_1_f ), .e(\n7段译码器_1_e ), .d(\n7段译码器_1_d ), .c(\n7段译码器_1_c ),
    .b(\n7段译码器_1_b ), .a(\n7段译码器_1_a ), .A3(in_11), .A2(in_12), .A1(in_13), .A0(in_14));
  _7_Segment_Display u_7_segment_display_2 (
    .g(\n7段译码器_1_g ), .f(\n7段译码器_1_f ), .a(\n7段译码器_1_a ), .b(\n7段译码器_1_b ), .e(\n7段译码器_1_e ),
    .d(\n7段译码器_1_d ), .c(\n7段译码器_1_c ));  // open: dp
  _7_Segment_Display u_7_segment_display_3 (
    .g(\门禁系统_1_out_17 ), .f(\门禁系统_1_out_16 ), .a(\门禁系统_1_out_11 ), .b(\门禁系统_1_out_12 ), .e(\门禁系统_1_out_15 ),
    .d(\门禁系统_1_out_14 ), .c(\门禁系统_1_out_13 ));  // open: dp
  LED led_2 (.in(\门禁系统_1_alert ));
endmodule
