// Logisim project 一位二进制全加器.circ as structural Verilog: 1 circuit, main circuit main
module main (
  input  Ci_1,
  input  A,
  input  B,
  output Si,
  output Ci
);

  wire and_1_out, and_2_out, xor_1_out, xor_2_out;

  xor xor_1 (xor_1_out, B, A);
  xor xor_2 (xor_2_out, B, A);
  and and_1 (and_1_out, A, B);
  xor xor_3 (Si, Ci_1, xor_1_out);
  and and_2 (and_2_out, Ci_1, xor_2_out);
  or or_1 (Ci, and_2_out, and_1_out);
endmodule
