// Logisim project 串行进位的四位二进制并行加法器.circ as structural Verilog: 2 circuits, main circuit main
module main (
  input  A3,
  input  B3,
  input  A2,
  input  B2,
  input  A1,
  input  B1,
  input  A0,
  input  B0,
  input  C0,
  output C4,
  output S1,
  output S3,
  output S2,
  output S0
);

  wire and_1_out, and_2_out, and_3_out, and_4_out, and_5_out, and_6_out, and_7_out, and_8_out, or_2_out,
       or_3_out, or_4_out, xor_2_out, xor_4_out, xor_5_out, xor_7_out;

  or or_1 (C4, and_1_out, and_2_out);
  and and_1 (and_1_out, or_2_out, xor_2_out);
  and and_2 (and_2_out, A3, B3);
  xor xor_1 (S3, xor_2_out, or_2_out);
  xor xor_2 (xor_2_out, A3, B3);
  and and_3 (and_3_out, or_3_out, xor_4_out);
  or or_2 (or_2_out, and_3_out, and_4_out);
  and and_4 (and_4_out, A2, B2);
  xor xor_3 (S2, xor_4_out, or_3_out);
  xor xor_4 (xor_4_out, A2, B2);
  or or_3 (or_3_out, and_5_out, and_6_out);
  and and_5 (and_5_out, or_4_out, xor_5_out);
  xor xor_5 (xor_5_out, A1, B1);
  and and_6 (and_6_out, A1, B1);
  xor xor_6 (S1, xor_5_out, or_4_out);
  and and_7 (and_7_out, C0, xor_7_out);
  or or_4 (or_4_out, and_7_out, and_8_out);
  and and_8 (and_8_out, A0, B0);
  xor xor_7 (xor_7_out, A0, B0);
  xor xor_8 (S0, xor_7_out, C0);
endmodule

module KK (
  input  in_1,
  input  in_2,
  input  in_3,
  input  in_4,
  input  in_5,
  input  in_6,
  input  in_7,
  input  in_8,
  input  in_9,
  output out_10,
  output out_11,
  output out_12,
  output out_13,
  output out_14
);

  main main_1 (
    .C4(out_14), .S3(out_10), .S2(out_11), .S1(out_12), .S0(out_13), .A3(in_2), .B3(in_6), .A2(in_3),
    .B2(in_7), .A1(in_4), .B1(in_8), .A0(in_5), .B0(in_9), .C0(in_1));
  main main_2 ();  // open: C4, S3, S2, S1, S0, A3, B3, A2, B2, A1, B1, A0, B0, C0
endmodule
