// Logisim project 全加器.circ as structural Verilog: 6 circuits, main circuit main
module main (
  input  C0,
  input  A3,
  input  B3,
  input  A2,
  input  B2,
  input  A1,
  input  B1,
  input  A0,
  input  B0,
  output F3,
  output F2,
  output F1,
  output F0,
  output C4
);

  wire \一位二进制全加器_2_c2 , \一位二进制全加器_3_c2 , \一位二进制全加器_4_c2 ;

  \一位二进制全加器  \u_一位二进制全加器_1  (.A(A3), .B(B3), .C1(\一位二进制全加器_2_c2 ), .S(F3), .C2(C4));
  \一位二进制全加器  \u_一位二进制全加器_2  (.A(A2), .B(B2), .C1(\一位二进制全加器_3_c2 ), .S(F2), .C2(\一位二进制全加器_2_c2 ));
  \一位二进制全加器  \u_一位二进制全加器_3  (.A(A1), .B(B1), .C1(\一位二进制全加器_4_c2 ), .S(F1), .C2(\一位二进制全加器_3_c2 ));
  \一位二进制全加器  \u_一位二进制全加器_4  (.A(A0), .B(B0), .C1(C0), .S(F0), .C2(\一位二进制全加器_4_c2 ));
endmodule

module \一位二进制全加器  (
  input  A,
  input  B,
  input  C1,
  output S,
  output C2
);

  wire and_1_out, and_2_out, xor_1_out;

  xor xor_1 (xor_1_out, A, B);
  and and_1 (and_1_out, xor_1_out, C1);
  and and_2 (and_2_out, B, A);
  xor xor_2 (S, xor_1_out, C1);
  or or_1 (C2, and_1_out, and_2_out);
endmodule

module \串行进位的四位二进制并行加法器  (
  input  C0,
  input  A3,
  input  B3,
  input  A2,
  input  B2,
  input  A1,
  input  B1,
  input  A0,
  input  B0,
  output F3,
  output F2,
  output F1,
  output F0,
  output C4
);

  wire \一位二进制全加器_2_c2 , \一位二进制全加器_3_c2 , \一位二进制全加器_4_c2 ;

  \一位二进制全加器  \u_一位二进制全加器_1  (.A(A3), .B(B3), .C1(\一位二进制全加器_2_c2 ), .S(F3), .C2(C4));
  \一位二进制全加器  \u_一位二进制全加器_2  (.A(A2), .B(B2), .C1(\一位二进制全加器_3_c2 ), .S(F2), .C2(\一位二进制全加器_2_c2 ));
  \一位二进制全加器  \u_一位二进制全加器_3  (.A(A1), .B(B1), .C1(\一位二进制全加器_4_c2 ), .S(F1), .C2(\一位二进制全加器_3_c2 ));
  \一位二进制全加器  \u_一位二进制全加器_4  (.A(A0), .B(B0), .C1(C0), .S(F0), .C2(\一位二进制全加器_4_c2 ));
endmodule

module \先行进位的四位二进制并行加法器  (
  input  C0,
  input  A1,
  input  B1,
  input  A2,
  input  B2,
  input  A3,
  input  B3,
  input  A4,
  input  B4,
  output F1,
  output F2,
  output F3,
  output F4,
  output C4
);

  wire and_1_out, and_2_out, and_3_out, and_4_out, and_5_out, and_6_out, and_7_out, and_8_out, and_9_out,
       and_10_out, and_11_out, and_12_out, and_13_out, and_14_out, or_1_out, or_2_out, or_3_out, xor_1_out,
       xor_2_out, xor_3_out, xor_4_out;

  and and_1 (and_1_out, B1, A1);
  and and_2 (and_2_out, B2, A2);
  and and_3 (and_3_out, B3, A3);
  and and_4 (and_4_out, B4, A4);
  xor xor_1 (xor_1_out, B1, A1);
  xor xor_2 (xor_2_out, B2, A2);
  xor xor_3 (xor_3_out, B3, A3);
  xor xor_4 (xor_4_out, B4, A4);
  and and_5 (and_5_out, xor_1_out, C0);
  and and_6 (and_6_out, xor_2_out, xor_1_out, C0);
  and and_7 (and_7_out, xor_2_out, and_1_out);
  and and_8 (and_8_out, xor_1_out, C0, xor_2_out, xor_3_out);
  and and_9 (and_9_out, xor_3_out, and_1_out, xor_2_out);
  and and_10 (and_10_out, xor_3_out, and_2_out);
  and and_11 (and_11_out, xor_4_out, xor_3_out, xor_2_out, xor_1_out, C0);
  and and_12 (and_12_out, xor_4_out, xor_3_out, xor_2_out, and_1_out);
  and and_13 (and_13_out, xor_4_out, xor_3_out, and_2_out);
  and and_14 (and_14_out, xor_4_out, and_3_out);
  or or_1 (or_1_out, and_5_out, and_1_out);
  or or_2 (or_2_out, and_6_out, and_2_out, and_7_out);
  or or_3 (or_3_out, and_3_out, and_8_out, and_10_out, and_9_out);
  xor xor_5 (F1, C0, xor_1_out);
  xor xor_6 (F2, or_1_out, xor_2_out);
  xor xor_7 (F3, or_2_out, xor_3_out);
  xor xor_8 (F4, or_3_out, xor_4_out);
  or or_4 (C4, and_4_out, and_11_out, and_13_out, and_14_out, and_12_out);

  // Notes on the sheet:
  //   P2
  //   P4
  //   G4
  //   P1
  //   G1
  //   G2
  //   P3
  //   G3
  //   C1
  //   C2
  //   C3
  //   C4
endmodule

module \一位二进制半加器  (
  input  A,
  input  B,
  output C,
  output S
);

  and and_1 (C, B, A);
  xor xor_1 (S, B, A);
endmodule

module \封装先行进位加法器  (
  input  C0,
  input  A4,
  input  A3,
  input  A2,
  input  A1,
  input  B4,
  input  B3,
  input  B2,
  input  B1,
  output F4,
  output F3,
  output F2,
  output F1,
  output C4
);

  \先行进位的四位二进制并行加法器  \u_先行进位的四位二进制并行加法器_1  (
    .C0(C0), .A1(A1), .B1(B1), .A2(A2), .B2(B2), .A3(A3), .B3(B3), .A4(A4), .B4(B4), .F1(F1), .F2(F2),
    .F3(F3), .F4(F4), .C4(C4));
endmodule
