// Logisim project 门禁系统.circ as structural Verilog
module \四位二进制可逆加法器  (
  input  CLR,
  input  CPU,
  input  CPD,
  output Q3,
  output Q2,
  output Q1,
  output Q0
);

  wire and_1_out, and_2_out, and_3_out, and_4_out, and_5_out, and_6_out, d_ff_1_qn, d_ff_2_qn, d_ff_3_qn,
       d_ff_4_qn, or_1_out, or_2_out, or_3_out, or_4_out;

  or or_1 (or_1_out, and_1_out, and_2_out);
  and and_1 (and_1_out, d_ff_2_qn, d_ff_3_qn, d_ff_4_qn, CPD);
  D_Flip_Flop #(.trigger("falling")) d_ff_1 (
    .clk(or_1_out), .D(d_ff_1_qn), .Q(Q3), .Qn(d_ff_1_qn), .reset(CLR));  // open: preset, en
  and and_2 (and_2_out, Q2, Q1, Q0, CPU);
  or or_2 (or_2_out, and_3_out, and_4_out);
  and and_3 (and_3_out, d_ff_3_qn, d_ff_4_qn, CPD);
  D_Flip_Flop #(.trigger("falling")) d_ff_2 (
    .clk(or_2_out), .D(d_ff_2_qn), .Q(Q2), .Qn(d_ff_2_qn), .reset(CLR));  // open: preset, en
  and and_4 (and_4_out, Q1, Q0, CPU);
  or or_3 (or_3_out, and_5_out, and_6_out);
  and and_5 (and_5_out, d_ff_4_qn, CPD);
  D_Flip_Flop #(.trigger("falling")) d_ff_3 (
    .clk(or_3_out), .D(d_ff_3_qn), .Q(Q1), .Qn(d_ff_3_qn), .reset(CLR));  // open: preset, en
  and and_6 (and_6_out, Q0, CPU);
  or or_4 (or_4_out, CPD, CPU);
  D_Flip_Flop #(.trigger("falling")) d_ff_4 (
    .clk(or_4_out), .D(d_ff_4_qn), .Q(Q0), .Qn(d_ff_4_qn), .reset(CLR));  // open: preset, en
endmodule

module \二进制转8421BCD码电路  (
  input  A4,
  input  A3,
  input  A2,
  input  A1,
  output S13,
  output S12,
  output S11,
  output S10,
  output S03,
  output S02,
  output S01,
  output S00
);

  wire and_1_out, or_1_out;

  \先行进位的四位二进制并行加法器  \u_先行进位的四位二进制并行加法器_1  (
    .C0(1'b0), .A1(A1), .B1(1'b0), .A2(A2), .B2(and_1_out), .A3(A3), .B3(and_1_out), .A4(A4), .B4(1'b0),
    .F1(S00), .F2(S01), .F3(S02), .F4(S03), .C4(S10));
  or or_1 (or_1_out, A2, A3);
  and and_1 (and_1_out, A4, or_1_out);

  assign S11 = 1'b0;
  assign S12 = 1'b0;
  assign S13 = 1'b0;
endmodule

module \二进制转8421BCD码电路封装  (
  input  A4,
  input  A3,
  input  A2,
  input  A1,
  output out_5,
  output \十位 ,
  output out_7,
  output out_8,
  output out_9,
  output \个位 ,
  output out_11,
  output out_12
);

  // 二进制转8421BCD码电路 二进制转8421bcd码电路_1: pin names not known; wires that end beside it: out_5, \十位 , A4, out_7, A3, out_8, out_9, A2, \个位 , out_11, A1, out_12
endmodule

module \_7段译码器译码电路  (
  input  A3,
  input  A2,
  input  A1,
  input  A0,
  output a,
  output b,
  output c,
  output d,
  output e,
  output f,
  output g
);

  wire and_1_out, and_2_out, and_3_out, and_4_out, and_5_out, and_6_out, and_7_out, and_8_out, and_9_out,
       and_10_out, and_11_out, and_12_out, and_13_out, and_14_out, and_15_out, and_16_out, and_17_out,
       and_18_out, and_19_out, and_20_out, not_1_out, not_2_out, not_3_out, not_4_out;

  not not_1 (not_1_out, A3);
  not not_2 (not_2_out, A2);
  not not_3 (not_3_out, A1);
  not not_4 (not_4_out, A0);
  and and_1 (and_1_out, not_2_out, not_3_out, not_4_out);
  and and_2 (and_2_out, not_1_out, not_2_out, A1);
  and and_3 (and_3_out, not_1_out, A2, A0);
  and and_4 (and_4_out, not_3_out, A3, A0);
  and and_5 (and_5_out, not_1_out, not_2_out);
  and and_6 (and_6_out, not_2_out, not_3_out);
  and and_7 (and_7_out, not_3_out, not_4_out);
  and and_8 (and_8_out, not_1_out, A1, A0);
  and and_9 (and_9_out, not_1_out, A2);
  and and_10 (and_10_out, not_2_out, A0);
  and and_11 (and_11_out, not_2_out, A1);
  and and_12 (and_12_out, not_2_out, not_4_out);
  and and_13 (and_13_out, not_4_out, A1);
  and and_14 (and_14_out, A2, A0, not_3_out);
  and and_15 (and_15_out, not_4_out, not_3_out);
  and and_16 (and_16_out, not_3_out, A3);
  and and_17 (and_17_out, not_3_out, A2);
  and and_18 (and_18_out, not_4_out, A2);
  and and_19 (and_19_out, A1, not_4_out);
  and and_20 (and_20_out, not_2_out, A1);
  or or_1 (a, and_1_out, and_2_out, and_3_out, and_4_out);
  or or_2 (b, and_5_out, and_6_out, and_7_out, and_8_out);
  or or_3 (c, and_9_out, and_6_out, and_10_out);
  or or_4 (d, and_11_out, and_12_out, and_13_out, and_14_out);
  or or_5 (e, and_12_out, and_13_out);
  or or_6 (f, and_15_out, and_16_out, and_17_out, and_18_out);
  or or_7 (g, and_19_out, and_16_out, and_17_out, and_20_out);
endmodule

module \_7段数码显示管8421码显示电路  (
  input  in_1,
  input  in_2,
  input  in_3,
  input  in_4,
  output out_5,
  output out_6,
  output out_7,
  output out_8,
  output out_9,
  output out_10,
  output out_11,
  output out_12,
  output out_13,
  output out_14,
  output out_15,
  output out_16,
  output out_17,
  output out_18
);

  wire \二进制转8421bcd码电路_1_p1 , \二进制转8421bcd码电路_1_p2 , \二进制转8421bcd码电路_1_p4 , \二进制转8421bcd码电路_1_p6 ,
       \二进制转8421bcd码电路_1_p7 , \二进制转8421bcd码电路_1_p9 , \二进制转8421bcd码电路_1_p10 , \二进制转8421bcd码电路_1_p12 ;

  \_7段译码器译码电路  \u_7段译码器译码电路_1  (
    .A3(\二进制转8421bcd码电路_1_p1 ), .A2(\二进制转8421bcd码电路_1_p2 ), .A1(\二进制转8421bcd码电路_1_p4 ),
    .A0(\二进制转8421bcd码电路_1_p6 ), .a(out_5), .b(out_6), .c(out_7), .d(out_8), .e(out_9), .f(out_10), .g(out_11));
  // 二进制转8421BCD码电路 二进制转8421bcd码电路_1: pin names not known; wires that end beside it: \二进制转8421bcd码电路_1_p1 , \二进制转8421bcd码电路_1_p2 , in_1, \二进制转8421bcd码电路_1_p4 , in_2, \二进制转8421bcd码电路_1_p6 , \二进制转8421bcd码电路_1_p7 , in_3, \二进制转8421bcd码电路_1_p9 , \二进制转8421bcd码电路_1_p10 , in_4, \二进制转8421bcd码电路_1_p12 
  \_7段译码器译码电路  \u_7段译码器译码电路_2  (
    .A3(\二进制转8421bcd码电路_1_p7 ), .A2(\二进制转8421bcd码电路_1_p9 ), .A1(\二进制转8421bcd码电路_1_p10 ),
    .A0(\二进制转8421bcd码电路_1_p12 ), .a(out_12), .b(out_13), .c(out_14), .d(out_15), .e(out_16), .f(out_17),
    .g(out_18));
endmodule

module \_7段数码显示管显示电路封装  (
  input  in_1,
  input  in_2,
  input  in_3,
  input  in_4
);

  wire \n7段数码显示管8421码显示电路_1_out_5 , \n7段数码显示管8421码显示电路_1_out_6 , \n7段数码显示管8421码显示电路_1_out_7 ,
       \n7段数码显示管8421码显示电路_1_out_8 , \n7段数码显示管8421码显示电路_1_out_9 , \n7段数码显示管8421码显示电路_1_out_10 ,
       \n7段数码显示管8421码显示电路_1_out_11 , \n7段数码显示管8421码显示电路_1_out_12 , \n7段数码显示管8421码显示电路_1_out_13 ,
       \n7段数码显示管8421码显示电路_1_out_14 , \n7段数码显示管8421码显示电路_1_out_15 , \n7段数码显示管8421码显示电路_1_out_16 ,
       \n7段数码显示管8421码显示电路_1_out_17 , \n7段数码显示管8421码显示电路_1_out_18 ;

  _7_Segment_Display u_7_segment_display_1 (
    .g(\n7段数码显示管8421码显示电路_1_out_11 ), .f(\n7段数码显示管8421码显示电路_1_out_10 ), .a(\n7段数码显示管8421码显示电路_1_out_5 ),
    .b(\n7段数码显示管8421码显示电路_1_out_6 ), .e(\n7段数码显示管8421码显示电路_1_out_9 ), .d(\n7段数码显示管8421码显示电路_1_out_8 ),
    .c(\n7段数码显示管8421码显示电路_1_out_7 ));  // open: dp
  _7_Segment_Display u_7_segment_display_2 (
    .g(\n7段数码显示管8421码显示电路_1_out_18 ), .f(\n7段数码显示管8421码显示电路_1_out_17 ), .a(\n7段数码显示管8421码显示电路_1_out_12 ),
    .b(\n7段数码显示管8421码显示电路_1_out_13 ), .e(\n7段数码显示管8421码显示电路_1_out_16 ), .d(\n7段数码显示管8421码显示电路_1_out_15 ),
    .c(\n7段数码显示管8421码显示电路_1_out_14 ));  // open: dp
  \_7段数码显示管8421码显示电路  \u_7段数码显示管8421码显示电路_1  (
    .out_5(\n7段数码显示管8421码显示电路_1_out_5 ), .out_6(\n7段数码显示管8421码显示电路_1_out_6 ),
    .out_7(\n7段数码显示管8421码显示电路_1_out_7 ), .out_8(\n7段数码显示管8421码显示电路_1_out_8 ),
    .out_9(\n7段数码显示管8421码显示电路_1_out_9 ), .out_10(\n7段数码显示管8421码显示电路_1_out_10 ),
    .out_11(\n7段数码显示管8421码显示电路_1_out_11 ), .out_12(\n7段数码显示管8421码显示电路_1_out_12 ),
    .out_13(\n7段数码显示管8421码显示电路_1_out_13 ), .out_14(\n7段数码显示管8421码显示电路_1_out_14 ),
    .out_15(\n7段数码显示管8421码显示电路_1_out_15 ), .out_16(\n7段数码显示管8421码显示电路_1_out_16 ),
    .out_17(\n7段数码显示管8421码显示电路_1_out_17 ), .out_18(\n7段数码显示管8421码显示电路_1_out_18 ), .in_1(in_1), .in_2(in_2),
    .in_3(in_3), .in_4(in_4));
endmodule

module \报警器  (
  input  CPu,
  input  CLR,
  input  CPd,
  output A3,
  output A2,
  output A1,
  output A0,
  output \报警器 
);

  wire and_2_out, and_3_out, and_4_out, not_1_out, or_1_out;

  and and_1 (\报警器 , CPu, and_2_out);
  not not_1 (not_1_out, and_2_out);
  or or_1 (or_1_out, A0, A1, A2, A3);
  and and_2 (and_2_out, A0, A1, A2, A3);
  and and_3 (and_3_out, not_1_out, CPu);
  and and_4 (and_4_out, or_1_out, CPd);
  \四位二进制可逆加法器  \u_四位二进制可逆加法器_1  (.CLR(CLR), .CPU(and_3_out), .CPD(and_4_out), .Q3(A3), .Q2(A2), .Q1(A1), .Q0(A0));
endmodule

module \小型实验室门禁系统电路的封装  (
  input  CPu,
  input  CLR,
  input  CPd,
  output out_4,
  output out_5,
  output out_6,
  output out_7,
  output out_8,
  output out_9,
  output out_10,
  output out_11,
  output out_12,
  output out_13,
  output out_14,
  output out_15,
  output out_16,
  output out_17,
  output \报警器 
);

  wire \报警器_1_a0 , \报警器_1_a1 , \报警器_1_a2 , \报警器_1_a3 ;

  \_7段数码显示管8421码显示电路  \u_7段数码显示管8421码显示电路_1  (
    .out_5(out_4), .out_6(out_5), .out_7(out_6), .out_8(out_7), .out_9(out_8), .out_10(out_9),
    .out_11(out_10), .out_12(out_11), .out_13(out_12), .out_14(out_13), .out_15(out_14), .out_16(out_15),
    .out_17(out_16), .out_18(out_17), .in_1(\报警器_1_a3 ), .in_2(\报警器_1_a2 ), .in_3(\报警器_1_a1 ),
    .in_4(\报警器_1_a0 ));
  \报警器  \u_报警器_1  (
    .CLR(CLR), .CPu(CPu), .CPd(CPd), .A3(\报警器_1_a3 ), .A2(\报警器_1_a2 ), .A1(\报警器_1_a1 ), .A0(\报警器_1_a0 ),
    .\报警器 (\报警器 ));
endmodule

module \小型实验室门禁系统电路的测试及显示  (
);

  wire button_1_out, button_2_out, button_3_out, \小型实验室门禁系统电路的封装_1_out_4 , \小型实验室门禁系统电路的封装_1_out_5 ,
       \小型实验室门禁系统电路的封装_1_out_6 , \小型实验室门禁系统电路的封装_1_out_7 , \小型实验室门禁系统电路的封装_1_out_8 ,
       \小型实验室门禁系统电路的封装_1_out_9 , \小型实验室门禁系统电路的封装_1_out_10 , \小型实验室门禁系统电路的封装_1_out_11 ,
       \小型实验室门禁系统电路的封装_1_out_12 , \小型实验室门禁系统电路的封装_1_out_13 , \小型实验室门禁系统电路的封装_1_out_14 ,
       \小型实验室门禁系统电路的封装_1_out_15 , \小型实验室门禁系统电路的封装_1_out_16 , \小型实验室门禁系统电路的封装_1_out_17 ,
       \小型实验室门禁系统电路的封装_1_报警器 ;

  Button button_1 (.out(button_1_out));
  Button button_2 (.out(button_2_out));
  Button button_3 (.out(button_3_out));
  \小型实验室门禁系统电路的封装  \u_小型实验室门禁系统电路的封装_1  (
    .CPu(button_1_out), .CLR(button_2_out), .CPd(button_3_out), .out_4(\小型实验室门禁系统电路的封装_1_out_4 ),
    .out_5(\小型实验室门禁系统电路的封装_1_out_5 ), .out_6(\小型实验室门禁系统电路的封装_1_out_6 ), .out_7(\小型实验室门禁系统电路的封装_1_out_7 ),
    .out_8(\小型实验室门禁系统电路的封装_1_out_8 ), .out_9(\小型实验室门禁系统电路的封装_1_out_9 ), .out_10(\小型实验室门禁系统电路的封装_1_out_10 ),
    .out_11(\小型实验室门禁系统电路的封装_1_out_11 ), .out_12(\小型实验室门禁系统电路的封装_1_out_12 ),
    .out_13(\小型实验室门禁系统电路的封装_1_out_13 ), .out_14(\小型实验室门禁系统电路的封装_1_out_14 ),
    .out_15(\小型实验室门禁系统电路的封装_1_out_15 ), .out_16(\小型实验室门禁系统电路的封装_1_out_16 ),
    .out_17(\小型实验室门禁系统电路的封装_1_out_17 ), .\报警器 (\小型实验室门禁系统电路的封装_1_报警器 ));
  _7_Segment_Display u_7_segment_display_1 (
    .g(\小型实验室门禁系统电路的封装_1_out_10 ), .f(\小型实验室门禁系统电路的封装_1_out_9 ), .a(\小型实验室门禁系统电路的封装_1_out_4 ),
    .b(\小型实验室门禁系统电路的封装_1_out_5 ), .e(\小型实验室门禁系统电路的封装_1_out_8 ), .d(\小型实验室门禁系统电路的封装_1_out_7 ),
    .c(\小型实验室门禁系统电路的封装_1_out_6 ));  // open: dp
  _7_Segment_Display u_7_segment_display_2 (
    .g(\小型实验室门禁系统电路的封装_1_out_17 ), .f(\小型实验室门禁系统电路的封装_1_out_16 ), .a(\小型实验室门禁系统电路的封装_1_out_11 ),
    .b(\小型实验室门禁系统电路的封装_1_out_12 ), .e(\小型实验室门禁系统电路的封装_1_out_15 ), .d(\小型实验室门禁系统电路的封装_1_out_14 ),
    .c(\小型实验室门禁系统电路的封装_1_out_13 ));  // open: dp
  LED \u_报警灯  (.in(\小型实验室门禁系统电路的封装_1_报警器 ));
endmodule

module \四位二进制可逆加法器封装测试电路  (
  input  CPu,
  input  CLR,
  input  CPd,
  output Q3,
  output Q2,
  output Q1,
  output Q0
);

  \四位二进制可逆加法器  \u_四位二进制可逆加法器_1  (.CLR(CLR), .CPU(CPu), .CPD(CPd), .Q3(Q3), .Q2(Q2), .Q1(Q1), .Q0(Q0));
endmodule

module \报警电路私有封装测试  (
  input  CPu,
  input  CLR,
  input  Cpd,
  output A3,
  output A2,
  output A1,
  output A0
);

  wire \报警器_1_报警器 ;

  \报警器  \u_报警器_1  (.CLR(CLR), .CPu(CPu), .CPd(Cpd), .A3(A3), .A2(A2), .A1(A1), .A0(A0), .\报警器 (\报警器_1_报警器 ));
  LED led_1 (.in(\报警器_1_报警器 ));
endmodule
