// Logisim project 闹钟.circ as structural Verilog: 8 circuits, main circuit main
module main (
  input  [3:0] in_1,
  input  [7:0] in_2,
  input  [3:0] in_3,
  input  [3:0] in_4,
  input  [3:0] in_5,
  input  [3:0] in_6,
  input  [3:0] in_7,
  input  [3:0] in_8,
  input  [3:0] in_9,
  input  [3:0] in_10,
  input  [3:0] in_11,
  input  in_12,
  input  [7:0] in_13,
  input  in_14,
  input  in_15,
  input  in_16,
  input  in_17,
  input  [3:0] in_18,
  input  [3:0] in_19,
  input  [3:0] in_20,
  input  [3:0] in_21,
  output out_22
);

  wire button_1_out, button_2_out, button_3_out, button_4_out, button_5_out, button_6_out, clock_1_out,
       clock_2_out, \多功能数字钟电路_1_out_18 , \多功能数字钟电路_1_定点报时 , \电子钟整点报时电路_1_out_17 , \闹钟_1_led ;
  wire [3:0] \多功能数字钟电路_1_out_10 , \多功能数字钟电路_1_out_11 , \多功能数字钟电路_1_out_12 , \多功能数字钟电路_1_out_13 ,
       \多功能数字钟电路_1_out_19 , \多功能数字钟电路_1_out_21 , \校准12进制计数器_1_q0a , \校准12进制计数器_1_q1a ;
  wire [4:0] \多功能数字钟电路_1_out_14 , \多功能数字钟电路_1_out_15 , \多功能数字钟电路_1_out_16 , \多功能数字钟电路_1_out_17 ;

  DotMatrix #(.matrixcols(4), .matrixrows(5)) dotmatrix_1 (
    .col0(\多功能数字钟电路_1_out_14 ), .col1(\多功能数字钟电路_1_out_15 ), .col2(\多功能数字钟电路_1_out_16 ),
    .col3(\多功能数字钟电路_1_out_17 ));
  \多功能数字钟电路  \u_多功能数字钟电路_1  (
    .out_18(\多功能数字钟电路_1_out_18 ), .in_1(in_2), .in_2(in_13), .SET(in_15), .CLR(button_3_out),
    .out_12(\多功能数字钟电路_1_out_12 ), .out_13(\多功能数字钟电路_1_out_13 ), .out_14(\多功能数字钟电路_1_out_14 ),
    .out_15(\多功能数字钟电路_1_out_15 ), .out_16(\多功能数字钟电路_1_out_16 ), .out_17(\多功能数字钟电路_1_out_17 ),
    .out_21(\多功能数字钟电路_1_out_21 ), .out_19(\多功能数字钟电路_1_out_19 ), .\定点报时 (\多功能数字钟电路_1_定点报时 ),
    .out_10(\多功能数字钟电路_1_out_10 ), .out_11(\多功能数字钟电路_1_out_11 ), .Adj0(in_12), .Adj1(in_14),
    .CPd(button_2_out), .CPu(button_1_out), .CP(clock_1_out));
  Clock clock_1 (.out(clock_1_out));
  Hex_Digit_Display hex_digit_display_1 (.value(\多功能数字钟电路_1_out_12 ));  // open: dp
  Button button_1 (.out(button_1_out));
  \电子钟整点报时电路  \u_电子钟整点报时电路_1  (
    .out_17(\电子钟整点报时电路_1_out_17 ), .in_1(in_18[3]), .in_2(in_18[2]), .in_3(in_18[1]), .in_4(in_18[0]),
    .in_5(in_20[3]), .in_6(in_20[2]), .in_7(in_20[1]), .in_8(in_20[0]), .in_9(in_21[3]), .in_10(in_21[2]),
    .in_11(in_21[1]), .in_12(in_21[0]), .in_13(in_19[3]), .in_14(in_19[2]), .in_15(in_19[1]), .in_16(in_19[0]));
  Hex_Digit_Display hex_digit_display_2 (.value(\多功能数字钟电路_1_out_21 ));  // open: dp
  Hex_Digit_Display hex_digit_display_3 (.value(\多功能数字钟电路_1_out_13 ));  // open: dp
  Button button_2 (.out(button_2_out));
  LED led_1 (.in(\电子钟整点报时电路_1_out_17 ));
  Hex_Digit_Display hex_digit_display_4 (.value(\多功能数字钟电路_1_out_19 ));  // open: dp
  Button button_3 (.out(button_3_out));
  Hex_Digit_Display hex_digit_display_5 (.value(\多功能数字钟电路_1_out_10 ));  // open: dp
  Hex_Digit_Display hex_digit_display_6 (.value(\多功能数字钟电路_1_out_11 ));  // open: dp
  LED led_2 (.in(\多功能数字钟电路_1_out_18 ));
  LED led_3 (.in(\多功能数字钟电路_1_定点报时 ));
  \校准12进制计数器  \u_校准12进制计数器_1  (
    .Q1d(\校准12进制计数器_1_q1a [3]), .Q1c(\校准12进制计数器_1_q1a [2]), .Q1b(\校准12进制计数器_1_q1a [1]),
    .Q1a(\校准12进制计数器_1_q1a [0]), .Adj(in_16), .CPd(button_5_out), .Qcc(out_22), .Q0d(\校准12进制计数器_1_q0a [3]),
    .Q0c(\校准12进制计数器_1_q0a [2]), .Q0b(\校准12进制计数器_1_q0a [1]), .Q0a(\校准12进制计数器_1_q0a [0]), .CPu(button_4_out),
    .Clr(button_6_out), .Set(in_17), .CP(clock_2_out));
  Button button_4 (.out(button_4_out));
  Button button_5 (.out(button_5_out));
  LED led_4 (.in(\闹钟_1_led ));
  Hex_Digit_Display hex_digit_display_7 (.value(\校准12进制计数器_1_q1a ));  // open: dp
  \闹钟  \u_闹钟_1  (
    .in_1(in_3[3]), .in_2(in_7[3]), .in_3(in_3[2]), .in_4(in_7[2]), .in_5(in_3[1]), .in_6(in_7[1]),
    .in_7(in_3[0]), .in_8(in_7[0]), .in_9(in_4[3]), .in_10(in_8[3]), .in_11(in_4[2]), .in_12(in_8[2]),
    .in_13(in_4[1]), .in_14(in_8[1]), .in_15(in_4[0]), .in_16(in_8[0]), .in_17(in_5[3]), .in_18(in_9[3]),
    .in_19(in_5[2]), .in_20(in_9[2]), .in_21(in_5[1]), .in_22(in_9[1]), .in_23(in_5[0]), .in_24(in_9[0]),
    .in_25(in_6[3]), .in_26(in_10[3]), .in_27(in_6[2]), .in_28(in_10[2]), .in_29(in_6[1]), .in_30(in_10[1]),
    .in_31(in_6[0]), .in_32(in_10[0]), .in_33(in_11[3]), .in_34(in_11[2]), .in_35(in_11[1]),
    .in_36(in_11[0]), .in_37(in_1[0]), .in_38(in_1[3]), .in_39(in_1[2]), .in_40(in_1[1]), .LED(\闹钟_1_led ));
  Clock clock_2 (.out(clock_2_out));
  Hex_Digit_Display hex_digit_display_8 (.value(\校准12进制计数器_1_q0a ));  // open: dp
  Button button_6 (.out(button_6_out));
endmodule

module \校准60进制计数器  (
  input  CPd,
  input  Adj,
  input  Clock,
  input  CPu,
  input  Clr,
  output Qcc,
  output Q1d,
  output Q1c,
  output Q1b,
  output Q1a,
  output Q0d,
  output Q0c,
  output Q0b,
  output Q0a
);

  wire and_1_out, and_2_out, and_3_out, and_4_out, and_5_out, not_1_out, not_2_out, not_3_out, not_4_out,
       not_5_out, or_1_out, or_2_out, or_3_out, or_4_out;

  or or_1 (or_1_out, Q0d, Q0c, Q0b, Q0a);
  not not_1 (not_1_out, Q0c);
  and and_1 (and_1_out, Q0d, not_1_out, Q0b, not_3_out);
  and and_2 (and_2_out, or_1_out, CPd);
  and and_3 (and_3_out, and_2_out, Adj);
  not not_2 (not_2_out, Adj);
  and and_4 (and_4_out, not_2_out, Clock);
  and and_5 (and_5_out, Adj, CPu);
  not not_3 (not_3_out, Q0a);
  \四位二进制可逆加法器  \u_四位二进制可逆加法器_1  (.CLR(or_2_out), .CPU(and_1_out), .CPD(1'b0), .Q3(Q1d), .Q2(Q1c), .Q1(Q1b), .Q0(Q1a));
  or or_2 (or_2_out, Clr, Qcc);
  not not_4 (not_4_out, Q1d);
  or or_3 (or_3_out, and_1_out, or_2_out);
  not not_5 (not_5_out, Q1a);
  or or_4 (or_4_out, and_4_out, and_5_out);
  \四位二进制可逆加法器  \u_四位二进制可逆加法器_2  (
    .CLR(or_3_out), .CPU(or_4_out), .CPD(and_3_out), .Q3(Q0d), .Q2(Q0c), .Q1(Q0b), .Q0(Q0a));
  and and_6 (Qcc, not_5_out, Q1b, Q1c, not_4_out);
endmodule

module \校准12进制计数器  (
  input  Set,
  input  CPu,
  input  Adj,
  input  CP,
  input  CPd,
  input  Clr,
  output Qcc,
  output Q1d,
  output Q1c,
  output Q1b,
  output Q1a,
  output Q0d,
  output Q0c,
  output Q0b,
  output Q0a
);

  wire and_1_out, and_2_out, and_3_out, and_4_out, and_5_out, and_6_out, not_1_out, not_2_out, not_3_out,
       not_4_out, not_5_out, not_6_out, not_7_out, not_8_out, not_9_out, or_1_out, \校准60进制计数器_1_qcc ;

  and and_1 (and_1_out, not_2_out, not_4_out, Q1b, not_1_out);
  not not_1 (not_1_out, Q1a);
  not not_2 (not_2_out, Q1d);
  \校准60进制计数器  \u_校准60进制计数器_1  (
    .CPd(CPd), .Adj(Adj), .CPu(CPu), .Clr(or_1_out), .Q1d(Q1d), .Q1c(Q1c), .Q1b(Q1b), .Q1a(Q1a), .Q0d(Q0d),
    .Qcc(\校准60进制计数器_1_qcc ), .Q0c(Q0c), .Q0b(Q0b), .Q0a(Q0a), .Clock(CP));
  and and_2 (and_2_out, not_2_out, not_4_out, not_3_out, Q1a);
  not not_3 (not_3_out, Q1b);
  not not_4 (not_4_out, Q1c);
  and and_3 (and_3_out, not_7_out, Q0c, not_5_out, not_8_out);
  not not_5 (not_5_out, Q0b);
  and and_4 (and_4_out, not_7_out, not_6_out, Q0b, not_8_out);
  not not_6 (not_6_out, Q0c);
  not not_7 (not_7_out, Q0d);
  not not_8 (not_8_out, Q0a);
  or or_1 (or_1_out, Qcc, Clr);
  not not_9 (not_9_out, Set);
  and and_5 (and_5_out, and_2_out, and_4_out, not_9_out);
  or or_2 (Qcc, and_5_out, and_6_out);
  and and_6 (and_6_out, and_1_out, and_3_out, Set);
  // also tied to GND on the sheet: \校准60进制计数器_1_qcc 
endmodule

module \显示上午下午的电路  (
  input  AM_FM,
  input  TT,
  output [4:0] out_3,
  output [4:0] out_4,
  output [4:0] out_5,
  output [4:0] out_6
);

  wire [4:0] multiplexer_1_out, multiplexer_2_out;

  Multiplexer #(.width(5), .enable("false")) multiplexer_1 (
    .in0(5'b00001), .in1(5'b10000), .out(multiplexer_1_out), .sel(AM_FM));
  Multiplexer #(.width(5), .enable("false")) multiplexer_2 (
    .in0(5'b00101), .in1(5'b10100), .out(multiplexer_2_out), .sel(AM_FM));
  Multiplexer #(.width(5), .enable("false")) multiplexer_3 (
    .in0({5{1'b0}}), .in1(multiplexer_1_out), .out(out_3), .sel(TT));
  Multiplexer #(.width(5), .enable("false")) multiplexer_4 (.in0({5{1'b0}}), .in1({5{1'b1}}), .out(out_4), .sel(TT));
  Multiplexer #(.width(5), .enable("false")) multiplexer_5 (
    .in0({5{1'b0}}), .in1(multiplexer_2_out), .out(out_5), .sel(TT));

  assign out_6 = out_3;
endmodule

module \电子钟整点报时电路  (
  input  in_1,
  input  in_2,
  input  in_3,
  input  in_4,
  input  in_5,
  input  in_6,
  input  in_7,
  input  in_8,
  input  in_9,
  input  in_10,
  input  in_11,
  input  in_12,
  input  in_13,
  input  in_14,
  input  in_15,
  input  in_16,
  output out_17
);

  wire and_1_out, and_3_out, and_4_out, and_5_out, and_6_out, and_7_out, and_8_out, not_1_out, not_2_out,
       not_3_out, not_4_out, not_5_out, not_6_out, not_7_out, not_8_out, not_9_out, not_10_out, not_11_out,
       not_12_out, or_1_out;

  not not_1 (not_1_out, in_1);
  not not_2 (not_2_out, in_3);
  and and_1 (and_1_out, not_1_out, in_2, not_2_out, in_4, in_5, not_3_out, not_4_out, in_8);
  not not_3 (not_3_out, in_6);
  not not_4 (not_4_out, in_7);
  and and_2 (out_17, and_1_out, or_1_out);
  not not_5 (not_5_out, in_9);
  and and_3 (and_3_out, not_5_out, in_10, not_7_out, in_12, not_10_out, not_9_out, not_11_out, not_12_out);
  not not_6 (not_6_out, in_10);
  not not_7 (not_7_out, in_11);
  and and_4 (and_4_out, not_5_out, in_10, not_7_out, in_12, not_10_out, not_9_out, in_15, not_12_out);
  not not_8 (not_8_out, in_12);
  not not_9 (not_9_out, in_14);
  not not_10 (not_10_out, in_13);
  or or_1 (or_1_out, and_3_out, and_4_out, and_5_out, and_6_out, and_7_out, and_8_out);
  and and_5 (and_5_out, not_5_out, in_10, not_7_out, in_12, not_10_out, in_14, not_11_out, not_12_out);
  not not_11 (not_11_out, in_15);
  not not_12 (not_12_out, in_16);
  and and_6 (and_6_out, not_5_out, in_10, not_7_out, in_12, not_10_out, in_14, in_15, not_12_out);
  and and_7 (and_7_out, not_5_out, in_10, not_7_out, in_12, in_13, not_9_out, not_11_out, not_12_out);
  and and_8 (and_8_out, not_5_out, not_6_out, not_7_out, not_8_out, not_10_out, not_9_out, not_11_out, not_12_out);
endmodule

module \秒计时脉冲产生电路  (
  input  CP,
  output Z
);

  wire j_k_ff_2_q;

  J_K_Flip_Flop j_k_ff_1 (.J(1'b1), .clk(j_k_ff_2_q), .K(1'b1), .Q(Z));  // open: Qn, preset, en, reset
  J_K_Flip_Flop j_k_ff_2 (.J(1'b1), .clk(CP), .K(1'b1), .Q(j_k_ff_2_q));  // open: Qn, preset, en, reset
endmodule

module \闹钟  (
  input  in_1,
  input  in_2,
  input  in_3,
  input  in_4,
  input  in_5,
  input  in_6,
  input  in_7,
  input  in_8,
  input  in_9,
  input  in_10,
  input  in_11,
  input  in_12,
  input  in_13,
  input  in_14,
  input  in_15,
  input  in_16,
  input  in_17,
  input  in_18,
  input  in_19,
  input  in_20,
  input  in_21,
  input  in_22,
  input  in_23,
  input  in_24,
  input  in_25,
  input  in_26,
  input  in_27,
  input  in_28,
  input  in_29,
  input  in_30,
  input  in_31,
  input  in_32,
  input  in_33,
  input  in_34,
  input  in_35,
  input  in_36,
  input  in_37,
  input  in_38,
  input  in_39,
  input  in_40,
  output LED
);

  wire and_1_out, not_2_out, not_3_out, not_4_out, or_1_out, or_2_out, or_3_out, or_4_out, or_5_out,
       or_6_out, or_7_out, or_8_out, xor_1_out, xor_2_out, xor_3_out, xor_4_out, xor_5_out, xor_6_out,
       xor_7_out, xor_8_out, xor_9_out, xor_10_out, xor_11_out, xor_12_out, xor_13_out, xor_14_out,
       xor_15_out, xor_16_out;

  xor xor_1 (xor_1_out, in_1, in_2);
  xor xor_2 (xor_2_out, in_3, in_4);
  xor xor_3 (xor_3_out, in_7, in_8);
  xor xor_4 (xor_4_out, in_5, in_6);
  xor xor_5 (xor_5_out, in_9, in_10);
  xor xor_6 (xor_6_out, in_11, in_12);
  xor xor_7 (xor_7_out, in_13, in_14);
  xor xor_8 (xor_8_out, in_15, in_16);
  or or_1 (or_1_out, xor_1_out, xor_2_out, xor_4_out, xor_3_out, xor_5_out, xor_6_out, xor_7_out, xor_8_out, xor_9_out, xor_10_out, xor_11_out, xor_13_out, xor_12_out, xor_14_out, xor_15_out, xor_16_out);
  xor xor_9 (xor_9_out, in_17, in_18);
  xor xor_10 (xor_10_out, in_19, in_20);
  xor xor_11 (xor_11_out, in_21, in_22);
  xor xor_12 (xor_12_out, in_25, in_26);
  xor xor_13 (xor_13_out, in_23, in_24);
  not not_1 (LED, or_2_out);
  or or_2 (or_2_out, or_1_out, or_3_out);
  xor xor_14 (xor_14_out, in_27, in_28);
  xor xor_15 (xor_15_out, in_29, in_30);
  xor xor_16 (xor_16_out, in_31, in_32);
  or or_3 (or_3_out, in_33, in_34, in_35, in_36, in_37, and_1_out);
  and and_1 (and_1_out, or_5_out, or_4_out, or_7_out, or_6_out, or_8_out);
  or or_4 (or_4_out, in_38, not_4_out, in_40);
  or or_5 (or_5_out, in_38, in_39, not_3_out);
  or or_6 (or_6_out, not_2_out, in_39, in_40);
  or or_7 (or_7_out, in_38, not_4_out, not_3_out);
  not not_2 (not_2_out, in_38);
  or or_8 (or_8_out, in_38, in_39, in_40);
  not not_3 (not_3_out, in_40);
  not not_4 (not_4_out, in_39);
endmodule

module \多功能数字钟电路  (
  input  [7:0] in_1,
  input  [7:0] in_2,
  input  SET,
  input  CLR,
  input  CP,
  input  Adj0,
  input  Adj1,
  input  CPd,
  input  CPu,
  output [3:0] out_10,
  output [3:0] out_11,
  output [3:0] out_12,
  output [3:0] out_13,
  output [4:0] out_14,
  output [4:0] out_15,
  output [4:0] out_16,
  output [4:0] out_17,
  output out_18,
  output [3:0] out_19,
  output \定点报时 ,
  output [3:0] out_21
);

  wire and_1_out, and_2_out, and_3_out, and_4_out, and_5_out, and_6_out, not_1_out, not_2_out, t_ff_1_q,
       \校准12进制计数器_1_qcc , \校准60进制计数器_1_qcc , \校准60进制计数器_2_qcc , \秒计时脉冲产生电路_1_z ;

  \校准12进制计数器  \u_校准12进制计数器_1  (
    .Q1d(out_12[3]), .Q1c(out_12[2]), .Q1b(out_12[1]), .Q1a(out_12[0]), .Adj(and_2_out), .CPd(and_1_out),
    .Qcc(\校准12进制计数器_1_qcc ), .Q0d(out_13[3]), .Q0c(out_13[2]), .Q0b(out_13[1]), .Q0a(out_13[0]),
    .CPu(and_3_out), .Clr(CLR), .Set(SET), .CP(\校准60进制计数器_1_qcc ));
  and and_1 (and_1_out, and_2_out, CPd);
  and and_2 (and_2_out, Adj0, not_2_out);
  \显示上午下午的电路  \u_显示上午下午的电路_1  (
    .AM_FM(t_ff_1_q), .TT(not_1_out), .out_3(out_14), .out_4(out_15), .out_5(out_16), .out_6(out_17));
  not not_1 (not_1_out, SET);
  T_Flip_Flop t_ff_1 (.clk(\校准12进制计数器_1_qcc ), .T(1'b1), .Q(t_ff_1_q));  // open: Qn, preset, reset, en
  and and_3 (and_3_out, and_2_out, CPu);
  not not_2 (not_2_out, Adj1);
  and and_4 (and_4_out, Adj0, Adj1);
  \校准60进制计数器  \u_校准60进制计数器_1  (
    .CPd(and_5_out), .Adj(and_4_out), .CPu(and_6_out), .Clr(CLR), .Q1d(out_21[3]), .Q1c(out_21[2]),
    .Q1b(out_21[1]), .Q1a(out_21[0]), .Q0d(out_19[3]), .Qcc(\校准60进制计数器_1_qcc ), .Q0c(out_19[2]),
    .Q0b(out_19[1]), .Q0a(out_19[0]), .Clock(\校准60进制计数器_2_qcc ));
  and and_5 (and_5_out, and_4_out, CPd);
  and and_6 (and_6_out, and_4_out, CPu);
  \闹钟  \u_闹钟_1  (
    .in_1(in_1[7]), .in_2(out_12[3]), .in_3(in_1[6]), .in_4(out_12[2]), .in_5(in_1[5]), .in_6(out_12[1]),
    .in_7(in_1[4]), .in_8(out_12[0]), .in_9(in_1[3]), .in_10(out_13[3]), .in_11(in_1[2]), .in_12(out_13[2]),
    .in_13(in_1[1]), .in_14(out_13[1]), .in_15(in_1[0]), .in_16(out_13[0]), .in_17(in_2[7]),
    .in_18(out_19[0]), .in_19(in_2[6]), .in_20(out_19[1]), .in_21(in_2[5]), .in_22(out_19[2]),
    .in_23(in_2[4]), .in_24(out_19[3]), .in_25(in_2[3]), .in_26(out_21[0]), .in_27(in_2[2]),
    .in_28(out_21[1]), .in_29(in_2[1]), .in_30(out_21[2]), .in_31(in_2[0]), .in_32(out_21[3]),
    .in_33(out_10[3]), .in_34(out_10[2]), .in_35(out_10[1]), .in_36(out_10[0]), .in_37(out_11[0]),
    .in_38(out_11[3]), .in_39(out_11[2]), .in_40(out_11[1]), .LED(out_18));
  \电子钟整点报时电路  \u_电子钟整点报时电路_1  (
    .out_17(\定点报时 ), .in_1(out_21[3]), .in_2(out_21[2]), .in_3(out_21[1]), .in_4(out_21[0]),
    .in_5(out_19[3]), .in_6(out_19[2]), .in_7(out_19[1]), .in_8(out_19[0]), .in_9(out_10[3]),
    .in_10(out_10[2]), .in_11(out_10[1]), .in_12(out_10[0]), .in_13(out_11[3]), .in_14(out_11[2]),
    .in_15(out_11[1]), .in_16(out_11[0]));
  \校准60进制计数器  \u_校准60进制计数器_2  (
    .CPd(1'b0), .Adj(1'b0), .CPu(1'b0), .Clr(CLR), .Q1d(out_10[3]), .Q1c(out_10[2]), .Q1b(out_10[1]),
    .Q1a(out_10[0]), .Q0d(out_11[3]), .Qcc(\校准60进制计数器_2_qcc ), .Q0c(out_11[2]), .Q0b(out_11[1]),
    .Q0a(out_11[0]), .Clock(\秒计时脉冲产生电路_1_z ));
  \秒计时脉冲产生电路  \u_秒计时脉冲产生电路_1  (.CP(CP), .Z(\秒计时脉冲产生电路_1_z ));
endmodule
