// Logisim project 32_1除法器.circ as structural Verilog: 1 circuit, main circuit main
module main (
  input  [31:0] n2,
  input  [31:0] n1,
  input  [31:0] d,
  output [31:0] n2_prime,
  output [31:0] n1_prime
);

  wire bitselector_1_out, comparator_1_lt;
  wire [31:0] adder_1_out, bit_extender_1_out, multiplexer_2_out, shifter_1_out, shifter_2_out,
       subtractor_1_out;

  Shifter #(.width(32)) shifter_1 (.in(n2), .\dist (5'b00001), .out(shifter_1_out));
  BitSelector #(.width(32)) bitselector_1 (.in(n2), .out(bitselector_1_out), .sel({5{1'b1}}));
  Shifter #(.width(32)) shifter_2 (.in(n1), .\dist (5'b00001), .out(shifter_2_out));
  assign bit_extender_1_out = {{31{1'b0}}, bitselector_1_out};  // Bit_Extender bit_extender_1
  Adder #(.width(32)) adder_1 (.a(bit_extender_1_out), .b(shifter_2_out), .out(adder_1_out));  // open: cin, cout
  Subtractor #(.width(32)) subtractor_1 (.a(adder_1_out), .b(d), .out(subtractor_1_out));  // open: bin, bout
  Comparator #(.width(32)) comparator_1 (.a(adder_1_out), .b(d), .lt(comparator_1_lt));  // open: gt, eq
  Multiplexer #(.width(32), .enable("false")) multiplexer_1 (
    .in0(subtractor_1_out), .in1(adder_1_out), .out(n1_prime), .sel(comparator_1_lt));
  Multiplexer #(.width(32), .enable("false")) multiplexer_2 (
    .in0(32'h1), .in1({32{1'b0}}), .out(multiplexer_2_out), .sel(comparator_1_lt));
  Adder #(.width(32)) adder_2 (.a(shifter_1_out), .b(multiplexer_2_out), .out(n2_prime));  // open: cin, cout
endmodule
