// Logisim project 32_32乘法器.circ as structural Verilog: 1 circuit, main circuit main
module main (
  input  [31:0] a,
  input  [31:0] b,
  output [31:0] p
);

  wire [31:0] adder_1_out, adder_2_out, adder_3_out, adder_4_out, adder_5_out, adder_6_out, main_1_p,
       main_2_p, main_3_p, main_4_p, main_5_p, main_6_p, main_7_p, main_8_p, shifter_1_out, shifter_2_out,
       shifter_3_out, shifter_4_out, shifter_5_out, shifter_6_out, shifter_7_out;

  \_32_4乘法器_main  main_1 (.a(a[3:0]), .b(b), .p(main_1_p));
  \_32_4乘法器_main  main_2 (.a(a[7:4]), .b(b), .p(main_2_p));
  \_32_4乘法器_main  main_3 (.a(a[11:8]), .b(b), .p(main_3_p));
  \_32_4乘法器_main  main_4 (.a(a[15:12]), .b(b), .p(main_4_p));
  \_32_4乘法器_main  main_5 (.a(a[19:16]), .b(b), .p(main_5_p));
  \_32_4乘法器_main  main_6 (.a(a[23:20]), .b(b), .p(main_6_p));
  \_32_4乘法器_main  main_7 (.a(a[27:24]), .b(b), .p(main_7_p));
  \_32_4乘法器_main  main_8 (.a(a[31:28]), .b(b), .p(main_8_p));
  Shifter #(.width(32)) shifter_1 (.in(main_2_p), .\dist (5'b00100), .out(shifter_1_out));
  Shifter #(.width(32)) shifter_2 (.in(main_3_p), .\dist (5'b01000), .out(shifter_2_out));
  Shifter #(.width(32)) shifter_3 (.in(main_4_p), .\dist (5'b01100), .out(shifter_3_out));
  Shifter #(.width(32)) shifter_4 (.in(main_5_p), .\dist (5'b10000), .out(shifter_4_out));
  Shifter #(.width(32)) shifter_5 (.in(main_6_p), .\dist (5'b10100), .out(shifter_5_out));
  Shifter #(.width(32)) shifter_6 (.in(main_7_p), .\dist (5'b11000), .out(shifter_6_out));
  Shifter #(.width(32)) shifter_7 (.in(main_8_p), .\dist (5'b11100), .out(shifter_7_out));
  Adder #(.width(32)) adder_1 (.a(main_1_p), .b(shifter_1_out), .out(adder_1_out));  // open: cin, cout
  Adder #(.width(32)) adder_2 (.a(adder_1_out), .b(shifter_2_out), .out(adder_2_out));  // open: cin, cout
  Adder #(.width(32)) adder_3 (.a(adder_2_out), .b(shifter_3_out), .out(adder_3_out));  // open: cin, cout
  Adder #(.width(32)) adder_4 (.a(adder_3_out), .b(shifter_4_out), .out(adder_4_out));  // open: cin, cout
  Adder #(.width(32)) adder_5 (.a(adder_4_out), .b(shifter_5_out), .out(adder_5_out));  // open: cin, cout
  Adder #(.width(32)) adder_6 (.a(adder_5_out), .b(shifter_6_out), .out(adder_6_out));  // open: cin, cout
  Adder #(.width(32)) adder_7 (.a(adder_6_out), .b(shifter_7_out), .out(p));  // open: cin, cout
endmodule
