// Logisim project 32位除法器_1.circ as structural Verilog: 1 circuit, main circuit main
module main (
  input  [31:0] in_1,
  input  [31:0] in_2,
  output [31:0] out_3,
  output [31:0] out_4,
  output [31:0] out_5
);

  wire [31:0] main_1_n1_prime, main_1_n2_prime, main_2_n1_prime, main_2_n2_prime, main_3_n1_prime,
       main_3_n2_prime, main_5_n1_prime, main_5_n2_prime, main_6_n1_prime, main_6_n2_prime, main_7_n1_prime,
       main_7_n2_prime, main_8_n1_prime, main_8_n2_prime, main_9_n1_prime, main_9_n2_prime, main_10_n1_prime,
       main_10_n2_prime, main_11_n1_prime, main_11_n2_prime, main_12_n1_prime, main_12_n2_prime,
       main_13_n1_prime, main_13_n2_prime, main_14_n1_prime, main_14_n2_prime, main_15_n1_prime,
       main_15_n2_prime, main_16_n1_prime, main_16_n2_prime, main_17_n1_prime, main_17_n2_prime,
       main_18_n1_prime, main_18_n2_prime, main_19_n1_prime, main_19_n2_prime, main_20_n1_prime,
       main_20_n2_prime, main_21_n1_prime, main_21_n2_prime, main_22_n1_prime, main_22_n2_prime,
       main_23_n1_prime, main_23_n2_prime, main_24_n1_prime, main_24_n2_prime, main_25_n1_prime,
       main_25_n2_prime, main_26_n1_prime, main_26_n2_prime, main_27_n1_prime, main_27_n2_prime,
       main_28_n1_prime, main_28_n2_prime, main_29_n1_prime, main_29_n2_prime, main_30_n1_prime,
       main_30_n2_prime, main_31_n1_prime, main_31_n2_prime, main_32_n1_prime, main_32_n2_prime;

  \_32_1除法器_main  main_1 (.n2(in_1), .n1({32{1'b0}}), .d(in_2), .n2_prime(main_1_n2_prime), .n1_prime(main_1_n1_prime));
  \_32_1除法器_main  main_2 (
    .n2(main_3_n2_prime), .n1(main_3_n1_prime), .d(in_2), .n2_prime(main_2_n2_prime),
    .n1_prime(main_2_n1_prime));
  \_32_1除法器_main  main_3 (
    .n2(main_8_n2_prime), .n1(main_8_n1_prime), .d(in_2), .n2_prime(main_3_n2_prime),
    .n1_prime(main_3_n1_prime));
  \_32_1除法器_main  main_4 (.n2(main_10_n2_prime), .n1(main_10_n1_prime), .d(in_2), .n2_prime(out_5), .n1_prime(out_4));
  \_32_1除法器_main  main_5 (
    .n2(main_1_n2_prime), .n1(main_1_n1_prime), .d(in_2), .n2_prime(main_5_n2_prime),
    .n1_prime(main_5_n1_prime));
  \_32_1除法器_main  main_6 (
    .n2(main_2_n2_prime), .n1(main_2_n1_prime), .d(in_2), .n2_prime(main_6_n2_prime),
    .n1_prime(main_6_n1_prime));
  \_32_1除法器_main  main_7 (
    .n2(main_5_n2_prime), .n1(main_5_n1_prime), .d(in_2), .n2_prime(main_7_n2_prime),
    .n1_prime(main_7_n1_prime));
  \_32_1除法器_main  main_8 (
    .n2(main_12_n2_prime), .n1(main_12_n1_prime), .d(in_2), .n2_prime(main_8_n2_prime),
    .n1_prime(main_8_n1_prime));
  \_32_1除法器_main  main_9 (
    .n2(main_6_n2_prime), .n1(main_6_n1_prime), .d(in_2), .n2_prime(main_9_n2_prime),
    .n1_prime(main_9_n1_prime));
  \_32_1除法器_main  main_10 (
    .n2(main_14_n2_prime), .n1(main_14_n1_prime), .d(in_2), .n2_prime(main_10_n2_prime),
    .n1_prime(main_10_n1_prime));
  \_32_1除法器_main  main_11 (
    .n2(main_7_n2_prime), .n1(main_7_n1_prime), .d(in_2), .n2_prime(main_11_n2_prime),
    .n1_prime(main_11_n1_prime));
  \_32_1除法器_main  main_12 (
    .n2(main_16_n2_prime), .n1(main_16_n1_prime), .d(in_2), .n2_prime(main_12_n2_prime),
    .n1_prime(main_12_n1_prime));
  \_32_1除法器_main  main_13 (
    .n2(main_9_n2_prime), .n1(main_9_n1_prime), .d(in_2), .n2_prime(main_13_n2_prime),
    .n1_prime(main_13_n1_prime));
  \_32_1除法器_main  main_14 (
    .n2(main_18_n2_prime), .n1(main_18_n1_prime), .d(in_2), .n2_prime(main_14_n2_prime),
    .n1_prime(main_14_n1_prime));
  \_32_1除法器_main  main_15 (
    .n2(main_11_n2_prime), .n1(main_11_n1_prime), .d(in_2), .n2_prime(main_15_n2_prime),
    .n1_prime(main_15_n1_prime));
  \_32_1除法器_main  main_16 (
    .n2(main_19_n2_prime), .n1(main_19_n1_prime), .d(in_2), .n2_prime(main_16_n2_prime),
    .n1_prime(main_16_n1_prime));
  \_32_1除法器_main  main_17 (
    .n2(main_13_n2_prime), .n1(main_13_n1_prime), .d(in_2), .n2_prime(main_17_n2_prime),
    .n1_prime(main_17_n1_prime));
  \_32_1除法器_main  main_18 (
    .n2(main_20_n2_prime), .n1(main_20_n1_prime), .d(in_2), .n2_prime(main_18_n2_prime),
    .n1_prime(main_18_n1_prime));
  \_32_1除法器_main  main_19 (
    .n2(main_24_n2_prime), .n1(main_24_n1_prime), .d(in_2), .n2_prime(main_19_n2_prime),
    .n1_prime(main_19_n1_prime));
  \_32_1除法器_main  main_20 (
    .n2(main_26_n2_prime), .n1(main_26_n1_prime), .d(in_2), .n2_prime(main_20_n2_prime),
    .n1_prime(main_20_n1_prime));
  \_32_1除法器_main  main_21 (
    .n2(main_15_n2_prime), .n1(main_15_n1_prime), .d(in_2), .n2_prime(main_21_n2_prime),
    .n1_prime(main_21_n1_prime));
  \_32_1除法器_main  main_22 (
    .n2(main_17_n2_prime), .n1(main_17_n1_prime), .d(in_2), .n2_prime(main_22_n2_prime),
    .n1_prime(main_22_n1_prime));
  \_32_1除法器_main  main_23 (
    .n2(main_21_n2_prime), .n1(main_21_n1_prime), .d(in_2), .n2_prime(main_23_n2_prime),
    .n1_prime(main_23_n1_prime));
  \_32_1除法器_main  main_24 (
    .n2(main_28_n2_prime), .n1(main_28_n1_prime), .d(in_2), .n2_prime(main_24_n2_prime),
    .n1_prime(main_24_n1_prime));
  \_32_1除法器_main  main_25 (
    .n2(main_22_n2_prime), .n1(main_22_n1_prime), .d(in_2), .n2_prime(main_25_n2_prime),
    .n1_prime(main_25_n1_prime));
  \_32_1除法器_main  main_26 (
    .n2(main_30_n2_prime), .n1(main_30_n1_prime), .d(in_2), .n2_prime(main_26_n2_prime),
    .n1_prime(main_26_n1_prime));
  \_32_1除法器_main  main_27 (
    .n2(main_23_n2_prime), .n1(main_23_n1_prime), .d(in_2), .n2_prime(main_27_n2_prime),
    .n1_prime(main_27_n1_prime));
  \_32_1除法器_main  main_28 (
    .n2(main_31_n2_prime), .n1(main_31_n1_prime), .d(in_2), .n2_prime(main_28_n2_prime),
    .n1_prime(main_28_n1_prime));
  \_32_1除法器_main  main_29 (
    .n2(main_25_n2_prime), .n1(main_25_n1_prime), .d(in_2), .n2_prime(main_29_n2_prime),
    .n1_prime(main_29_n1_prime));
  \_32_1除法器_main  main_30 (
    .n2(main_32_n2_prime), .n1(main_32_n1_prime), .d(in_2), .n2_prime(main_30_n2_prime),
    .n1_prime(main_30_n1_prime));
  \_32_1除法器_main  main_31 (
    .n2(main_27_n2_prime), .n1(main_27_n1_prime), .d(in_2), .n2_prime(main_31_n2_prime),
    .n1_prime(main_31_n1_prime));
  \_32_1除法器_main  main_32 (
    .n2(main_29_n2_prime), .n1(main_29_n1_prime), .d(in_2), .n2_prime(main_32_n2_prime),
    .n1_prime(main_32_n1_prime));
endmodule
