// Logisim project 4位除法器.circ as structural Verilog: 1 circuit, main circuit main
module main (
  input  [3:0] a,
  input  [3:0] b,
  output [3:0] quo,
  output [3:0] rem
);

  wire comparator_1_lt, comparator_2_lt, comparator_3_lt, comparator_4_lt;
  wire [3:0] adder_1_out, adder_3_out, adder_5_out, adder_7_out, subtractor_1_out, subtractor_2_out,
       subtractor_3_out, subtractor_4_out;
  wire [7:0] adder_2_out, adder_4_out, adder_6_out, adder_8_out, bit_extender_1_out, bit_extender_2_out,
       bit_extender_3_out, bit_extender_4_out, bit_extender_5_out, bit_extender_6_out, bit_extender_7_out,
       bit_extender_8_out, bit_extender_9_out, multiplexer_1_out, multiplexer_2_out, multiplexer_3_out,
       shifter_1_out, shifter_2_out, shifter_3_out, shifter_4_out, shifter_5_out, shifter_6_out,
       shifter_7_out, shifter_8_out;

  assign bit_extender_1_out = {{4{1'b0}}, a};  // Bit_Extender bit_extender_1
  Shifter shifter_1 (.in(bit_extender_1_out), .\dist (3'b001), .out(shifter_1_out));
  Adder #(.width(4)) adder_1 (.a(4'b0001), .b(shifter_1_out[3:0]), .out(adder_1_out));  // open: cin, cout
  Comparator #(.width(4)) comparator_1 (.a(shifter_1_out[7:4]), .b(b), .lt(comparator_1_lt));  // open: gt, eq
  Subtractor #(.width(4)) subtractor_1 (.a(shifter_1_out[7:4]), .b(b), .out(subtractor_1_out));  // open: bin, bout
  assign bit_extender_2_out = {{4{1'b0}}, adder_1_out};  // Bit_Extender bit_extender_2
  assign bit_extender_3_out = {{4{1'b0}}, subtractor_1_out};  // Bit_Extender bit_extender_3
  Shifter shifter_2 (.in(bit_extender_3_out), .\dist (3'b100), .out(shifter_2_out));
  Multiplexer #(.width(8), .enable("false")) multiplexer_1 (
    .in0(adder_2_out), .in1(shifter_1_out), .out(multiplexer_1_out), .sel(comparator_1_lt));
  Shifter shifter_3 (.in(multiplexer_1_out), .\dist (3'b001), .out(shifter_3_out));
  Adder adder_2 (.a(bit_extender_2_out), .b(shifter_2_out), .out(adder_2_out));  // open: cin, cout
  assign bit_extender_4_out = {{4{1'b0}}, adder_3_out};  // Bit_Extender bit_extender_4
  Adder #(.width(4)) adder_3 (.a(4'b0001), .b(shifter_3_out[3:0]), .out(adder_3_out));  // open: cin, cout
  Comparator #(.width(4)) comparator_2 (.a(shifter_3_out[7:4]), .b(b), .lt(comparator_2_lt));  // open: gt, eq
  assign bit_extender_5_out = {{4{1'b0}}, subtractor_2_out};  // Bit_Extender bit_extender_5
  Subtractor #(.width(4)) subtractor_2 (.a(shifter_3_out[7:4]), .b(b), .out(subtractor_2_out));  // open: bin, bout
  Multiplexer #(.width(8), .enable("false")) multiplexer_2 (
    .in0(adder_4_out), .in1(shifter_3_out), .out(multiplexer_2_out), .sel(comparator_2_lt));
  Shifter shifter_4 (.in(bit_extender_5_out), .\dist (3'b100), .out(shifter_4_out));
  Shifter shifter_5 (.in(multiplexer_2_out), .\dist (3'b001), .out(shifter_5_out));
  Adder adder_4 (.a(bit_extender_4_out), .b(shifter_4_out), .out(adder_4_out));  // open: cin, cout
  Adder #(.width(4)) adder_5 (.a(4'b0001), .b(shifter_5_out[3:0]), .out(adder_5_out));  // open: cin, cout
  Comparator #(.width(4)) comparator_3 (.a(shifter_5_out[7:4]), .b(b), .lt(comparator_3_lt));  // open: gt, eq
  Subtractor #(.width(4)) subtractor_3 (.a(shifter_5_out[7:4]), .b(b), .out(subtractor_3_out));  // open: bin, bout
  assign bit_extender_6_out = {{4{1'b0}}, adder_5_out};  // Bit_Extender bit_extender_6
  assign bit_extender_7_out = {{4{1'b0}}, subtractor_3_out};  // Bit_Extender bit_extender_7
  Shifter shifter_6 (.in(bit_extender_7_out), .\dist (3'b100), .out(shifter_6_out));
  Multiplexer #(.width(8), .enable("false")) multiplexer_3 (
    .in0(adder_6_out), .in1(shifter_5_out), .out(multiplexer_3_out), .sel(comparator_3_lt));
  Shifter shifter_7 (.in(multiplexer_3_out), .\dist (3'b001), .out(shifter_7_out));
  Adder adder_6 (.a(bit_extender_6_out), .b(shifter_6_out), .out(adder_6_out));  // open: cin, cout
  Adder #(.width(4)) adder_7 (.a(4'b0001), .b(shifter_7_out[3:0]), .out(adder_7_out));  // open: cin, cout
  assign bit_extender_8_out = {{4{1'b0}}, adder_7_out};  // Bit_Extender bit_extender_8
  Comparator #(.width(4)) comparator_4 (.a(shifter_7_out[7:4]), .b(b), .lt(comparator_4_lt));  // open: gt, eq
  assign bit_extender_9_out = {{4{1'b0}}, subtractor_4_out};  // Bit_Extender bit_extender_9
  Subtractor #(.width(4)) subtractor_4 (.a(shifter_7_out[7:4]), .b(b), .out(subtractor_4_out));  // open: bin, bout
  Multiplexer #(.width(8), .enable("false")) multiplexer_4 (
    .in0(adder_8_out), .in1(shifter_7_out), .out({rem, quo}), .sel(comparator_4_lt));
  Shifter shifter_8 (.in(bit_extender_9_out), .\dist (3'b100), .out(shifter_8_out));
  Adder adder_8 (.a(bit_extender_8_out), .b(shifter_8_out), .out(adder_8_out));  // open: cin, cout
endmodule
