// Logisim project 除法器.circ as structural Verilog
module \_4位除法器  (
  input  [3:0] n2,
  input  [3:0] d,
  output [3:0] quot,
  output [3:0] rem
);

  wire comparator_1_lt, comparator_2_lt, comparator_3_lt, comparator_4_lt;
  wire [3:0] multiplexer_1_out, multiplexer_2_out, multiplexer_3_out, multiplexer_4_out, multiplexer_5_out,
       multiplexer_6_out, subtractor_1_out, subtractor_2_out, subtractor_3_out, subtractor_4_out;
  wire [3:1] shifter_3_out_2;
  wire [7:0] bit_extender_1_out, shifter_1_out, shifter_2_out, shifter_3_out, shifter_4_out;

  assign bit_extender_1_out = {{4{1'b0}}, n2};  // Bit_Extender bit_extender_1
  Shifter shifter_1 (.in(bit_extender_1_out), .\dist (3'b001), .out(shifter_1_out));
  Comparator #(.width(4), .mode("unsigned")) comparator_1 (
    .a(shifter_1_out[7:4]), .b(d), .lt(comparator_1_lt));  // open: gt, eq
  Subtractor #(.width(4)) subtractor_1 (.a(shifter_1_out[7:4]), .b(d), .out(subtractor_1_out));  // open: bin, bout
  Multiplexer #(.width(4), .enable("false")) multiplexer_1 (
    .in0({shifter_1_out[3:1], 1'b1}), .in1(shifter_1_out[3:0]), .out(multiplexer_1_out), .sel(comparator_1_lt));
  Multiplexer #(.width(4), .enable("false")) multiplexer_2 (
    .in0(subtractor_1_out), .in1(shifter_1_out[7:4]), .out(multiplexer_2_out), .sel(comparator_1_lt));
  Shifter shifter_2 (.in({multiplexer_2_out, multiplexer_1_out}), .\dist (3'b001), .out(shifter_2_out));
  Comparator #(.width(4), .mode("unsigned")) comparator_2 (
    .a(shifter_2_out[7:4]), .b(d), .lt(comparator_2_lt));  // open: gt, eq
  Subtractor #(.width(4)) subtractor_2 (.a(shifter_2_out[7:4]), .b(d), .out(subtractor_2_out));  // open: bin, bout
  Multiplexer #(.width(4), .enable("false")) multiplexer_3 (
    .in0({shifter_2_out[3:1], 1'b1}), .in1(shifter_2_out[3:0]), .out(multiplexer_3_out), .sel(comparator_2_lt));
  Multiplexer #(.width(4), .enable("false")) multiplexer_4 (
    .in0(subtractor_2_out), .in1(shifter_2_out[7:4]), .out(multiplexer_4_out), .sel(comparator_2_lt));
  Shifter shifter_3 (
    .in({multiplexer_4_out, multiplexer_3_out}), .\dist (3'b001),
    .out({shifter_3_out[7:4], shifter_3_out_2, shifter_3_out[0]}));
  Comparator #(.width(4), .mode("unsigned")) comparator_3 (
    .a(shifter_3_out[7:4]), .b(d), .lt(comparator_3_lt));  // open: gt, eq
  Subtractor #(.width(4)) subtractor_3 (.a(shifter_3_out[7:4]), .b(d), .out(subtractor_3_out));  // open: bin, bout
  Multiplexer #(.width(4), .enable("false")) multiplexer_5 (
    .in0({shifter_3_out_2, 1'b1}), .in1({shifter_3_out_2, shifter_3_out[0]}), .out(multiplexer_5_out),
    .sel(comparator_3_lt));
  Multiplexer #(.width(4), .enable("false")) multiplexer_6 (
    .in0(subtractor_3_out), .in1(shifter_3_out[7:4]), .out(multiplexer_6_out), .sel(comparator_3_lt));
  Shifter shifter_4 (.in({multiplexer_6_out, multiplexer_5_out}), .\dist (3'b001), .out(shifter_4_out));
  Multiplexer #(.width(4), .enable("false")) multiplexer_7 (
    .in0({shifter_4_out[3:1], 1'b1}), .in1(shifter_4_out[3:0]), .out(quot), .sel(comparator_4_lt));
  Comparator #(.width(4), .mode("unsigned")) comparator_4 (
    .a(shifter_4_out[7:4]), .b(d), .lt(comparator_4_lt));  // open: gt, eq
  Subtractor #(.width(4)) subtractor_4 (.a(shifter_4_out[7:4]), .b(d), .out(subtractor_4_out));  // open: bin, bout
  Multiplexer #(.width(4), .enable("false")) multiplexer_8 (
    .in0(subtractor_4_out), .in1(shifter_4_out[7:4]), .out(rem), .sel(comparator_4_lt));
endmodule

module \_32位除法器  (
  input  [31:0] n,
  input  [31:0] d,
  output [31:0] rem,
  output [31:0] quot
);

  wire [31:0] div1_1_out_4, div1_1_out_5, div1_3_out_4, div1_3_out_5, div1_4_out_4, div1_4_out_5,
       div1_5_out_4, div1_5_out_5, div1_6_out_4, div1_6_out_5, div1_7_out_4, div1_7_out_5, div1_8_out_4,
       div1_8_out_5, div1_9_out_4, div1_9_out_5, div1_10_out_4, div1_10_out_5, div1_11_out_4, div1_11_out_5,
       div1_12_out_4, div1_12_out_5, div1_13_out_4, div1_13_out_5, div1_14_out_4, div1_14_out_5,
       div1_15_out_4, div1_15_out_5, div1_16_out_4, div1_16_out_5, div1_17_out_4, div1_17_out_5,
       div1_18_out_4, div1_18_out_5, div1_19_out_4, div1_19_out_5, div1_20_out_4, div1_20_out_5,
       div1_21_out_4, div1_21_out_5, div1_22_out_4, div1_22_out_5, div1_23_out_4, div1_23_out_5,
       div1_24_out_4, div1_24_out_5, div1_25_out_4, div1_25_out_5, div1_26_out_4, div1_26_out_5,
       div1_27_out_4, div1_27_out_5, div1_28_out_4, div1_28_out_5, div1_29_out_4, div1_29_out_5,
       div1_30_out_4, div1_30_out_5, div1_31_out_4, div1_31_out_5, div1_32_out_4, div1_32_out_5;

  div1 div1_1 (.n2(div1_4_out_4), .n1(div1_4_out_5), .d(d), .out_4(div1_1_out_4), .out_5(div1_1_out_5));
  div1 div1_2 (.n2(div1_6_out_4), .n1(div1_6_out_5), .d(d), .out_4(quot), .out_5(rem));
  div1 div1_3 (.n2(n), .n1({32{1'b0}}), .d(d), .out_4(div1_3_out_4), .out_5(div1_3_out_5));
  div1 div1_4 (.n2(div1_9_out_4), .n1(div1_9_out_5), .d(d), .out_4(div1_4_out_4), .out_5(div1_4_out_5));
  div1 div1_5 (.n2(div1_1_out_4), .n1(div1_1_out_5), .d(d), .out_4(div1_5_out_4), .out_5(div1_5_out_5));
  div1 div1_6 (.n2(div1_10_out_4), .n1(div1_10_out_5), .d(d), .out_4(div1_6_out_4), .out_5(div1_6_out_5));
  div1 div1_7 (.n2(div1_3_out_4), .n1(div1_3_out_5), .d(d), .out_4(div1_7_out_4), .out_5(div1_7_out_5));
  div1 div1_8 (.n2(div1_5_out_4), .n1(div1_5_out_5), .d(d), .out_4(div1_8_out_4), .out_5(div1_8_out_5));
  div1 div1_9 (.n2(div1_12_out_4), .n1(div1_12_out_5), .d(d), .out_4(div1_9_out_4), .out_5(div1_9_out_5));
  div1 div1_10 (.n2(div1_14_out_4), .n1(div1_14_out_5), .d(d), .out_4(div1_10_out_4), .out_5(div1_10_out_5));
  div1 div1_11 (.n2(div1_7_out_4), .n1(div1_7_out_5), .d(d), .out_4(div1_11_out_4), .out_5(div1_11_out_5));
  div1 div1_12 (.n2(div1_16_out_4), .n1(div1_16_out_5), .d(d), .out_4(div1_12_out_4), .out_5(div1_12_out_5));
  div1 div1_13 (.n2(div1_8_out_4), .n1(div1_8_out_5), .d(d), .out_4(div1_13_out_4), .out_5(div1_13_out_5));
  div1 div1_14 (.n2(div1_18_out_4), .n1(div1_18_out_5), .d(d), .out_4(div1_14_out_4), .out_5(div1_14_out_5));
  div1 div1_15 (.n2(div1_11_out_4), .n1(div1_11_out_5), .d(d), .out_4(div1_15_out_4), .out_5(div1_15_out_5));
  div1 div1_16 (.n2(div1_20_out_4), .n1(div1_20_out_5), .d(d), .out_4(div1_16_out_4), .out_5(div1_16_out_5));
  div1 div1_17 (.n2(div1_13_out_4), .n1(div1_13_out_5), .d(d), .out_4(div1_17_out_4), .out_5(div1_17_out_5));
  div1 div1_18 (.n2(div1_22_out_4), .n1(div1_22_out_5), .d(d), .out_4(div1_18_out_4), .out_5(div1_18_out_5));
  div1 div1_19 (.n2(div1_15_out_4), .n1(div1_15_out_5), .d(d), .out_4(div1_19_out_4), .out_5(div1_19_out_5));
  div1 div1_20 (.n2(div1_25_out_4), .n1(div1_25_out_5), .d(d), .out_4(div1_20_out_4), .out_5(div1_20_out_5));
  div1 div1_21 (.n2(div1_17_out_4), .n1(div1_17_out_5), .d(d), .out_4(div1_21_out_4), .out_5(div1_21_out_5));
  div1 div1_22 (.n2(div1_26_out_4), .n1(div1_26_out_5), .d(d), .out_4(div1_22_out_4), .out_5(div1_22_out_5));
  div1 div1_23 (.n2(div1_19_out_4), .n1(div1_19_out_5), .d(d), .out_4(div1_23_out_4), .out_5(div1_23_out_5));
  div1 div1_24 (.n2(div1_21_out_4), .n1(div1_21_out_5), .d(d), .out_4(div1_24_out_4), .out_5(div1_24_out_5));
  div1 div1_25 (.n2(div1_28_out_4), .n1(div1_28_out_5), .d(d), .out_4(div1_25_out_4), .out_5(div1_25_out_5));
  div1 div1_26 (.n2(div1_30_out_4), .n1(div1_30_out_5), .d(d), .out_4(div1_26_out_4), .out_5(div1_26_out_5));
  div1 div1_27 (.n2(div1_23_out_4), .n1(div1_23_out_5), .d(d), .out_4(div1_27_out_4), .out_5(div1_27_out_5));
  div1 div1_28 (.n2(div1_31_out_4), .n1(div1_31_out_5), .d(d), .out_4(div1_28_out_4), .out_5(div1_28_out_5));
  div1 div1_29 (.n2(div1_24_out_4), .n1(div1_24_out_5), .d(d), .out_4(div1_29_out_4), .out_5(div1_29_out_5));
  div1 div1_30 (.n2(div1_32_out_4), .n1(div1_32_out_5), .d(d), .out_4(div1_30_out_4), .out_5(div1_30_out_5));
  div1 div1_31 (.n2(div1_27_out_4), .n1(div1_27_out_5), .d(d), .out_4(div1_31_out_4), .out_5(div1_31_out_5));
  div1 div1_32 (.n2(div1_29_out_4), .n1(div1_29_out_5), .d(d), .out_4(div1_32_out_4), .out_5(div1_32_out_5));
endmodule

module \_64位移位器  (
  input  [31:0] in_1,
  input  [31:0] in_2,
  output [31:0] out_3,
  output [31:0] out_4
);

  wire [0:0] shifter_1_out;

  Shifter #(.width(32)) shifter_1 (.in(in_1), .\dist (5'b00001), .out({out_3[31:1], shifter_1_out[0]}));
  Shifter #(.width(32)) shifter_2 (.in(in_2), .\dist (5'b00001), .out(out_4));

  assign out_3[0] = in_2[31];
endmodule

module div1 (
  input  [31:0] n2,
  input  [31:0] n1,
  input  [31:0] d,
  output [31:0] out_4,
  output [31:0] out_5
);

  wire comparator_1_lt;
  wire [31:0] \n64位移位器_1_out_3 , \n64位移位器_1_out_4 , subtractor_1_out;

  \_64位移位器  \u_64位移位器_1  (.in_1(n1), .in_2(n2), .out_3(\n64位移位器_1_out_3 ), .out_4(\n64位移位器_1_out_4 ));
  Comparator #(.width(32), .mode("unsigned")) comparator_1 (
    .a(\n64位移位器_1_out_3 ), .b(d), .lt(comparator_1_lt));  // open: gt, eq
  Subtractor #(.width(32)) subtractor_1 (.a(\n64位移位器_1_out_3 ), .b(d), .out(subtractor_1_out));  // open: bin, bout
  Multiplexer #(.width(32), .enable("false")) multiplexer_1 (
    .in0({\n64位移位器_1_out_4 [31:1], 1'b1}), .in1(\n64位移位器_1_out_4 ), .out(out_4), .sel(comparator_1_lt));
  Multiplexer #(.width(32), .enable("false")) multiplexer_2 (
    .in0(subtractor_1_out), .in1(\n64位移位器_1_out_3 ), .out(out_5), .sel(comparator_1_lt));
endmodule
