// Logisim project F.circ as structural Verilog: 8 circuits, main circuit main
module main (
  input  [5:0] n
);

  wire clear_out, clock_out, contraller_1_clk_2, contraller_1_clr_2, contraller_1_n_i, contraller_1_start;
  wire [3:0] display_1_d0, display_1_d1, display_1_d2, display_1_d3, display_1_d4, display_1_d5,
       display_1_d6, display_1_d7, display_1_d8, display_1_d9;
  wire [31:0] fibo_1_b;

  Button clear (.out(clear_out));
  Button clock (.out(clock_out));
  contraller contraller_1 (
    .n(n), .clr(clear_out), .clk(clock_out), .n_i(contraller_1_n_i), .clr_2(contraller_1_clr_2),
    .start(contraller_1_start), .clk_2(contraller_1_clk_2));
  // Probe on fibo_1_b
  Display display_1 (
    .\输入 (fibo_1_b), .D0(display_1_d0), .D1(display_1_d1), .D2(display_1_d2), .D3(display_1_d3),
    .D4(display_1_d4), .D5(display_1_d5), .D6(display_1_d6), .D7(display_1_d7), .D8(display_1_d8),
    .D9(display_1_d9));
  Fibo fibo_1 (
    .start(contraller_1_start), .clk(contraller_1_clk_2), .clr(contraller_1_clr_2), .n_i_1(contraller_1_n_i),
    .b(fibo_1_b));
  Hex_Digit_Display hex_digit_display_1 (.value(display_1_d9));  // open: dp
  Hex_Digit_Display hex_digit_display_2 (.value(display_1_d7));  // open: dp
  Hex_Digit_Display hex_digit_display_3 (.value(display_1_d8));  // open: dp
  Hex_Digit_Display hex_digit_display_4 (.value(display_1_d6));  // open: dp
  Hex_Digit_Display hex_digit_display_5 (.value(display_1_d5));  // open: dp
  Hex_Digit_Display hex_digit_display_6 (.value(display_1_d3));  // open: dp
  Hex_Digit_Display hex_digit_display_7 (.value(display_1_d4));  // open: dp
  Hex_Digit_Display hex_digit_display_8 (.value(display_1_d2));  // open: dp
  Hex_Digit_Display hex_digit_display_9 (.value(display_1_d1));  // open: dp
  Hex_Digit_Display hex_digit_display_10 (.value(display_1_d0));  // open: dp
endmodule

module sqrX (
  input  [31:0] a,
  input  [31:0] b,
  input  [31:0] c,
  input  [31:0] d,
  output [31:0] a_a_bc,
  output [31:0] ab_bd,
  output [31:0] ac_cd,
  output [31:0] bc_d_d
);

  wire [31:0] multiplier_1_out, multiplier_2_out, multiplier_3_out, multiplier_4_out, multiplier_5_out,
       multiplier_6_out, multiplier_7_out, multiplier_8_out;

  Multiplier #(.width(32)) multiplier_1 (.a(a), .b(a), .out(multiplier_1_out), .cin({32{1'b0}}));  // open: cout
  Multiplier #(.width(32)) multiplier_2 (.a(b), .b(c), .out(multiplier_2_out), .cin({32{1'b0}}));  // open: cout
  Multiplier #(.width(32)) multiplier_3 (.a(a), .b(b), .out(multiplier_3_out), .cin({32{1'b0}}));  // open: cout
  Multiplier #(.width(32)) multiplier_4 (.a(b), .b(d), .out(multiplier_4_out), .cin({32{1'b0}}));  // open: cout
  Multiplier #(.width(32)) multiplier_5 (.a(a), .b(c), .out(multiplier_5_out), .cin({32{1'b0}}));  // open: cout
  Multiplier #(.width(32)) multiplier_6 (.a(c), .b(d), .out(multiplier_6_out), .cin({32{1'b0}}));  // open: cout
  Multiplier #(.width(32)) multiplier_7 (.a(b), .b(c), .out(multiplier_7_out), .cin({32{1'b0}}));  // open: cout
  Multiplier #(.width(32)) multiplier_8 (.a(d), .b(d), .out(multiplier_8_out), .cin({32{1'b0}}));  // open: cout
  Adder #(.width(32)) adder_1 (.a(multiplier_1_out), .b(multiplier_2_out), .out(a_a_bc), .cin(1'b0));  // open: cout
  Adder #(.width(32)) adder_2 (.a(multiplier_3_out), .b(multiplier_4_out), .out(ab_bd), .cin(1'b0));  // open: cout
  Adder #(.width(32)) adder_3 (.a(multiplier_5_out), .b(multiplier_6_out), .out(ac_cd), .cin(1'b0));  // open: cout
  Adder #(.width(32)) adder_4 (.a(multiplier_7_out), .b(multiplier_8_out), .out(bc_d_d), .cin(1'b0));  // open: cout
endmodule

module sqrX_A (
  input  [31:0] a,
  input  [31:0] b,
  input  [31:0] c,
  input  [31:0] d,
  output [31:0] ab_bd,
  output [31:0] a_a_bc_ab_bd,
  output [31:0] bc_d_d,
  output [31:0] ac_cd_bc_d_d
);

  wire [31:0] adder_2_out, adder_4_out, multiplier_1_out, multiplier_2_out, multiplier_3_out,
       multiplier_4_out, multiplier_5_out, multiplier_6_out, multiplier_7_out;

  Multiplier #(.width(32)) multiplier_1 (.a(a), .b(b), .out(multiplier_1_out));  // open: cin, cout
  Multiplier #(.width(32)) multiplier_2 (.a(b), .b(d), .out(multiplier_2_out));  // open: cin, cout
  Multiplier #(.width(32)) multiplier_3 (.a(a), .b(a), .out(multiplier_3_out));  // open: cin, cout
  Multiplier #(.width(32)) multiplier_4 (.a(b), .b(c), .out(multiplier_4_out));  // open: cin, cout
  Multiplier #(.width(32)) multiplier_5 (.a(d), .b(d), .out(multiplier_5_out));  // open: cin, cout
  Multiplier #(.width(32)) multiplier_6 (.a(a), .b(c), .out(multiplier_6_out));  // open: cin, cout
  Multiplier #(.width(32)) multiplier_7 (.a(c), .b(d), .out(multiplier_7_out));  // open: cin, cout
  Adder #(.width(32)) adder_1 (.a(multiplier_1_out), .b(multiplier_2_out), .out(ab_bd));  // open: cin, cout
  Adder #(.width(32)) adder_2 (.a(multiplier_3_out), .b(multiplier_4_out), .out(adder_2_out));  // open: cin, cout
  Adder #(.width(32)) adder_3 (.a(multiplier_4_out), .b(multiplier_5_out), .out(bc_d_d));  // open: cin, cout
  Adder #(.width(32)) adder_4 (.a(multiplier_6_out), .b(multiplier_7_out), .out(adder_4_out));  // open: cin, cout
  Adder #(.width(32)) adder_5 (.a(ab_bd), .b(adder_2_out), .out(a_a_bc_ab_bd));  // open: cin, cout
  Adder #(.width(32)) adder_6 (.a(bc_d_d), .b(adder_4_out), .out(ac_cd_bc_d_d));  // open: cin, cout
endmodule

module Fibo (
  input  start,
  input  clk,
  input  clr,
  input  n_i_1,
  output [31:0] b
);

  wire [31:0] multiplexer_1_out, multiplexer_2_out, multiplexer_3_out, multiplexer_4_out, multiplexer_5_out,
       multiplexer_6_out, multiplexer_7_out, multiplexer_8_out, register_1_q, register_3_q, register_4_q,
       sqrx_1_a_a_bc, sqrx_1_ab_bd, sqrx_1_ac_cd, sqrx_1_bc_d_d, sqrx_a_1_a_a_bc_ab_bd, sqrx_a_1_ab_bd,
       sqrx_a_1_ac_cd_bc_d_d, sqrx_a_1_bc_d_d;

  Multiplexer #(.width(32), .enable("false")) multiplexer_1 (
    .in0({32{1'b0}}), .in1(multiplexer_5_out), .out(multiplexer_1_out), .sel(start));
  Multiplexer #(.width(32), .enable("false")) multiplexer_2 (
    .in0({32{1'b1}}), .in1(multiplexer_6_out), .out(multiplexer_2_out), .sel(start));
  Multiplexer #(.width(32), .enable("false")) multiplexer_3 (
    .in0({32{1'b1}}), .in1(multiplexer_7_out), .out(multiplexer_3_out), .sel(start));
  Multiplexer #(.width(32), .enable("false")) multiplexer_4 (
    .in0({32{1'b1}}), .in1(multiplexer_8_out), .out(multiplexer_4_out), .sel(start));
  Register #(.width(32)) register_1 (.D(multiplexer_1_out), .Q(register_1_q), .clk(clk), .clr(clr));  // open: en
  Register #(.width(32)) register_2 (.D(multiplexer_2_out), .Q(b), .clk(clk), .clr(clr));  // open: en
  Register #(.width(32)) register_3 (.D(multiplexer_3_out), .Q(register_3_q), .clk(clk), .clr(clr));  // open: en
  Register #(.width(32)) register_4 (.D(multiplexer_4_out), .Q(register_4_q), .clk(clk), .clr(clr));  // open: en
  sqrX sqrx_1 (
    .a(register_1_q), .b(b), .c(register_3_q), .d(register_4_q), .a_a_bc(sqrx_1_a_a_bc),
    .ab_bd(sqrx_1_ab_bd), .ac_cd(sqrx_1_ac_cd), .bc_d_d(sqrx_1_bc_d_d));
  sqrX_A sqrx_a_1 (
    .a(register_1_q), .b(b), .c(register_3_q), .d(register_4_q), .ab_bd(sqrx_a_1_ab_bd),
    .a_a_bc_ab_bd(sqrx_a_1_a_a_bc_ab_bd), .bc_d_d(sqrx_a_1_bc_d_d), .ac_cd_bc_d_d(sqrx_a_1_ac_cd_bc_d_d));
  Multiplexer #(.width(32), .enable("false")) multiplexer_5 (
    .in0(sqrx_1_a_a_bc), .in1(sqrx_a_1_ab_bd), .out(multiplexer_5_out), .sel(n_i_1));
  Multiplexer #(.width(32), .enable("false")) multiplexer_6 (
    .in0(sqrx_1_ab_bd), .in1(sqrx_a_1_a_a_bc_ab_bd), .out(multiplexer_6_out), .sel(n_i_1));
  Multiplexer #(.width(32), .enable("false")) multiplexer_7 (
    .in0(sqrx_1_ac_cd), .in1(sqrx_a_1_bc_d_d), .out(multiplexer_7_out), .sel(n_i_1));
  Multiplexer #(.width(32), .enable("false")) multiplexer_8 (
    .in0(sqrx_1_bc_d_d), .in1(sqrx_a_1_ac_cd_bc_d_d), .out(multiplexer_8_out), .sel(n_i_1));

  // Notes on the sheet:
  //   a
  //   b
  //   c
  //   d
  //   a
  //   b
  //   c
  //   d
endmodule

module contraller (
  input  [5:0] n,
  input  clr,
  input  clk,
  output n_i,
  output clr_2,
  output start,
  output clk_2
);

  wire and_2_out, and_3_out, and_4_out, and_5_out, and_6_out, and_7_out, and_8_out, comparator_1_eq,
       d_ff_1_q, d_ff_2_q, d_ff_3_q, d_ff_5_q, d_ff_5_qn, d_ff_6_q, d_ff_7_q, not_1_out, not_2_out,
       not_3_out, not_4_out, not_5_out, not_6_out, not_7_out, or_1_out, or_2_out;
  wire [2:0] \模十_1_a0 ;
  wire [5:0] multiplexer_1_out;

  Multiplexer #(.width(6), .enable("false")) multiplexer_1 (
    .in0({6{1'b0}}), .in1(n), .out(multiplexer_1_out), .sel(clr_2));
  and and_1 (clr_2, clr, not_1_out);
  not not_1 (not_1_out, clk);
  and and_2 (and_2_out, d_ff_5_qn, clk);
  D_Flip_Flop d_ff_1 (
    .clk(clk), .D(1'b0), .Q(d_ff_1_q), .preset(multiplexer_1_out[0]), .reset(and_3_out));  // open: Qn, en
  and and_3 (and_3_out, not_2_out, clr_2);
  not not_2 (not_2_out, multiplexer_1_out[0]);
  D_Flip_Flop d_ff_2 (
    .clk(clk), .D(d_ff_1_q), .Q(d_ff_2_q), .preset(multiplexer_1_out[1]), .reset(and_4_out));  // open: Qn, en
  and and_4 (and_4_out, not_3_out, clr_2);
  not not_3 (not_3_out, multiplexer_1_out[1]);
  \模十  \u_模十_1  (.Cpd(and_2_out), .Clr(clr_2), .A0(\模十_1_a0 [0]), .A1(\模十_1_a0 [1]), .A2(\模十_1_a0 [2]));
  D_Flip_Flop d_ff_3 (
    .clk(clk), .D(d_ff_2_q), .Q(d_ff_3_q), .preset(multiplexer_1_out[2]), .reset(and_5_out));  // open: Qn, en
  and and_5 (and_5_out, not_4_out, clr_2);
  not not_4 (not_4_out, multiplexer_1_out[2]);
  D_Flip_Flop d_ff_4 (.clk(clk), .D(or_1_out), .Q(start), .reset(clr_2));  // open: Qn, preset, en
  or or_1 (or_1_out, n_i, start);
  D_Flip_Flop #(.trigger("falling")) d_ff_5 (
    .clk(clk), .D(or_2_out), .Q(d_ff_5_q), .Qn(d_ff_5_qn), .reset(clr_2));  // open: preset, en
  or or_2 (or_2_out, d_ff_5_q, comparator_1_eq);
  D_Flip_Flop d_ff_6 (
    .clk(clk), .D(d_ff_3_q), .Q(d_ff_6_q), .preset(multiplexer_1_out[3]), .reset(and_6_out));  // open: Qn, en
  and and_6 (and_6_out, not_5_out, clr_2);
  not not_5 (not_5_out, multiplexer_1_out[3]);
  Comparator #(.width(3), .mode("unsigned")) comparator_1 (
    .a(\模十_1_a0 ), .b(3'b101), .eq(comparator_1_eq));  // open: gt, lt
  D_Flip_Flop d_ff_7 (
    .clk(clk), .D(d_ff_6_q), .Q(d_ff_7_q), .preset(multiplexer_1_out[4]), .reset(and_7_out));  // open: Qn, en
  and and_7 (and_7_out, not_6_out, clr_2);
  not not_6 (not_6_out, multiplexer_1_out[4]);
  not not_7 (not_7_out, multiplexer_1_out[5]);
  D_Flip_Flop d_ff_8 (
    .clk(clk), .D(d_ff_7_q), .Q(n_i), .preset(multiplexer_1_out[5]), .reset(and_8_out));  // open: Qn, en
  and and_8 (and_8_out, not_7_out, clr_2);
  and and_9 (clk_2, clk, d_ff_5_qn);
endmodule

module \模十  (
  input  Cpd,
  input  Clr,
  output A0,
  output A1,
  output A2
);

  wire d_ff_1_q, d_ff_2_q;

  D_Flip_Flop d_ff_1 (.clk(Cpd), .D(A0), .Q(d_ff_1_q), .Qn(A0), .reset(Clr));  // open: preset, en
  D_Flip_Flop d_ff_2 (.clk(d_ff_1_q), .D(A1), .Q(d_ff_2_q), .Qn(A1), .reset(Clr));  // open: preset, en
  D_Flip_Flop d_ff_3 (.clk(d_ff_2_q), .D(A2), .Qn(A2), .reset(Clr));  // open: Q, preset, en
endmodule

module Display (
  input  [31:0] \输入 ,
  output [3:0] D0,
  output [3:0] D1,
  output [3:0] D2,
  output [3:0] D3,
  output [3:0] D4,
  output [3:0] D5,
  output [3:0] D6,
  output [3:0] D7,
  output [3:0] D8,
  output [3:0] D9
);

  wire [31:0] divider_1_out, divider_1_rem, divider_2_out, divider_2_rem, divider_3_out, divider_3_rem,
       divider_4_out, divider_4_rem, divider_5_out, divider_5_rem, divider_6_out, divider_6_rem,
       divider_7_out, divider_7_rem, divider_8_out, divider_8_rem, divider_9_out, divider_9_rem;

  Divider #(.width(32)) divider_1 (.a(\输入 ), .b(32'ha), .out(divider_1_out), .upper({32{1'b0}}), .rem(divider_1_rem));
  Divider #(.width(32)) divider_2 (
    .a(divider_1_out), .b(32'ha), .out(divider_2_out), .upper({32{1'b0}}), .rem(divider_2_rem));
  \取前四位  \u_取前四位_1  (.\输入 (divider_1_rem), .\输出 (D0));
  \取前四位  \u_取前四位_2  (.\输入 (divider_2_rem), .\输出 (D1));
  Divider #(.width(32)) divider_3 (
    .a(divider_2_out), .b(32'ha), .out(divider_3_out), .upper({32{1'b0}}), .rem(divider_3_rem));
  \取前四位  \u_取前四位_3  (.\输入 (divider_3_rem), .\输出 (D2));
  Divider #(.width(32)) divider_4 (
    .a(divider_3_out), .b(32'ha), .out(divider_4_out), .upper({32{1'b0}}), .rem(divider_4_rem));
  Divider #(.width(32)) divider_5 (
    .a(divider_4_out), .b(32'ha), .out(divider_5_out), .upper({32{1'b0}}), .rem(divider_5_rem));
  \取前四位  \u_取前四位_4  (.\输入 (divider_4_rem), .\输出 (D3));
  \取前四位  \u_取前四位_5  (.\输入 (divider_5_rem), .\输出 (D4));
  Divider #(.width(32)) divider_6 (
    .a(divider_5_out), .b(32'ha), .out(divider_6_out), .upper({32{1'b0}}), .rem(divider_6_rem));
  \取前四位  \u_取前四位_6  (.\输入 (divider_6_rem), .\输出 (D5));
  Divider #(.width(32)) divider_7 (
    .a(divider_6_out), .b(32'ha), .out(divider_7_out), .upper({32{1'b0}}), .rem(divider_7_rem));
  Divider #(.width(32)) divider_8 (
    .a(divider_7_out), .b(32'ha), .out(divider_8_out), .upper({32{1'b0}}), .rem(divider_8_rem));
  \取前四位  \u_取前四位_7  (.\输入 (divider_7_rem), .\输出 (D6));
  Divider #(.width(32)) divider_9 (
    .a(divider_8_out), .b(32'ha), .out(divider_9_out), .upper({32{1'b0}}), .rem(divider_9_rem));
  \取前四位  \u_取前四位_8  (.\输入 (divider_8_rem), .\输出 (D7));
  \取前四位  \u_取前四位_9  (.\输入 (divider_9_rem), .\输出 (D8));
  \取前四位  \u_取前四位_10  (.\输入 (divider_9_out), .\输出 (D9));
endmodule

module \取前四位  (
  input  [31:0] \输入 ,
  output [3:0] \输出 
);


  assign \输出  = \输入 [3:0];
endmodule
