// Logisim project 斐波拉契数列.circ as structural Verilog: 7 circuits, main circuit main
module main (
  input  [5:0] n
);

  wire clear_out, clock_out, controller_1_clear_2, controller_1_clk, controller_1_n_i_1, controller_1_start;
  wire [3:0] display_1_d0, display_1_d1, display_1_d2, display_1_d3, display_1_d4, display_1_d5,
       display_1_d6, display_1_d7, display_1_d8, display_1_d9;
  wire [31:0] fibo_1_b_prime;

  Controller controller_1 (
    .n(n), .clear(clear_out), .n_i_1(controller_1_n_i_1), .start(controller_1_start), .clk(controller_1_clk),
    .clear_2(controller_1_clear_2), .clock(clock_out));
  Button clear (.out(clear_out));
  Button clock (.out(clock_out));
  Fibo fibo_1 (
    .start(controller_1_start), .clr(controller_1_clear_2), .clk(controller_1_clk),
    .ni_1(controller_1_n_i_1), .b_prime(fibo_1_b_prime));
  Display display_1 (
    .Fi(fibo_1_b_prime), .D0(display_1_d0), .D1(display_1_d1), .D2(display_1_d2), .D3(display_1_d3),
    .D4(display_1_d4), .D5(display_1_d5), .D6(display_1_d6), .D7(display_1_d7), .D8(display_1_d8),
    .D9(display_1_d9));
  Hex_Digit_Display hex_digit_display_1 (.value(display_1_d9));  // open: dp
  Hex_Digit_Display hex_digit_display_2 (.value(display_1_d8));  // open: dp
  Hex_Digit_Display hex_digit_display_3 (.value(display_1_d7));  // open: dp
  Hex_Digit_Display hex_digit_display_4 (.value(display_1_d6));  // open: dp
  Hex_Digit_Display hex_digit_display_5 (.value(display_1_d5));  // open: dp
  Hex_Digit_Display hex_digit_display_6 (.value(display_1_d3));  // open: dp
  Hex_Digit_Display hex_digit_display_7 (.value(display_1_d4));  // open: dp
  Hex_Digit_Display hex_digit_display_8 (.value(display_1_d2));  // open: dp
  Hex_Digit_Display hex_digit_display_9 (.value(display_1_d1));  // open: dp
  Hex_Digit_Display hex_digit_display_10 (.value(display_1_d0));  // open: dp
endmodule

module SqrX (
  input  [31:0] a,
  input  [31:0] b,
  input  [31:0] c,
  input  [31:0] d,
  output [31:0] a_prime,
  output [31:0] b_prime,
  output [31:0] c_prime,
  output [31:0] d_prime
);

  wire [31:0] multiplier_1_out, multiplier_2_out, multiplier_3_out, multiplier_4_out, multiplier_5_out,
       multiplier_6_out, multiplier_7_out, multiplier_8_out;

  Multiplier #(.width(32)) multiplier_1 (.a(a), .b(a), .out(multiplier_1_out));  // open: cin, cout
  Multiplier #(.width(32)) multiplier_2 (.a(b), .b(c), .out(multiplier_2_out));  // open: cin, cout
  Multiplier #(.width(32)) multiplier_3 (.a(a), .b(b), .out(multiplier_3_out));  // open: cin, cout
  Multiplier #(.width(32)) multiplier_4 (.a(b), .b(d), .out(multiplier_4_out));  // open: cin, cout
  Multiplier #(.width(32)) multiplier_5 (.a(a), .b(c), .out(multiplier_5_out));  // open: cin, cout
  Multiplier #(.width(32)) multiplier_6 (.a(c), .b(d), .out(multiplier_6_out));  // open: cin, cout
  Multiplier #(.width(32)) multiplier_7 (.a(b), .b(c), .out(multiplier_7_out));  // open: cin, cout
  Multiplier #(.width(32)) multiplier_8 (.a(d), .b(d), .out(multiplier_8_out));  // open: cin, cout
  Adder #(.width(32)) adder_1 (.a(multiplier_1_out), .b(multiplier_2_out), .out(a_prime));  // open: cin, cout
  Adder #(.width(32)) adder_2 (.a(multiplier_3_out), .b(multiplier_4_out), .out(b_prime));  // open: cin, cout
  Adder #(.width(32)) adder_3 (.a(multiplier_5_out), .b(multiplier_6_out), .out(c_prime));  // open: cin, cout
  Adder #(.width(32)) adder_4 (.a(multiplier_7_out), .b(multiplier_8_out), .out(d_prime));  // open: cin, cout
endmodule

module sqrX_A (
  input  [31:0] a,
  input  [31:0] b,
  input  [31:0] c,
  input  [31:0] d,
  output [31:0] a_prime_prime,
  output [31:0] b_prime_prime,
  output [31:0] c_prime_prime,
  output [31:0] d_prime_prime
);

  wire [31:0] adder_2_out, adder_4_out, multiplier_1_out, multiplier_2_out, multiplier_3_out,
       multiplier_4_out, multiplier_5_out, multiplier_6_out, multiplier_7_out;

  Multiplier #(.width(32)) multiplier_1 (.a(a), .b(b), .out(multiplier_1_out));  // open: cin, cout
  Multiplier #(.width(32)) multiplier_2 (.a(b), .b(d), .out(multiplier_2_out));  // open: cin, cout
  Multiplier #(.width(32)) multiplier_3 (.a(a), .b(a), .out(multiplier_3_out));  // open: cin, cout
  Multiplier #(.width(32)) multiplier_4 (.a(b), .b(c), .out(multiplier_4_out));  // open: cin, cout
  Multiplier #(.width(32)) multiplier_5 (.a(d), .b(d), .out(multiplier_5_out));  // open: cin, cout
  Multiplier #(.width(32)) multiplier_6 (.a(a), .b(c), .out(multiplier_6_out));  // open: cin, cout
  Multiplier #(.width(32)) multiplier_7 (.a(c), .b(d), .out(multiplier_7_out));  // open: cin, cout
  Adder #(.width(32)) adder_1 (.a(multiplier_1_out), .b(multiplier_2_out), .out(a_prime_prime));  // open: cin, cout
  Adder #(.width(32)) adder_2 (.a(multiplier_3_out), .b(multiplier_4_out), .out(adder_2_out));  // open: cin, cout
  Adder #(.width(32)) adder_3 (.a(multiplier_4_out), .b(multiplier_5_out), .out(c_prime_prime));  // open: cin, cout
  Adder #(.width(32)) adder_4 (.a(multiplier_6_out), .b(multiplier_7_out), .out(adder_4_out));  // open: cin, cout
  Adder #(.width(32)) adder_5 (.a(a_prime_prime), .b(adder_2_out), .out(b_prime_prime));  // open: cin, cout
  Adder #(.width(32)) adder_6 (.a(c_prime_prime), .b(adder_4_out), .out(d_prime_prime));  // open: cin, cout
endmodule

module Fibo (
  input  start,
  input  clr,
  input  clk,
  input  ni_1,
  output [31:0] b_prime
);

  wire [31:0] multiplexer_1_out, multiplexer_2_out, multiplexer_3_out, multiplexer_4_out, multiplexer_5_out,
       multiplexer_6_out, multiplexer_7_out, multiplexer_8_out, register_1_q, register_3_q, register_4_q,
       sqrx_1_a_prime, sqrx_1_b_prime, sqrx_1_c_prime, sqrx_1_d_prime, sqrx_a_1_a_prime_prime,
       sqrx_a_1_b_prime_prime, sqrx_a_1_c_prime_prime, sqrx_a_1_d_prime_prime;

  Multiplexer #(.width(32), .enable("false")) multiplexer_1 (
    .in0({32{1'b0}}), .in1(multiplexer_5_out), .out(multiplexer_1_out), .sel(start));
  Multiplexer #(.width(32), .enable("false")) multiplexer_2 (
    .in0({32{1'b1}}), .in1(multiplexer_6_out), .out(multiplexer_2_out), .sel(start));
  Multiplexer #(.width(32), .enable("false")) multiplexer_3 (
    .in0({32{1'b1}}), .in1(multiplexer_7_out), .out(multiplexer_3_out), .sel(start));
  Multiplexer #(.width(32), .enable("false")) multiplexer_4 (
    .in0({32{1'b1}}), .in1(multiplexer_8_out), .out(multiplexer_4_out), .sel(start));
  Register #(.width(32)) register_1 (.D(multiplexer_1_out), .Q(register_1_q), .clk(clk), .clr(clr));  // open: en
  Register #(.width(32)) register_2 (.D(multiplexer_2_out), .Q(b_prime), .clk(clk), .clr(clr));  // open: en
  Register #(.width(32)) register_3 (.D(multiplexer_3_out), .Q(register_3_q), .clk(clk), .clr(clr));  // open: en
  Register #(.width(32)) register_4 (.D(multiplexer_4_out), .Q(register_4_q), .clk(clk), .clr(clr));  // open: en
  SqrX sqrx_1 (
    .a(register_1_q), .b(b_prime), .c(register_3_q), .d(register_4_q), .a_prime(sqrx_1_a_prime),
    .b_prime(sqrx_1_b_prime), .c_prime(sqrx_1_c_prime), .d_prime(sqrx_1_d_prime));
  sqrX_A sqrx_a_1 (
    .a(register_1_q), .b(b_prime), .c(register_3_q), .d(register_4_q),
    .a_prime_prime(sqrx_a_1_a_prime_prime), .b_prime_prime(sqrx_a_1_b_prime_prime),
    .c_prime_prime(sqrx_a_1_c_prime_prime), .d_prime_prime(sqrx_a_1_d_prime_prime));
  Multiplexer #(.width(32), .enable("false")) multiplexer_5 (
    .in0(sqrx_1_a_prime), .in1(sqrx_a_1_a_prime_prime), .out(multiplexer_5_out), .sel(ni_1));
  Multiplexer #(.width(32), .enable("false")) multiplexer_6 (
    .in0(sqrx_1_b_prime), .in1(sqrx_a_1_b_prime_prime), .out(multiplexer_6_out), .sel(ni_1));
  Multiplexer #(.width(32), .enable("false")) multiplexer_7 (
    .in0(sqrx_1_c_prime), .in1(sqrx_a_1_c_prime_prime), .out(multiplexer_7_out), .sel(ni_1));
  Multiplexer #(.width(32), .enable("false")) multiplexer_8 (
    .in0(sqrx_1_d_prime), .in1(sqrx_a_1_d_prime_prime), .out(multiplexer_8_out), .sel(ni_1));
endmodule

module Display (
  input  [31:0] Fi,
  output [3:0] D0,
  output [3:0] D1,
  output [3:0] D2,
  output [3:0] D3,
  output [3:0] D4,
  output [3:0] D5,
  output [3:0] D6,
  output [3:0] D7,
  output [3:0] D8,
  output [3:0] D9
);

  wire [31:0] divider_1_out, divider_1_rem, divider_2_out, divider_2_rem, divider_3_out, divider_3_rem,
       divider_4_out, divider_4_rem, divider_5_out, divider_5_rem, divider_6_out, divider_6_rem,
       divider_7_out, divider_7_rem, divider_8_out, divider_8_rem, divider_9_out, divider_9_rem;

  Divider #(.width(32)) divider_1 (.a(Fi), .b(32'ha), .out(divider_1_out), .upper({32{1'b0}}), .rem(divider_1_rem));
  \取低位  \u_取低位_1  (.number(divider_1_rem), .number_prime(D0));
  Divider #(.width(32)) divider_2 (
    .a(divider_1_out), .b(32'ha), .out(divider_2_out), .upper({32{1'b0}}), .rem(divider_2_rem));
  \取低位  \u_取低位_2  (.number(divider_2_rem), .number_prime(D1));
  Divider #(.width(32)) divider_3 (
    .a(divider_2_out), .b(32'ha), .out(divider_3_out), .upper({32{1'b0}}), .rem(divider_3_rem));
  \取低位  \u_取低位_3  (.number(divider_3_rem), .number_prime(D2));
  Divider #(.width(32)) divider_4 (
    .a(divider_3_out), .b(32'ha), .out(divider_4_out), .upper({32{1'b0}}), .rem(divider_4_rem));
  \取低位  \u_取低位_4  (.number(divider_4_rem), .number_prime(D3));
  Divider #(.width(32)) divider_5 (
    .a(divider_4_out), .b(32'ha), .out(divider_5_out), .upper({32{1'b0}}), .rem(divider_5_rem));
  \取低位  \u_取低位_5  (.number(divider_5_rem), .number_prime(D4));
  Divider #(.width(32)) divider_6 (
    .a(divider_5_out), .b(32'ha), .out(divider_6_out), .upper({32{1'b0}}), .rem(divider_6_rem));
  \取低位  \u_取低位_6  (.number(divider_6_rem), .number_prime(D5));
  Divider #(.width(32)) divider_7 (
    .a(divider_6_out), .b(32'ha), .out(divider_7_out), .upper({32{1'b0}}), .rem(divider_7_rem));
  \取低位  \u_取低位_7  (.number(divider_7_rem), .number_prime(D6));
  Divider #(.width(32)) divider_8 (
    .a(divider_7_out), .b(32'ha), .out(divider_8_out), .upper({32{1'b0}}), .rem(divider_8_rem));
  \取低位  \u_取低位_8  (.number(divider_8_rem), .number_prime(D7));
  Divider #(.width(32)) divider_9 (
    .a(divider_8_out), .b(32'ha), .out(divider_9_out), .upper({32{1'b0}}), .rem(divider_9_rem));
  \取低位  \u_取低位_9  (.number(divider_9_rem), .number_prime(D8));
  \取低位  \u_取低位_10  (.number(divider_9_out), .number_prime(D9));
endmodule

module \取低位  (
  input  [31:0] number,
  output [3:0] number_prime
);


  assign number_prime = number[3:0];
endmodule

module Controller (
  input  [5:0] n,
  input  clear,
  input  clock,
  output n_i_1,
  output start,
  output clk,
  output clear_2
);

  wire comparator_1_gt, not_1_out, not_2_out, or_1_out, or_2_out;
  wire [7:0] counter_1_q;

  Shift_Register #(.length(6)) shift_register_1 (
    .shift(1'b1), .in(1'b0), .clk(or_1_out), .out(n_i_1), .load(clear), .clr(1'b0), .d0(n[0]), .d1(n[1]),
    .d2(n[2]), .d3(n[3]), .d4(n[4]), .d5(n[5]));  // open: q0, q1, q2, q3, q4, q5
  or or_1 (or_1_out, clear, clock);
  and and_1 (clear_2, clear, not_1_out);
  not not_1 (not_1_out, clock);
  Counter counter_1 (
    .load(1'b0), .D({8{1'b0}}), .count(1'b1), .Q(counter_1_q), .clk(clock), .clr(clear));  // open: carry
  Comparator comparator_1 (.a(counter_1_q), .b(8'h5), .gt(comparator_1_gt));  // open: eq, lt
  D_Flip_Flop d_ff_1 (.clk(clock), .D(or_2_out), .Q(start), .reset(clear));  // open: Qn, preset, en
  or or_2 (or_2_out, n_i_1, start);
  and and_2 (clk, clock, not_2_out);
  not not_2 (not_2_out, comparator_1_gt);
endmodule
