// Logisim project cpu_.circ as structural Verilog: 10 circuits, main circuit ◇多周期MIPS(微程序)
module \单周期MIPS_硬布线  (
);

  wire and_1_out, and_2_out, CLK, mips_alu_1_equal, not_1_out, not_2_out, not_3_out, or_1_out, RST,
       \单周期硬布线控制器_1_alusrc , \单周期硬布线控制器_1_beq , \单周期硬布线控制器_1_bne , \单周期硬布线控制器_1_halt ,
       \单周期硬布线控制器_1_memtoreg , \单周期硬布线控制器_1_memwrite , \单周期硬布线控制器_1_regdst , \单周期硬布线控制器_1_regwrite ;
  wire [1:0] PC_q;
  wire [3:0] \单周期硬布线控制器_1_alu_op ;
  wire [4:0] multiplexer_2_out, rom_1_data, rom_1_data_4, rom_1_data_5;
  wire [5:0] rom_1_data_3;
  wire [9:0] PC_q_2;
  wire [15:0] adder_3_out, \总周期数 ;
  wire [19:0] PC_q_3;
  wire [31:0] adder_1_out, adder_2_out, bit_extender_1_out, mips_alu_1_result, mips_regifile_1_r1,
       mips_regifile_1_r2, multiplexer_1_out, multiplexer_3_out, multiplexer_4_out, ram_1_data, shifter_1_out;
  wire [31:21] rom_1_data_2;

  Button \u_总复位  (.out(RST));
  not not_1 (not_1_out, \单周期硬布线控制器_1_halt );
  Register #(.width(32)) PC (
    .D(multiplexer_1_out), .en(not_1_out), .Q({PC_q_3, PC_q_2, PC_q}), .clk(CLK));  // open: clr
  Multiplexer #(.width(32), .enable("false")) multiplexer_1 (
    .in0(adder_1_out), .in1(adder_2_out), .out(multiplexer_1_out), .sel(or_1_out));
  Clock clock_1 (.out(CLK));
  Adder #(.width(32)) adder_1 (.a({PC_q_3, PC_q_2, PC_q}), .b(32'h4), .out(adder_1_out), .cin(1'b0));  // open: cout
  ROM #(.addrWidth(10), .dataWidth(32)) rom_1 (
    .addr(PC_q_2), .data({rom_1_data_2, rom_1_data, rom_1_data_5, rom_1_data_4, rom_1_data_3}));  // open: sel
  Multiplexer #(.width(5), .enable("false")) multiplexer_2 (
    .in0(rom_1_data), .in1(rom_1_data_5), .out(multiplexer_2_out), .sel(\单周期硬布线控制器_1_regdst ));
  assign bit_extender_1_out = {{16{rom_1_data_5[4]}}, {rom_1_data_5, rom_1_data_4, rom_1_data_3}};  // Bit_Extender bit_extender_1
  or or_1 (or_1_out, and_1_out, and_2_out);
  MIPS_Regifile mips_regifile_1 (
    .Din(multiplexer_4_out), .Clk(CLK), .R1(mips_regifile_1_r1), .R2(mips_regifile_1_r2),
    .WE(\单周期硬布线控制器_1_regwrite ), .W_num(multiplexer_2_out), .R1_num(rom_1_data_2[25:21]), .R2_num(rom_1_data));
  Multiplexer #(.width(32), .enable("false")) multiplexer_3 (
    .in0(mips_regifile_1_r2), .in1(bit_extender_1_out), .out(multiplexer_3_out), .sel(\单周期硬布线控制器_1_alusrc ));
  Shifter #(.width(32)) shifter_1 (.in(bit_extender_1_out), .\dist (5'b00010), .out(shifter_1_out));
  // Probe on \总周期数 
  and and_1 (and_1_out, \单周期硬布线控制器_1_bne , ~mips_alu_1_equal);  // AND_Gate
  and and_2 (and_2_out, \单周期硬布线控制器_1_beq , mips_alu_1_equal);
  MIPS_ALU mips_alu_1 (
    .X(mips_regifile_1_r1), .Y(multiplexer_3_out), .AluOP(\单周期硬布线控制器_1_alu_op ), .Equal(mips_alu_1_equal),
    .Result(mips_alu_1_result));  // open: Result_2
  Adder #(.width(32)) adder_2 (.a(shifter_1_out), .b(adder_1_out), .out(adder_2_out), .cin(1'b0));  // open: cout
  not not_2 (not_2_out, \单周期硬布线控制器_1_memwrite );
  Multiplexer #(.width(32), .enable("false")) multiplexer_4 (
    .in0(mips_alu_1_result), .in1(ram_1_data), .out(multiplexer_4_out), .sel(\单周期硬布线控制器_1_memtoreg ));
  RAM #(.addrWidth(10), .dataWidth(32), .bus("separate")) ram_1 (
    .addr(mips_alu_1_result[11:2]), .din(mips_regifile_1_r2), .data(ram_1_data),
    .str(\单周期硬布线控制器_1_memwrite ), .clk(CLK), .ld(not_2_out), .clr(RST));  // open: sel
  Adder #(.width(16)) adder_3 (.a(\总周期数 ), .b(16'h1), .out(adder_3_out));  // open: cin, cout
  not not_3 (not_3_out, \单周期硬布线控制器_1_halt );
  \单周期硬布线控制器  \u_单周期硬布线控制器_1  (
    .Func(rom_1_data_3), .RegWrite(\单周期硬布线控制器_1_regwrite ), .MemToReg(\单周期硬布线控制器_1_memtoreg ),
    .MemWrite(\单周期硬布线控制器_1_memwrite ), .Beq(\单周期硬布线控制器_1_beq ), .Bne(\单周期硬布线控制器_1_bne ),
    .RegDst(\单周期硬布线控制器_1_regdst ), .AluSrc(\单周期硬布线控制器_1_alusrc ), .ALU_OP(\单周期硬布线控制器_1_alu_op ),
    .OP(rom_1_data_2[31:26]), .Halt(\单周期硬布线控制器_1_halt ));
  Register #(.width(16)) \u_周期  (.D(adder_3_out), .en(not_3_out), .Q(\总周期数 ), .clk(CLK));  // open: clr

  // Notes on the sheet:
  //   指令存储器
  //   contents of rom_1 (hex, n*v repeats v):
  //   2010ffff 20110000 ae300200 22100001 22310004 ae300200 22100001 22310004 ae300200 22100001 22310004
  //   ae300200 22100001 22310004 ae300200 22100001 22310004 ae300200 22100001 22310004 ae300200 22100001
  //   22310004 ae300200 8020 2011001c 8e130200 8e340200 274402a 11000002 ae330200 ae140200 2231fffc
  //   1611fff8 22100004 2011001c 1611fff5 2002000a c
  //   Ctrl+K  Command+K触发时钟连续仿真，程序运行结束后可停机，查看数据存储器中80单元的排序情况是有符号降序
  //   总周期数参考值：224
  //   Halt
  //   Op
  //   Func
  //   MemToReg
  //   MemWrite
  //   Beq
  //   Bne
  //   AluOP
  //   AluSrcB
  //   RegWrite
  //   RegDst
endmodule

// 单周期硬布线控制器
module \单周期硬布线控制器  (
  input  [5:0] OP,
  input  [5:0] Func,
  output [3:0] ALU_OP,
  output RegDst,
  output RegWrite,
  output MemToReg,
  output MemWrite,
  output AluSrc,
  output Beq,
  output Bne,
  output Halt
);

  wire ADD, ADDI, and_5_out, and_6_out, and_7_out, comparator_6_eq, comparator_7_eq, comparator_8_eq,
       comparator_9_eq, R_TYPE, SLT;

  Comparator #(.width(6)) comparator_1 (.a(OP), .b(6'b100011), .eq(MemToReg));  // open: gt, lt
  Comparator #(.width(6)) comparator_2 (.a(OP), .b(6'b101011), .eq(MemWrite));  // open: gt, lt
  Comparator #(.width(6)) comparator_3 (.a(OP), .b(6'b000100), .eq(Beq));  // open: gt, lt
  Comparator #(.width(6)) comparator_4 (.a(OP), .b(6'b000101), .eq(Bne));  // open: gt, lt
  Comparator #(.width(6)) comparator_5 (.a(OP), .b(6'b001000), .eq(ADDI));  // open: gt, lt
  Comparator #(.width(6)) comparator_6 (.a(OP), .b({6{1'b0}}), .eq(comparator_6_eq));  // open: gt, lt
  Comparator #(.width(6)) comparator_7 (.a(Func), .b(6'b001100), .eq(comparator_7_eq));  // open: gt, lt
  Comparator #(.width(6)) comparator_8 (.a(Func), .b(6'b101010), .eq(comparator_8_eq));  // open: gt, lt
  Comparator #(.width(6)) comparator_9 (.a(Func), .b(6'b100000), .eq(comparator_9_eq));  // open: gt, lt
  or or_1 (RegDst, Halt, R_TYPE);
  and and_1 (R_TYPE, ~comparator_7_eq, comparator_6_eq);  // AND_Gate
  and and_2 (Halt, comparator_7_eq, comparator_6_eq);
  and and_3 (SLT, comparator_8_eq, comparator_6_eq);
  and and_4 (ADD, comparator_9_eq, comparator_6_eq);
  or or_2 (RegWrite, ADDI, MemToReg, R_TYPE);
  or or_3 (AluSrc, ADDI, MemToReg, MemWrite);
  Multiplexer #(.width(4), .enable("false")) multiplexer_1 (
    .in0(4'b0101), .in1(4'b1011), .out(ALU_OP), .sel(and_7_out));
  and and_5 (and_5_out, ~OP[0], ~OP[1], ~OP[2], ~OP[4], ~OP[5], ~OP[3]);  // AND_Gate
  and and_6 (and_6_out, ~Func[0], Func[1], ~Func[2], Func[3], ~Func[4], Func[5]);  // AND_Gate
  and and_7 (and_7_out, and_5_out, and_6_out);

  // Other names for the same wires on the sheet: LW = MemToReg; SW = MemWrite; SysCall = Halt

  // Notes on the sheet:
  //   指令译码信号
  //   指令译码逻辑
  //   给出简单的逻辑实现对应指令译码信号，LW、SW、BEQ、BNE、ADDI、ADD、SLT、SYSCALL、R_TYPE。
  //   ALU控制器逻辑
  //   注意R_TYPE表示R型运算指令，SYSCALL是特殊的R型指令，不属于这个类别
  //   根据指令译码信号实现控制器输出控制信号的逻辑
  //   给出简单的逻辑实现ALU_OP与OP、Func之间的对应关系
  //   控制信号
endmodule

module \多周期MIPS_微程序  (
);

  wire and_1_out, and_2_out, CLK, comparator_1_eq, IorD, IRwr, Mered, Mewr, mips_alu_1_equal, not_1_out,
       or_1_out, RST, \多周期微程序控制器_1_alusrca , \多周期微程序控制器_1_beq , \多周期微程序控制器_1_bne , \多周期微程序控制器_1_memtoreg ,
       \多周期微程序控制器_1_pcsrc , \多周期微程序控制器_1_pcwrite , \多周期微程序控制器_1_regdst , \多周期微程序控制器_1_regwrite ;
  wire [1:0] multiplexer_1_out, \多周期微程序控制器_1_alusrcb ;
  wire [3:0] \多周期微程序控制器_1_alu_op , \多周期微程序控制器_1_当前微指令地址 ;
  wire [4:0] multiplexer_3_out;
  wire [9:0] addr;
  wire [15:0] adder_1_out, counter_1_q, \总周期数 ;
  wire [19:0] multiplexer_1_out_2;
  wire [31:0] A_q, B_q, bit_extender_1_out, C_q, data, insr, mips_alu_1_result, mips_regifile_1_r1,
       mips_regifile_1_r2, multiplexer_2_out, multiplexer_4_out, multiplexer_5_out, multiplexer_6_out, PC_q,
       ram_1_data, shifter_1_out;

  Button \u_总复位  (.out(RST));
  Multiplexer #(.width(32), .enable("false")) multiplexer_1 (
    .in0(PC_q), .in1(C_q), .out({multiplexer_1_out_2, addr, multiplexer_1_out}), .sel(IorD));
  Register #(.width(32)) PC (.D(multiplexer_6_out), .en(or_1_out), .Q(PC_q), .clk(CLK));  // open: clr
  Clock clock_1 (.out(CLK));
  Multiplexer #(.width(32), .enable("false")) multiplexer_2 (
    .in0(C_q), .in1(data), .out(multiplexer_2_out), .sel(\多周期微程序控制器_1_memtoreg ));
  RAM #(.addrWidth(10), .dataWidth(32), .bus("separate")) ram_1 (
    .addr(addr), .din(B_q), .data(ram_1_data), .str(Mewr), .clk(CLK), .ld(Mered));  // open: sel, clr
  Register #(.width(32)) IR (.D(ram_1_data), .en(IRwr), .Q(insr), .clk(CLK));  // open: clr
  Register #(.width(32)) DR (.D(ram_1_data), .Q(data), .clk(CLK));  // open: en, clr
  Multiplexer #(.width(5), .enable("false")) multiplexer_3 (
    .in0(insr[20:16]), .in1(insr[15:11]), .out(multiplexer_3_out), .sel(\多周期微程序控制器_1_regdst ));
  assign bit_extender_1_out = {{16{insr[15]}}, insr[15:0]};  // Bit_Extender bit_extender_1
  // Probe on \总周期数 
  MIPS_Regifile mips_regifile_1 (
    .Din(multiplexer_2_out), .Clk(CLK), .R1(mips_regifile_1_r1), .R2(mips_regifile_1_r2),
    .WE(\多周期微程序控制器_1_regwrite ), .W_num(multiplexer_3_out), .R1_num(insr[25:21]), .R2_num(insr[20:16]));
  Shifter #(.width(32)) shifter_1 (.in(bit_extender_1_out), .\dist (5'b00010), .out(shifter_1_out));
  Multiplexer #(.width(32), .enable("false")) multiplexer_4 (
    .in0(PC_q), .in1(A_q), .out(multiplexer_4_out), .sel(\多周期微程序控制器_1_alusrca ));
  Register #(.width(32)) A (.D(mips_regifile_1_r1), .Q(A_q), .clk(CLK));  // open: en, clr
  Register #(.width(32)) B (.D(mips_regifile_1_r2), .Q(B_q), .clk(CLK));  // open: en, clr
  Multiplexer #(.select(2), .width(32), .enable("false")) multiplexer_5 (
    .in0(B_q), .in1(32'h4), .in2(bit_extender_1_out), .in3(shifter_1_out), .out(multiplexer_5_out),
    .sel(\多周期微程序控制器_1_alusrcb ));
  MIPS_ALU mips_alu_1 (
    .X(multiplexer_4_out), .Y(multiplexer_5_out), .AluOP(\多周期微程序控制器_1_alu_op ), .Equal(mips_alu_1_equal),
    .Result(mips_alu_1_result));  // open: Result_2
  Multiplexer #(.width(32), .enable("false")) multiplexer_6 (
    .in0(mips_alu_1_result), .in1(C_q), .out(multiplexer_6_out), .sel(\多周期微程序控制器_1_pcsrc ));
  Register #(.width(32)) C (.D(mips_alu_1_result), .Q(C_q), .clk(CLK));  // open: en, clr
  // Probe on \多周期微程序控制器_1_当前微指令地址 
  \多周期微程序控制器  \u_多周期微程序控制器_1  (
    .PcWrite(\多周期微程序控制器_1_pcwrite ), .Beq(\多周期微程序控制器_1_beq ), .PCsrc(\多周期微程序控制器_1_pcsrc ),
    .AluSrcB(\多周期微程序控制器_1_alusrcb ), .AluSrcA(\多周期微程序控制器_1_alusrca ), .RegWrite(\多周期微程序控制器_1_regwrite ),
    .MemToReg(\多周期微程序控制器_1_memtoreg ), .RegDst(\多周期微程序控制器_1_regdst ), .IorD(IorD), .MemWrite(Mewr),
    .MemRead(Mered), .IrWrite(IRwr), .Bne(\多周期微程序控制器_1_bne ), .CLK(CLK), .\当前微指令地址 (\多周期微程序控制器_1_当前微指令地址 ),
    .RST(RST), .OP(insr[31:26]), .ALU_OP(\多周期微程序控制器_1_alu_op ), .Func(insr[5:0]));
  and and_1 (and_1_out, mips_alu_1_equal, \多周期微程序控制器_1_beq );
  and and_2 (and_2_out, \多周期微程序控制器_1_bne , ~mips_alu_1_equal);  // AND_Gate
  or or_1 (or_1_out, and_1_out, \多周期微程序控制器_1_pcwrite , and_2_out);
  Adder #(.width(16)) adder_1 (.a(counter_1_q), .b(16'h1), .out(adder_1_out));  // open: cin, cout
  not not_1 (not_1_out, comparator_1_eq);
  Comparator #(.width(10)) comparator_1 (.a(addr), .b(10'h27), .eq(comparator_1_eq));  // open: gt, lt
  Multiplexer #(.width(16), .enable("false")) multiplexer_7 (
    .in0(counter_1_q), .in1(adder_1_out), .out(\总周期数 ), .sel(comparator_1_eq));
  Counter #(.width(16), .max('hffff)) counter_1 (
    .D(adder_1_out), .count(not_1_out), .Q(counter_1_q), .clk(CLK), .clr(RST));  // open: load, carry

  // Notes on the sheet:
  //   存储器
  //   Ctrl+K  Command+K触发时钟连续仿真，程序运行结束后可停机，查看数据存储器中80单元的排序情况是有符号降序
  //   总周期数参考值：891
  //   IorD
  //   MemWrite
  //   MemRead
  //   IRWrite
  //   OP
  //   Func
  //   RegDst
  //   PcWrite
  //   Beq
  //   Bne
  //   PcSrc
  //   AluOP
  //   AluSrcB
  //   AluSrcA
  //   RegWrite
  //   MemToReg
endmodule

// 微程序控制器
module \多周期微程序控制器  (
  input  [5:0] OP,
  input  [5:0] Func,
  input  CLK,
  input  RST,
  output [3:0] ALU_OP,
  output Bne,
  output Beq,
  output MemRead,
  output MemWrite,
  output RegWrite,
  output PcWrite,
  output IrWrite,
  output RegDst,
  output MemToReg,
  output [3:0] \当前微指令地址 ,
  output [1:0] AluSrcB,
  output AluSrcA,
  output PCsrc,
  output IorD
);

  wire ADD, ADDI, and_5_out, BEQ_t, BNE_t, comparator_6_eq, comparator_7_eq, comparator_8_eq,
       comparator_9_eq, comparator_10_eq, comparator_11_eq, LW, P, R_TYPE, SLT, SW, SysCall;
  wire [1:0] ALU_Control;
  wire [3:0] multiplexer_1_out, multiplexer_2_out, rom_1_data, \微程序地址转移逻辑_1_s0 ;

  Comparator #(.width(6)) comparator_1 (.a(OP), .b(6'b100011), .eq(LW));  // open: gt, lt
  Comparator #(.width(6)) comparator_2 (.a(OP), .b(6'b101011), .eq(SW));  // open: gt, lt
  Comparator #(.width(6)) comparator_3 (.a(OP), .b(6'b000100), .eq(BEQ_t));  // open: gt, lt
  Comparator #(.width(6)) comparator_4 (.a(OP), .b(6'b000101), .eq(BNE_t));  // open: gt, lt
  Comparator #(.width(6)) comparator_5 (.a(OP), .b(6'b001000), .eq(ADDI));  // open: gt, lt
  Comparator #(.width(6)) comparator_6 (.a(OP), .b({6{1'b0}}), .eq(comparator_6_eq));  // open: gt, lt
  \微程序地址转移逻辑  \u_微程序地址转移逻辑_1  (
    .R_Type(R_TYPE), .S3(\微程序地址转移逻辑_1_s0 [3]), .ADDI(ADDI), .S2(\微程序地址转移逻辑_1_s0 [2]), .LW(LW),
    .S1(\微程序地址转移逻辑_1_s0 [1]), .SW(SW), .S0(\微程序地址转移逻辑_1_s0 [0]), .BEQ(BEQ_t), .BNE(BNE_t), .SYSCALL(SysCall));
  Comparator #(.width(6)) comparator_7 (.a(Func), .b(6'b001100), .eq(comparator_7_eq));  // open: gt, lt
  Comparator #(.width(6)) comparator_8 (.a(Func), .b(6'b101010), .eq(comparator_8_eq));  // open: gt, lt
  Comparator #(.width(6)) comparator_9 (.a(Func), .b(6'b100000), .eq(comparator_9_eq));  // open: gt, lt
  and and_1 (R_TYPE, ~comparator_7_eq, comparator_6_eq);  // AND_Gate
  and and_2 (SysCall, comparator_7_eq, comparator_6_eq);
  and and_3 (SLT, comparator_8_eq, comparator_6_eq);
  and and_4 (ADD, comparator_9_eq, comparator_6_eq);
  Multiplexer #(.width(4), .enable("false")) multiplexer_1 (
    .in0(rom_1_data), .in1(\微程序地址转移逻辑_1_s0 ), .out(multiplexer_1_out), .sel(P));
  Register #(.width(4)) register_1 (.D(multiplexer_1_out), .Q(\当前微指令地址 ), .clk(CLK), .clr(RST));  // open: en
  Comparator #(.width(6)) comparator_10 (.a(OP), .b({6{1'b0}}), .eq(comparator_10_eq));  // open: gt, lt
  Comparator #(.width(6)) comparator_11 (.a(Func), .b(6'b101010), .eq(comparator_11_eq));  // open: gt, lt
  ROM #(.addrWidth(4), .dataWidth(21)) rom_1 (
    .addr(\当前微指令地址 ),
    .data({IorD, PCsrc, AluSrcA, AluSrcB, MemToReg, RegDst, IrWrite, PcWrite, RegWrite, MemWrite, MemRead, Beq, Bne, ALU_Control, P, rom_1_data}));  // open: sel
  and and_5 (and_5_out, comparator_10_eq, comparator_11_eq);
  Multiplexer #(.width(4), .enable("false")) multiplexer_2 (
    .in0(4'b0101), .in1(4'b1011), .out(multiplexer_2_out), .sel(and_5_out));
  Multiplexer #(.select(2), .width(4), .enable("false")) multiplexer_3 (
    .in0(4'b0101), .in1(4'b0110), .in2(multiplexer_2_out), .out(ALU_OP), .sel(ALU_Control));  // open: in3

  // Notes on the sheet:
  //   指令译码信号
  //   根据指令进行微程序地址转移
  //   指令译码逻辑
  //   给出简单的逻辑实现对应指令译码信号，LW、SW、BEQ、BNE、ADDI、ADD、SLT、SYSCALL、R_TYPE。
  //   下址字段
  //   微程序
  //   入口地址
  //   判断逻辑
  //   μAR
  //   控制存储器
  //   contents of rom_1 (hex, n*v repeats v):
  //   13201 30010 60003 100204 8800 60006 100400 40048 4840 c0120 c00a0 6000c 800 6d
  //   微命令
  //   ALU控制器逻辑
  //   根据ALU_Control的值决定运算器运算选择控制信号ALU_OP的值
  //   注意R_TYPE表示R型运算指令，SYSCALL是特殊的R型指令，不属于这个类别
  //   微指令
  //   下址字段
  //   判断逻辑
  //   ALU_Control= 00 运算器做加法
  //   ALU_Control= 01 运算器做减法
  //   ALU_Control= 10 运算方式由Func决定 
endmodule

// 地址转移逻辑
module \微程序地址转移逻辑  (
  input  R_Type,
  input  ADDI,
  input  LW,
  input  SW,
  input  BEQ,
  input  BNE,
  input  SYSCALL,
  output S3,
  output S2,
  output S1,
  output S0
);

  or or_1 (S3, ADDI, BEQ, BNE, SYSCALL);
  or or_2 (S2, R_Type, SW, SYSCALL);
  or or_3 (S1, R_Type, ADDI, LW, BNE);
  or or_4 (S0, R_Type, ADDI, SW, BEQ, SYSCALL);
endmodule

module \多周期MIPS_硬布线  (
);

  wire and_1_out, and_2_out, CLK, comparator_1_eq, IorD, IRwr, Mered, Mewr, mips_alu_1_equal, not_1_out,
       or_1_out, RST, \多周期硬布线控制器_1_alusrca , \多周期硬布线控制器_1_beq , \多周期硬布线控制器_1_bne , \多周期硬布线控制器_1_memtoreg ,
       \多周期硬布线控制器_1_pcsrc , \多周期硬布线控制器_1_pcwrite , \多周期硬布线控制器_1_regdst , \多周期硬布线控制器_1_regwrite ;
  wire [1:0] \多周期硬布线控制器_1_alusrcb ;
  wire [3:0] \多周期硬布线控制器_1_alu_op , \多周期硬布线控制器_1_当前状态 ;
  wire [4:0] multiplexer_3_out;
  wire [9:0] addr;
  wire [15:0] adder_1_out, counter_1_q, \总周期数 ;
  wire [31:0] A_q, B_q, bit_extender_1_out, C_q, data, insr, mips_alu_1_result, mips_regifile_1_r1,
       mips_regifile_1_r2, multiplexer_1_out, multiplexer_2_out, multiplexer_4_out, multiplexer_5_out,
       multiplexer_6_out, PC_q, ram_1_data, shifter_1_out;

  Button \u_总复位  (.out(RST));
  Multiplexer #(.width(32), .enable("false")) multiplexer_1 (
    .in0(PC_q), .in1(C_q), .out({multiplexer_1_out[31:12], addr, multiplexer_1_out[1:0]}), .sel(IorD));
  Register #(.width(32)) PC (.D(multiplexer_6_out), .en(or_1_out), .Q(PC_q), .clk(CLK));  // open: clr
  Clock clock_1 (.out(CLK));
  RAM #(.addrWidth(10), .dataWidth(32), .bus("separate")) ram_1 (
    .addr(addr), .din(B_q), .data(ram_1_data), .str(Mewr), .clk(CLK), .ld(Mered));  // open: sel, clr
  Multiplexer #(.width(32), .enable("false")) multiplexer_2 (
    .in0(C_q), .in1(data), .out(multiplexer_2_out), .sel(\多周期硬布线控制器_1_memtoreg ));
  Register #(.width(32)) IR (.D(ram_1_data), .en(IRwr), .Q(insr), .clk(CLK));  // open: clr
  Register #(.width(32)) DR (.D(ram_1_data), .Q(data), .clk(CLK));  // open: en, clr
  Multiplexer #(.width(5), .enable("false")) multiplexer_3 (
    .in0(insr[20:16]), .in1(insr[15:11]), .out(multiplexer_3_out), .sel(\多周期硬布线控制器_1_regdst ));
  assign bit_extender_1_out = {{16{insr[15]}}, insr[15:0]};  // Bit_Extender bit_extender_1
  // Probe on \总周期数 
  MIPS_Regifile mips_regifile_1 (
    .Din(multiplexer_2_out), .Clk(CLK), .R1(mips_regifile_1_r1), .R2(mips_regifile_1_r2),
    .WE(\多周期硬布线控制器_1_regwrite ), .W_num(multiplexer_3_out), .R1_num(insr[25:21]), .R2_num(insr[20:16]));
  Shifter #(.width(32)) shifter_1 (.in(bit_extender_1_out), .\dist (5'b00010), .out(shifter_1_out));
  Multiplexer #(.width(32), .enable("false")) multiplexer_4 (
    .in0(PC_q), .in1(A_q), .out(multiplexer_4_out), .sel(\多周期硬布线控制器_1_alusrca ));
  Register #(.width(32)) A (.D(mips_regifile_1_r1), .Q(A_q), .clk(CLK));  // open: en, clr
  Register #(.width(32)) B (.D(mips_regifile_1_r2), .Q(B_q), .clk(CLK));  // open: en, clr
  Multiplexer #(.select(2), .width(32), .enable("false")) multiplexer_5 (
    .in0(B_q), .in1(32'h4), .in2(bit_extender_1_out), .in3(shifter_1_out), .out(multiplexer_5_out),
    .sel(\多周期硬布线控制器_1_alusrcb ));
  MIPS_ALU mips_alu_1 (
    .X(multiplexer_4_out), .Y(multiplexer_5_out), .AluOP(\多周期硬布线控制器_1_alu_op ), .Equal(mips_alu_1_equal),
    .Result(mips_alu_1_result));  // open: Result_2
  Multiplexer #(.width(32), .enable("false")) multiplexer_6 (
    .in0(mips_alu_1_result), .in1(C_q), .out(multiplexer_6_out), .sel(\多周期硬布线控制器_1_pcsrc ));
  Register #(.width(32)) C (.D(mips_alu_1_result), .Q(C_q), .clk(CLK));  // open: en, clr
  \多周期硬布线控制器  \u_多周期硬布线控制器_1  (
    .RST(RST), .AluSrcB(\多周期硬布线控制器_1_alusrcb ), .OP(insr[31:26]), .CLK(CLK), .\当前状态 (\多周期硬布线控制器_1_当前状态 ),
    .IorD(IorD), .PCsrc(\多周期硬布线控制器_1_pcsrc ), .AluSrcA(\多周期硬布线控制器_1_alusrca ),
    .MemToReg(\多周期硬布线控制器_1_memtoreg ), .RegDst(\多周期硬布线控制器_1_regdst ), .IrWrite(IRwr),
    .PcWrite(\多周期硬布线控制器_1_pcwrite ), .RegWrite(\多周期硬布线控制器_1_regwrite ), .MemWrite(Mewr), .MemRead(Mered),
    .Beq(\多周期硬布线控制器_1_beq ), .Bne(\多周期硬布线控制器_1_bne ), .Func(insr[5:0]), .ALU_OP(\多周期硬布线控制器_1_alu_op ));
  // Probe on \多周期硬布线控制器_1_当前状态 
  and and_1 (and_1_out, mips_alu_1_equal, \多周期硬布线控制器_1_beq );
  or or_1 (or_1_out, and_1_out, \多周期硬布线控制器_1_pcwrite , and_2_out);
  and and_2 (and_2_out, \多周期硬布线控制器_1_bne , ~mips_alu_1_equal);  // AND_Gate
  Adder #(.width(16)) adder_1 (.a(counter_1_q), .b(16'h1), .out(adder_1_out));  // open: cin, cout
  not not_1 (not_1_out, comparator_1_eq);
  Comparator #(.width(10)) comparator_1 (.a(addr), .b(10'h27), .eq(comparator_1_eq));  // open: gt, lt
  Multiplexer #(.width(16), .enable("false")) multiplexer_7 (
    .in0(counter_1_q), .in1(adder_1_out), .out(\总周期数 ), .sel(comparator_1_eq));
  Counter #(.width(16), .max('hffff)) counter_1 (
    .D(adder_1_out), .count(not_1_out), .Q(counter_1_q), .clk(CLK), .clr(RST));  // open: load, carry

  // Notes on the sheet:
  //   存储器
  //   Ctrl+K  Command+K触发时钟连续仿真，程序运行结束后可停机，查看数据存储器中80单元的排序情况是有符号降序
  //   完成微程序模式的多周期CPU后，将主机架构图复制到本电路中，替换控制器为硬布线控制器
  //   总周期数参考值：891
  //   IorD
  //   MemWrite
  //   MemRead
  //   IRWrite
  //   OP
  //   Func
  //   RegDst
  //   Beq
  //   Bne
  //   PcWrite
  //   PcSrc
  //   AluOP
  //   AluSrcB
  //   AluSrcA
  //   RegWrite
  //   MemToReg
endmodule

// 硬布线控制器
module \多周期硬布线控制器  (
  input  [5:0] OP,
  input  [5:0] Func,
  input  CLK,
  input  RST,
  output [3:0] ALU_OP,
  output Bne,
  output Beq,
  output MemRead,
  output MemWrite,
  output RegWrite,
  output PcWrite,
  output IrWrite,
  output RegDst,
  output MemToReg,
  output [3:0] \当前状态 ,
  output [1:0] AluSrcB,
  output AluSrcA,
  output PCsrc,
  output IorD
);

  wire ADD, ADDI, and_5_out, BEQ_t, BNE_t, comparator_6_eq, comparator_7_eq, comparator_8_eq,
       comparator_9_eq, comparator_10_eq, comparator_11_eq, LW, P, R_TYPE, SLT, SW, SysCall;
  wire [1:0] ALU_Control;
  wire [3:0] multiplexer_1_out, rom_1_data, \状态机fsm_1_n0 ;

  Comparator #(.width(6)) comparator_1 (.a(OP), .b(6'b100011), .eq(LW));  // open: gt, lt
  Comparator #(.width(6)) comparator_2 (.a(OP), .b(6'b101011), .eq(SW));  // open: gt, lt
  Comparator #(.width(6)) comparator_3 (.a(OP), .b(6'b000100), .eq(BEQ_t));  // open: gt, lt
  Comparator #(.width(6)) comparator_4 (.a(OP), .b(6'b000101), .eq(BNE_t));  // open: gt, lt
  Comparator #(.width(6)) comparator_5 (.a(OP), .b(6'b001000), .eq(ADDI));  // open: gt, lt
  Comparator #(.width(6)) comparator_6 (.a(OP), .b({6{1'b0}}), .eq(comparator_6_eq));  // open: gt, lt
  Comparator #(.width(6)) comparator_7 (.a(Func), .b(6'b001100), .eq(comparator_7_eq));  // open: gt, lt
  Comparator #(.width(6)) comparator_8 (.a(Func), .b(6'b101010), .eq(comparator_8_eq));  // open: gt, lt
  Comparator #(.width(6)) comparator_9 (.a(Func), .b(6'b100000), .eq(comparator_9_eq));  // open: gt, lt
  \状态机FSM  \u_状态机fsm_1  (
    .S3(\当前状态 [3]), .S2(\当前状态 [2]), .S1(\当前状态 [1]), .S0(\当前状态 [0]), .R_Type(R_TYPE), .ADDI(ADDI), .LW(LW),
    .N3(\状态机fsm_1_n0 [3]), .SW(SW), .BEQ(BEQ_t), .BNE(BNE_t), .SYSCALL(SysCall), .N2(\状态机fsm_1_n0 [2]),
    .N1(\状态机fsm_1_n0 [1]), .N0(\状态机fsm_1_n0 [0]));
  and and_1 (R_TYPE, ~comparator_7_eq, comparator_6_eq);  // AND_Gate
  and and_2 (SysCall, comparator_7_eq, comparator_6_eq);
  and and_3 (SLT, comparator_8_eq, comparator_6_eq);
  and and_4 (ADD, comparator_9_eq, comparator_6_eq);
  Register #(.width(4)) register_1 (.D(\状态机fsm_1_n0 ), .Q(\当前状态 ), .clk(CLK), .clr(RST));  // open: en
  Comparator #(.width(6)) comparator_10 (.a(OP), .b({6{1'b0}}), .eq(comparator_10_eq));  // open: gt, lt
  Comparator #(.width(6)) comparator_11 (.a(Func), .b(6'b101010), .eq(comparator_11_eq));  // open: gt, lt
  ROM #(.addrWidth(4), .dataWidth(21)) rom_1 (
    .addr(\当前状态 ),
    .data({IorD, PCsrc, AluSrcA, AluSrcB, MemToReg, RegDst, IrWrite, PcWrite, RegWrite, MemWrite, MemRead, Beq, Bne, ALU_Control, P, rom_1_data}));  // open: sel
  and and_5 (and_5_out, comparator_10_eq, comparator_11_eq);
  Multiplexer #(.width(4), .enable("false")) multiplexer_1 (
    .in0(4'b0101), .in1(4'b1011), .out(multiplexer_1_out), .sel(and_5_out));
  Multiplexer #(.select(2), .width(4), .enable("false")) multiplexer_2 (
    .in0(4'b0101), .in1(4'b0110), .in2(multiplexer_1_out), .out(ALU_OP), .sel(ALU_Control));  // open: in3

  // Notes on the sheet:
  //   指令译码信号
  //   现态
  //   组合逻辑
  //   指令译码逻辑
  //   次态
  //   状态寄存器
  //   控制存储器
  //   contents of rom_1 (hex, n*v repeats v):
  //   13201 30010 60003 100204 8800 60006 100400 40048 4840 c0120 c00a0 6000c 800 6d
  //   ALU控制器逻辑
  //   根据ALU_Control的值决定运算器运算选择控制信号ALU_OP的值
  //   ALU_Control= 00 运算器做加法
  //   ALU_Control= 01 运算器做减法
  //   ALU_Control= 10 运算方式由Func决定 
endmodule

// 控制器状态机
module \状态机FSM  (
  input  S3,
  input  S2,
  input  S1,
  input  S0,
  input  R_Type,
  input  ADDI,
  input  LW,
  input  SW,
  input  BEQ,
  input  BNE,
  input  SYSCALL,
  output N3,
  output N2,
  output N1,
  output N0
);

  wire and_1_out, and_2_out, and_3_out, and_4_out, and_5_out, and_6_out, and_7_out, and_8_out, and_9_out,
       and_10_out, and_11_out, and_12_out, and_13_out, and_14_out, and_15_out, and_16_out, and_17_out,
       and_18_out, and_19_out, and_20_out, and_21_out, and_22_out, and_23_out, and_24_out, and_25_out,
       and_26_out, and_27_out, and_28_out, not_1_out, not_2_out, not_3_out, not_4_out, not_5_out, not_6_out,
       not_7_out, not_8_out, not_9_out, not_10_out, not_11_out, not_12_out, not_13_out, not_14_out,
       not_15_out, not_16_out, not_17_out, not_18_out, not_19_out, not_20_out, not_21_out, not_22_out,
       not_23_out, not_24_out, not_25_out, not_26_out, not_27_out, not_28_out, not_29_out, not_30_out,
       not_31_out, not_32_out, not_33_out, not_34_out, not_35_out, not_36_out, not_37_out, not_38_out,
       not_39_out, not_40_out, not_41_out, not_42_out, not_43_out, not_44_out, not_45_out, not_46_out,
       not_47_out, not_48_out, not_49_out, not_50_out, not_51_out, not_52_out, not_53_out, not_54_out,
       not_55_out, not_56_out, not_57_out, not_58_out, not_59_out, not_60_out, not_61_out, not_62_out,
       not_63_out, not_64_out, not_65_out, not_66_out, not_67_out, not_68_out, not_69_out, not_70_out;

  not not_1 (not_1_out, S3);
  not not_2 (not_2_out, S2);
  not not_3 (not_3_out, S1);
  not not_4 (not_4_out, S3);
  not not_5 (not_5_out, S2);
  not not_6 (not_6_out, S1);
  not not_7 (not_7_out, S3);
  not not_8 (not_8_out, S2);
  not not_9 (not_9_out, S1);
  not not_10 (not_10_out, S3);
  not not_11 (not_11_out, S2);
  not not_12 (not_12_out, S1);
  not not_13 (not_13_out, S3);
  not not_14 (not_14_out, S2);
  not not_15 (not_15_out, S1);
  not not_16 (not_16_out, S3);
  not not_17 (not_17_out, S2);
  not not_18 (not_18_out, S1);
  not not_19 (not_19_out, S3);
  not not_20 (not_20_out, S2);
  not not_21 (not_21_out, S1);
  not not_22 (not_22_out, S3);
  not not_23 (not_23_out, S2);
  not not_24 (not_24_out, S1);
  not not_25 (not_25_out, S3);
  not not_26 (not_26_out, S2);
  not not_27 (not_27_out, S3);
  not not_28 (not_28_out, S1);
  not not_29 (not_29_out, S2);
  not not_30 (not_30_out, S1);
  not not_31 (not_31_out, S3);
  not not_32 (not_32_out, S2);
  not not_33 (not_33_out, S1);
  not not_34 (not_34_out, S3);
  not not_35 (not_35_out, S2);
  not not_36 (not_36_out, S1);
  not not_37 (not_37_out, S3);
  not not_38 (not_38_out, S2);
  not not_39 (not_39_out, S1);
  not not_40 (not_40_out, S3);
  not not_41 (not_41_out, S2);
  not not_42 (not_42_out, S1);
  not not_43 (not_43_out, S3);
  not not_44 (not_44_out, S2);
  not not_45 (not_45_out, S0);
  not not_46 (not_46_out, S3);
  not not_47 (not_47_out, S1);
  not not_48 (not_48_out, S3);
  not not_49 (not_49_out, S2);
  not not_50 (not_50_out, S1);
  not not_51 (not_51_out, S0);
  not not_52 (not_52_out, S3);
  not not_53 (not_53_out, S2);
  not not_54 (not_54_out, S1);
  not not_55 (not_55_out, S3);
  not not_56 (not_56_out, S2);
  not not_57 (not_57_out, S1);
  not not_58 (not_58_out, S3);
  not not_59 (not_59_out, S2);
  not not_60 (not_60_out, S1);
  not not_61 (not_61_out, S3);
  not not_62 (not_62_out, S2);
  not not_63 (not_63_out, S1);
  not not_64 (not_64_out, S3);
  not not_65 (not_65_out, S2);
  not not_66 (not_66_out, S1);
  not not_67 (not_67_out, S3);
  not not_68 (not_68_out, S2);
  not not_69 (not_69_out, S0);
  not not_70 (not_70_out, S1);
  and and_1 (and_1_out, not_1_out, not_2_out, not_3_out, S0, BEQ);
  and and_2 (and_2_out, not_4_out, not_5_out, not_6_out, S0, BNE);
  and and_3 (and_3_out, not_7_out, not_8_out, not_9_out, S0, SYSCALL);
  and and_4 (and_4_out, not_10_out, not_11_out, not_12_out, S0, ADDI);
  and and_5 (and_5_out, not_13_out, S2, S1, S0);
  and and_6 (and_6_out, S3, not_14_out, S1, S0);
  and and_7 (and_7_out, S3, S2, not_15_out, S0);
  and and_8 (and_8_out, not_16_out, not_17_out, not_18_out, S0, R_Type);
  and and_9 (and_9_out, not_19_out, not_20_out, not_21_out, S0, SW);
  and and_10 (and_10_out, not_22_out, not_23_out, not_24_out, S0, SYSCALL);
  and and_11 (and_11_out, not_25_out, not_26_out, S1, S0);
  and and_12 (and_12_out, not_27_out, S2, not_28_out, S0);
  and and_13 (and_13_out, S3, not_29_out, S1, S0);
  and and_14 (and_14_out, S3, S2, not_30_out, S0);
  and and_15 (and_15_out, not_31_out, not_32_out, not_33_out, S0, R_Type);
  and and_16 (and_16_out, not_34_out, not_35_out, not_36_out, S0, LW);
  and and_17 (and_17_out, not_37_out, not_38_out, not_39_out, S0, BNE);
  and and_18 (and_18_out, not_40_out, not_41_out, not_42_out, S0, ADDI);
  and and_19 (and_19_out, not_43_out, not_44_out, S1, not_45_out);
  and and_20 (and_20_out, not_46_out, S2, not_47_out, S0);
  and and_21 (and_21_out, not_48_out, not_49_out, not_50_out, not_51_out);
  and and_22 (and_22_out, not_52_out, not_53_out, not_54_out, S0, R_Type);
  and and_23 (and_23_out, not_55_out, not_56_out, not_57_out, S0, SW);
  and and_24 (and_24_out, not_58_out, not_59_out, not_60_out, S0, BEQ);
  and and_25 (and_25_out, not_61_out, not_62_out, not_63_out, S0, SYSCALL);
  and and_26 (and_26_out, not_64_out, not_65_out, not_66_out, S0, ADDI);
  and and_27 (and_27_out, not_67_out, not_68_out, S1, not_69_out);
  and and_28 (and_28_out, S3, S2, not_70_out, S0);
  or or_1 (N3, and_1_out, and_2_out, and_3_out, and_4_out, and_5_out, and_6_out, and_7_out);
  or or_2 (N2, and_8_out, and_9_out, and_10_out, and_11_out, and_12_out, and_13_out, and_14_out);
  or or_3 (N1, and_15_out, and_16_out, and_17_out, and_18_out, and_19_out, and_20_out);
  or or_4 (N0, and_21_out, and_22_out, and_23_out, and_24_out, and_25_out, and_26_out, and_27_out, and_28_out);
endmodule

module MIPS_Regifile (
  input  [31:0] Din,
  input  Clk,
  input  WE,
  input  [4:0] R1_num,
  input  [4:0] W_num,
  input  [4:0] R2_num,
  output [31:0] R1,
  output [31:0] R2
);

  // RegisterFile registerfile_1: pin names not known; wires that end beside it: Din, Clk, WE, W_num, R1_num, R2_num, R1, R2
endmodule

// ALU
module MIPS_ALU (
  input  [31:0] X,
  input  [31:0] Y,
  input  [3:0] AluOP,
  output Equal,
  output [31:0] Result,
  output [31:0] Result_2
);

  wire comparator_1_lt, comparator_2_lt;
  wire [0:0] comparator_4_lt, comparator_5_lt;
  wire [31:0] adder_1_out, adder_2_out, adder_3_out, and_1_out, AND_2_out, bit_extender_1_out,
       bit_extender_2_out, divider_1_out, divider_1_rem, divider_2_out, divider_2_rem, multiplier_1_cout,
       multiplier_1_out, multiplier_2_cout, multiplier_2_out, negator_1_out, NOR_out, OR_out, shifter_1_out,
       shifter_2_out, shifter_3_out, shifter_4_out, shifter_5_out, shifter_6_out, subtractor_1_out, XOR_out;

  Negator #(.width(32)) negator_1 (.in(Y), .out(negator_1_out));
  Shifter #(.width(32)) shifter_1 (.in(X), .\dist (Y[4:0]), .out(shifter_1_out));
  Shifter #(.width(32), .shift("ar")) shifter_2 (.in(X), .\dist (Y[4:0]), .out(shifter_2_out));
  Shifter #(.width(32), .shift("lr")) shifter_3 (.in(X), .\dist (Y[4:0]), .out(shifter_3_out));
  Multiplier #(.width(32)) multiplier_1 (.a(X), .b(Y), .out(multiplier_1_out), .cout(multiplier_1_cout));  // open: cin
  Divider #(.width(32)) divider_1 (.a(X), .b(Y), .out(divider_1_out), .rem(divider_1_rem));  // open: upper
  Adder #(.width(32)) adder_1 (.a(X), .b(Y), .out(adder_1_out));  // open: cin, cout
  Adder #(.width(32)) adder_2 (.a(X), .b(negator_1_out), .out(adder_2_out));  // open: cin, cout
  assign and_1_out = X & Y;  // AND_Gate and_1, 32 bits wide
  Comparator #(.width(32)) comparator_1 (.a(X), .b(Y), .lt(comparator_1_lt));  // open: gt, eq
  Comparator #(.width(32), .mode("unsigned")) comparator_2 (.a(X), .b(Y), .lt(comparator_2_lt));  // open: gt, eq
  Comparator #(.width(32), .mode("unsigned")) comparator_3 (.a(X), .b(Y), .eq(Equal));  // open: gt, lt
  assign bit_extender_1_out = {{31{1'b0}}, comparator_1_lt};  // Bit_Extender bit_extender_1
  assign bit_extender_2_out = {{31{1'b0}}, comparator_2_lt};  // Bit_Extender bit_extender_2
  Multiplexer #(.select(4), .width(32), .enable("false")) multiplexer_1 (
    .in0(shifter_1_out), .in1(shifter_2_out), .in2(shifter_3_out), .in3(multiplier_1_out),
    .in4(divider_1_out), .in5(adder_1_out), .in6(adder_2_out), .in7(and_1_out), .in8({32{1'b0}}),
    .in9({32{1'b0}}), .in10({32{1'b0}}), .in11(bit_extender_1_out), .in12(bit_extender_2_out),
    .in13({32{1'b0}}), .in14({32{1'b0}}), .in15({32{1'b0}}), .out(Result), .sel(AluOP));
  Multiplexer #(.select(4), .width(32), .enable("false")) multiplexer_2 (
    .in0({32{1'b0}}), .in1({32{1'b0}}), .in2({32{1'b0}}), .in3(multiplier_1_cout), .in4(divider_1_rem),
    .in5({32{1'b0}}), .in6({32{1'b0}}), .in7({32{1'b0}}), .in8({32{1'b0}}), .in9({32{1'b0}}),
    .in10({32{1'b0}}), .in11({32{1'b0}}), .in12({32{1'b0}}), .in13({32{1'b0}}), .in14({32{1'b0}}),
    .in15({32{1'b0}}), .out(Result_2), .sel(AluOP));
  Shifter #(.width(32)) shifter_4 (.in(X), .\dist (Y[4:0]), .out(shifter_4_out));
  Shifter #(.width(32), .shift("ar")) shifter_5 (.in(X), .\dist (Y[4:0]), .out(shifter_5_out));
  Shifter #(.width(32), .shift("lr")) shifter_6 (.in(X), .\dist (Y[4:0]), .out(shifter_6_out));
  Multiplier #(.width(32)) multiplier_2 (.a(X), .b(Y), .out(multiplier_2_out), .cout(multiplier_2_cout));  // open: cin
  Divider #(.width(32)) divider_2 (.a(X), .b(Y), .out(divider_2_out), .rem(divider_2_rem));  // open: upper
  Adder #(.width(32)) adder_3 (.a(X), .b(Y), .out(adder_3_out));  // open: cin, cout
  Subtractor #(.width(32)) subtractor_1 (.a(X), .b(Y), .out(subtractor_1_out));  // open: bin, bout
  assign AND_2_out = X & Y;  // AND_Gate AND_2, 32 bits wide
  assign OR_out = X | Y;  // OR_Gate OR, 32 bits wide
  assign XOR_out = X ^ Y;  // XOR_Gate XOR, 32 bits wide
  assign NOR_out = ~(X | Y);  // NOR_Gate NOR, 32 bits wide
  Comparator #(.width(32)) comparator_4 (.a(X), .b(Y), .eq(Equal), .lt(comparator_4_lt[0]));  // open: gt
  Comparator #(.width(32)) comparator_5 (.a(X), .b(Y), .lt(comparator_5_lt[0]));  // open: gt, eq
  Multiplexer #(.select(4), .width(32), .enable("false")) multiplexer_3 (
    .in0(shifter_4_out), .in1(shifter_5_out), .in2(shifter_6_out), .in3(multiplier_2_out),
    .in4(divider_2_out), .in5(adder_3_out), .in6(subtractor_1_out), .in7(AND_2_out), .in8(OR_out),
    .in9(XOR_out), .in10(NOR_out), .in11({{31{1'b0}}, comparator_4_lt[0]}),
    .in12({{31{1'b0}}, comparator_5_lt[0]}), .in13({32{1'b0}}), .in14({32{1'b0}}), .in15({32{1'b0}}),
    .out(Result), .sel(AluOP));
  Multiplexer #(.select(4), .width(32), .enable("false")) multiplexer_4 (
    .in0({32{1'b0}}), .in1({32{1'b0}}), .in2({32{1'b0}}), .in3(multiplier_2_cout), .in4(divider_2_rem),
    .in5({32{1'b0}}), .in6({32{1'b0}}), .in7({32{1'b0}}), .in8({32{1'b0}}), .in9({32{1'b0}}),
    .in10({32{1'b0}}), .in11({32{1'b0}}), .in12({32{1'b0}}), .in13({32{1'b0}}), .in14({32{1'b0}}),
    .in15({32{1'b0}}), .out(Result_2), .sel(AluOP));

  // Other names for the same wires on the sheet: Result2[31:0] = Result_2; S[3:0] = AluOP

  // Notes on the sheet:
  //   不要改变此引脚区域内容，也不要改变ALU封装形式
  //   输入引脚
  //   输出引脚
endmodule
