// Logisim project 新手实验.circ as structural Verilog: 7 circuits, main circuit LED计数电路
module \LED计数电路  (
  input  in_1,
  input  in_2,
  input  in_3,
  input  in_4,
  input  in_5,
  output out_6,
  output out_7,
  output out_8,
  output out_9,
  output out_10
);

  or or_1 (out_6, in_1, in_2, in_3, in_4, in_5);
  or or_2 (out_7, in_2, in_3, in_4, in_5);
  or or_3 (out_8, in_3, in_4, in_5);
  or or_4 (out_9, in_4, in_5);

  assign out_10 = in_5;
endmodule

module \LED计数测试  (
);

  wire _1_out, _2_out, _3_out, _4_out, _5_out, \led计数电路_1_out_6 , \led计数电路_1_out_7 , \led计数电路_1_out_8 ,
       \led计数电路_1_out_9 , \led计数电路_1_out_10 ;

  Button _1 (.out(_1_out));
  Button _2 (.out(_2_out));
  Button _3 (.out(_3_out));
  Button _4 (.out(_4_out));
  Button _5 (.out(_5_out));
  \LED计数电路  \led计数电路_1  (
    .in_1(_1_out), .in_2(_2_out), .in_3(_3_out), .in_4(_4_out), .in_5(_5_out), .out_6(\led计数电路_1_out_6 ),
    .out_7(\led计数电路_1_out_7 ), .out_8(\led计数电路_1_out_8 ), .out_9(\led计数电路_1_out_9 ),
    .out_10(\led计数电路_1_out_10 ));
  LED led_1 (.in(\led计数电路_1_out_6 ));
  LED led_2 (.in(\led计数电路_1_out_7 ));
  LED led_3 (.in(\led计数电路_1_out_8 ));
  LED led_4 (.in(\led计数电路_1_out_9 ));
  LED led_5 (.in(\led计数电路_1_out_10 ));
endmodule

module \_5输入编码器  (
  input  In1,
  input  In2,
  input  In3,
  input  In4,
  input  In5,
  output Out1,
  output Out2,
  output Out3
);

  wire and_1_out, and_2_out, and_3_out, and_4_out, not_1_out, not_2_out, not_3_out, not_4_out, not_5_out,
       not_6_out, not_7_out;

  not not_1 (not_1_out, In4);
  not not_2 (not_2_out, In2);
  not not_3 (not_3_out, In4);
  not not_4 (not_4_out, In4);
  not not_5 (not_5_out, In5);
  not not_6 (not_6_out, In4);
  not not_7 (not_7_out, In5);
  or or_1 (Out3, In5, In4);
  and and_1 (and_1_out, In3, not_1_out);
  and and_2 (and_2_out, In1, not_2_out, not_3_out);
  and and_3 (and_3_out, In3, not_4_out, not_5_out);
  and and_4 (and_4_out, In2, not_6_out, not_7_out);
  or or_2 (Out1, In5, and_1_out, and_2_out);
  or or_3 (Out2, and_3_out, and_4_out);
endmodule

module \_5输入编码测试电路  (
);

  wire _1_out, _2_out, _3_out, _4_out, _5_out, \led计数电路_1_out_6 , \led计数电路_1_out_7 , \led计数电路_1_out_8 ,
       \led计数电路_1_out_9 , \led计数电路_1_out_10 ;
  wire [2:0] \n5输入编码器_1_out1 ;

  Button _1 (.out(_1_out));
  Button _2 (.out(_2_out));
  Button _3 (.out(_3_out));
  Button _4 (.out(_4_out));
  Button _5 (.out(_5_out));
  \LED计数电路  \led计数电路_1  (
    .in_1(_1_out), .in_2(_2_out), .in_3(_3_out), .in_4(_4_out), .in_5(_5_out), .out_6(\led计数电路_1_out_6 ),
    .out_7(\led计数电路_1_out_7 ), .out_8(\led计数电路_1_out_8 ), .out_9(\led计数电路_1_out_9 ),
    .out_10(\led计数电路_1_out_10 ));
  \_5输入编码器  \u_5输入编码器_1  (
    .In1(_1_out), .In2(_2_out), .In3(_3_out), .In4(_4_out), .In5(_5_out), .Out1(\n5输入编码器_1_out1 [0]),
    .Out2(\n5输入编码器_1_out1 [1]), .Out3(\n5输入编码器_1_out1 [2]));
  LED led_1 (.in(\led计数电路_1_out_6 ));
  LED led_2 (.in(\led计数电路_1_out_7 ));
  LED led_3 (.in(\led计数电路_1_out_8 ));
  LED led_4 (.in(\led计数电路_1_out_9 ));
  LED led_5 (.in(\led计数电路_1_out_10 ));
  // Probe on \n5输入编码器_1_out1 
  Hex_Digit_Display hex_digit_display_1 (.value({1'b0, \n5输入编码器_1_out1 }), .dp(1'b1));
endmodule

module \_7段数码管显示驱动  (
  input  x3,
  input  x2,
  input  x1,
  input  x0,
  output Seg_1,
  output Seg_2,
  output Seg_3,
  output Seg_4,
  output Seg_5,
  output Seg_6,
  output Seg_7
);

  wire and_1_out, and_2_out, and_3_out, and_4_out, and_5_out, and_6_out, and_7_out, and_8_out, and_9_out,
       and_10_out, and_11_out, and_12_out, and_13_out, and_14_out, and_15_out, and_16_out, and_17_out,
       and_18_out, and_19_out, and_20_out, and_21_out, and_22_out, and_23_out, and_24_out, and_25_out,
       and_26_out, not_1_out, not_2_out, not_3_out, not_4_out, not_5_out, not_6_out, not_7_out, not_8_out,
       not_9_out, not_10_out, not_11_out, not_12_out, not_13_out, not_14_out, not_15_out, not_16_out,
       not_17_out, not_18_out, not_19_out, not_20_out, not_21_out, not_22_out, not_23_out, not_24_out,
       not_25_out, not_26_out, not_27_out, not_28_out, not_29_out, not_30_out, not_31_out, not_32_out,
       not_33_out, not_34_out, not_35_out, not_36_out, not_37_out;

  not not_1 (not_1_out, x3);
  not not_2 (not_2_out, x2);
  and and_1 (and_1_out, not_1_out, not_2_out, not_3_out);
  not not_3 (not_3_out, x0);
  not not_4 (not_4_out, x3);
  not not_5 (not_5_out, x2);
  and and_2 (and_2_out, not_4_out, not_5_out, x1);
  not not_6 (not_6_out, x3);
  and and_3 (and_3_out, not_6_out, x2, x0);
  not not_7 (not_7_out, x2);
  and and_4 (and_4_out, x3, not_7_out, not_8_out);
  not not_8 (not_8_out, x1);
  not not_9 (not_9_out, x1);
  and and_5 (and_5_out, x3, not_9_out, x0);
  not not_10 (not_10_out, x3);
  and and_6 (and_6_out, not_10_out, not_11_out);
  not not_11 (not_11_out, x2);
  not not_12 (not_12_out, x2);
  and and_7 (and_7_out, not_12_out, not_13_out);
  not not_13 (not_13_out, x1);
  not not_14 (not_14_out, x1);
  and and_8 (and_8_out, not_14_out, not_15_out);
  not not_15 (not_15_out, x0);
  not not_16 (not_16_out, x3);
  and and_9 (and_9_out, not_16_out, x1, x0);
  not not_17 (not_17_out, x2);
  and and_10 (and_10_out, not_17_out, not_18_out);
  not not_18 (not_18_out, x1);
  not not_19 (not_19_out, x2);
  and and_11 (and_11_out, not_19_out, x0);
  not not_20 (not_20_out, x3);
  and and_12 (and_12_out, not_20_out, x2);
  not not_21 (not_21_out, x2);
  and and_13 (and_13_out, not_21_out, not_22_out);
  not not_22 (not_22_out, x0);
  not not_23 (not_23_out, x2);
  and and_14 (and_14_out, not_23_out, x1);
  and and_15 (and_15_out, x1, not_24_out);
  not not_24 (not_24_out, x0);
  not not_25 (not_25_out, x1);
  and and_16 (and_16_out, x2, not_25_out, x0);
  not not_26 (not_26_out, x2);
  and and_17 (and_17_out, not_26_out, not_27_out);
  not not_27 (not_27_out, x0);
  and and_18 (and_18_out, x1, not_28_out);
  not not_28 (not_28_out, x0);
  not not_29 (not_29_out, x1);
  and and_19 (and_19_out, not_29_out, not_30_out);
  not not_30 (not_30_out, x0);
  and and_20 (and_20_out, x2, not_31_out);
  not not_31 (not_31_out, x1);
  and and_21 (and_21_out, x2, not_32_out);
  not not_32 (not_32_out, x0);
  and and_22 (and_22_out, x3, not_33_out);
  not not_33 (not_33_out, x1);
  not not_34 (not_34_out, x2);
  and and_23 (and_23_out, not_34_out, x1);
  and and_24 (and_24_out, x2, not_35_out);
  not not_35 (not_35_out, x1);
  and and_25 (and_25_out, x2, not_36_out);
  not not_36 (not_36_out, x0);
  and and_26 (and_26_out, x3, not_37_out);
  not not_37 (not_37_out, x2);
  or or_1 (Seg_1, and_1_out, and_2_out, and_3_out, and_4_out, and_5_out);
  or or_2 (Seg_2, and_6_out, and_7_out, and_8_out, and_9_out);
  or or_3 (Seg_3, and_10_out, and_11_out, and_12_out);
  or or_4 (Seg_4, and_13_out, and_14_out, and_15_out, and_16_out);
  or or_5 (Seg_5, and_17_out, and_18_out);
  or or_6 (Seg_6, and_19_out, and_20_out, and_21_out, and_22_out);
  or or_7 (Seg_7, and_23_out, and_24_out, and_25_out, and_26_out);
endmodule

module \数码管驱动自动测试  (
  input  in_1
);

  wire clock_1_out, \n7段数码管显示驱动_1_seg_1 , \n7段数码管显示驱动_1_seg_2 , \n7段数码管显示驱动_1_seg_3 , \n7段数码管显示驱动_1_seg_4 ,
       \n7段数码管显示驱动_1_seg_5 , \n7段数码管显示驱动_1_seg_6 , \n7段数码管显示驱动_1_seg_7 ;
  wire [3:0] counter_1_q;

  Counter #(.width(4), .max('hf)) counter_1 (
    .Q(counter_1_q), .clk(clock_1_out), .clr(in_1));  // open: load, D, count, carry
  Clock clock_1 (.out(clock_1_out));
  \_7段数码管显示驱动  \u_7段数码管显示驱动_1  (
    .x3(counter_1_q[3]), .x2(counter_1_q[2]), .x1(counter_1_q[1]), .x0(counter_1_q[0]),
    .Seg_1(\n7段数码管显示驱动_1_seg_1 ), .Seg_2(\n7段数码管显示驱动_1_seg_2 ), .Seg_3(\n7段数码管显示驱动_1_seg_3 ),
    .Seg_4(\n7段数码管显示驱动_1_seg_4 ), .Seg_5(\n7段数码管显示驱动_1_seg_5 ), .Seg_6(\n7段数码管显示驱动_1_seg_6 ),
    .Seg_7(\n7段数码管显示驱动_1_seg_7 ));
  _7_Segment_Display u_7_segment_display_1 (
    .g(\n7段数码管显示驱动_1_seg_7 ), .f(\n7段数码管显示驱动_1_seg_6 ), .a(\n7段数码管显示驱动_1_seg_1 ), .b(\n7段数码管显示驱动_1_seg_2 ),
    .e(\n7段数码管显示驱动_1_seg_5 ), .d(\n7段数码管显示驱动_1_seg_4 ), .c(\n7段数码管显示驱动_1_seg_3 ));  // open: dp
endmodule

module \集成到LED计数测试电路  (
);

  wire _1_out, _2_out, _3_out, _4_out, _5_out, \led计数电路_1_out_6 , \led计数电路_1_out_7 , \led计数电路_1_out_8 ,
       \led计数电路_1_out_9 , \led计数电路_1_out_10 , \n7段数码管显示驱动_1_seg_1 , \n7段数码管显示驱动_1_seg_2 ,
       \n7段数码管显示驱动_1_seg_3 , \n7段数码管显示驱动_1_seg_4 , \n7段数码管显示驱动_1_seg_5 , \n7段数码管显示驱动_1_seg_6 ,
       \n7段数码管显示驱动_1_seg_7 ;
  wire [2:0] \n5输入编码器_1_out1 ;

  Button _1 (.out(_1_out));
  Button _2 (.out(_2_out));
  Button _3 (.out(_3_out));
  Button _4 (.out(_4_out));
  Button _5 (.out(_5_out));
  \LED计数电路  \led计数电路_1  (
    .in_1(_1_out), .in_2(_2_out), .in_3(_3_out), .in_4(_4_out), .in_5(_5_out), .out_6(\led计数电路_1_out_6 ),
    .out_7(\led计数电路_1_out_7 ), .out_8(\led计数电路_1_out_8 ), .out_9(\led计数电路_1_out_9 ),
    .out_10(\led计数电路_1_out_10 ));
  \_5输入编码器  \u_5输入编码器_1  (
    .In1(_1_out), .In2(_2_out), .In3(_3_out), .In4(_4_out), .In5(_5_out), .Out1(\n5输入编码器_1_out1 [0]),
    .Out2(\n5输入编码器_1_out1 [1]), .Out3(\n5输入编码器_1_out1 [2]));
  LED led_1 (.in(\led计数电路_1_out_6 ));
  LED led_2 (.in(\led计数电路_1_out_7 ));
  LED led_3 (.in(\led计数电路_1_out_8 ));
  LED led_4 (.in(\led计数电路_1_out_9 ));
  LED led_5 (.in(\led计数电路_1_out_10 ));
  // Probe on \n5输入编码器_1_out1 
  \_7段数码管显示驱动  \u_7段数码管显示驱动_1  (
    .x3(1'b0), .x2(\n5输入编码器_1_out1 [2]), .x1(\n5输入编码器_1_out1 [1]), .x0(\n5输入编码器_1_out1 [0]),
    .Seg_1(\n7段数码管显示驱动_1_seg_1 ), .Seg_2(\n7段数码管显示驱动_1_seg_2 ), .Seg_3(\n7段数码管显示驱动_1_seg_3 ),
    .Seg_4(\n7段数码管显示驱动_1_seg_4 ), .Seg_5(\n7段数码管显示驱动_1_seg_5 ), .Seg_6(\n7段数码管显示驱动_1_seg_6 ),
    .Seg_7(\n7段数码管显示驱动_1_seg_7 ));
  Hex_Digit_Display hex_digit_display_1 (.value({1'b0, \n5输入编码器_1_out1 }), .dp(1'b1));
  _7_Segment_Display u_7_segment_display_1 (
    .g(\n7段数码管显示驱动_1_seg_7 ), .f(\n7段数码管显示驱动_1_seg_6 ), .a(\n7段数码管显示驱动_1_seg_1 ), .b(\n7段数码管显示驱动_1_seg_2 ),
    .e(\n7段数码管显示驱动_1_seg_5 ), .d(\n7段数码管显示驱动_1_seg_4 ), .c(\n7段数码管显示驱动_1_seg_3 ), .dp(1'b1));
endmodule
